// Logisim project S1-T9-TraCCS.circ as structural Verilog: 36 circuits, main circuit main
module main (
  input  RESET,
  input  Traffic_NS,
  input  in_3,
  input  Traffic_EW,
  input  in_5,
  output out_6,
  output NORTH,
  output out_8,
  output out_9,
  output out_10,
  output out_11,
  output SOUTH,
  output out_13
);

  wire green_1_o, green_2_o, green_3_o, green_4_o, high_high_1_p3, high_high_1_p4, high_low_1_e0,
       high_low_1_e1, high_low_1_n0, high_low_1_n1, high_mod_1_p5, high_mod_1_p6, high_mod_1_p7,
       high_mod_1_p8, high_mod_1_p9, high_mod_1_p10, low_high_1_e0, low_high_1_e1, low_high_1_n0,
       low_high_1_n1, low_low_1_p4, low_low_1_p5, low_low_1_p6, low_low_1_p7, low_moderate_1_e0,
       low_moderate_1_e1, low_moderate_1_n0, low_moderate_1_n1, mod_high_1_e0, mod_high_1_e1, mod_high_1_n0,
       mod_high_1_n1, mod_mod_1_p7, mod_mod_1_p8, moderate_low_1_p5, moderate_low_1_p6, moderate_low_1_p7,
       moderate_low_1_p8, moderate_low_1_p9, moderate_low_1_p10, red_1_o, red_2_o, red_3_o, red_4_o,
       traffic_selector_1_a2, traffic_selector_1_b2, traffic_selector_1_c2, traffic_selector_1_d2,
       traffic_selector_1_e, traffic_selector_1_f, traffic_selector_1_g, traffic_selector_1_h,
       traffic_selector_1_i, xor_1_out, xor_2_out, xor_3_out, xor_4_out, xor_5_out, xor_6_out, xor_7_out,
       xor_8_out, xor_9_out, yellow_1_o, yellow_2_o, yellow_3_o, yellow_4_o;

  xor xor_1 (xor_1_out, traffic_selector_1_a2, RESET);
  xor xor_2 (xor_2_out, traffic_selector_1_b2, RESET);
  xor xor_3 (xor_3_out, RESET, traffic_selector_1_c2);
  xor xor_4 (xor_4_out, traffic_selector_1_d2, RESET);
  xor xor_5 (xor_5_out, traffic_selector_1_e, RESET);
  traffic_selector traffic_selector_1 (
    .A(Traffic_NS), .B(in_3), .C(Traffic_EW), .D(in_5), .A2(traffic_selector_1_a2),
    .B2(traffic_selector_1_b2), .C2(traffic_selector_1_c2), .D2(traffic_selector_1_d2),
    .E(traffic_selector_1_e), .F(traffic_selector_1_f), .G(traffic_selector_1_g), .H(traffic_selector_1_h),
    .I(traffic_selector_1_i));
  xor xor_6 (xor_6_out, traffic_selector_1_f, RESET);
  xor xor_7 (xor_7_out, RESET, traffic_selector_1_g);
  xor xor_8 (xor_8_out, traffic_selector_1_h, RESET);
  xor xor_9 (xor_9_out, traffic_selector_1_i, RESET);
  // low_low low_low_1: pin names not known; wires that end beside it: traffic_selector_1_a2, traffic_selector_1_a2, xor_1_out, low_low_1_p4, low_low_1_p5, low_low_1_p6, low_low_1_p7
  low_moderate low_moderate_1 (
    .Enable(traffic_selector_1_b2), .Counter(traffic_selector_1_b2), .Reset(xor_2_out),
    .N1(low_moderate_1_n1), .N0(low_moderate_1_n0), .E1(low_moderate_1_e1), .E0(low_moderate_1_e0));  // open: W1, W0, S1, S0
  low_high low_high_1 (
    .Enable(traffic_selector_1_c2), .Counter(traffic_selector_1_c2), .Reset(xor_3_out), .N1(low_high_1_n1),
    .N0(low_high_1_n0), .E1(low_high_1_e1), .E0(low_high_1_e0));  // open: W1, W0, S1, S0
  // moderate_low moderate_low_1: pin names not known; wires that end beside it: traffic_selector_1_d2, traffic_selector_1_d2, xor_4_out, traffic_selector_1_e, moderate_low_1_p5, moderate_low_1_p6, moderate_low_1_p7, moderate_low_1_p8, moderate_low_1_p9, moderate_low_1_p10
  // mod_mod mod_mod_1: pin names not known; wires that end beside it: Traffic_EW, in_3, xor_5_out, traffic_selector_1_e, traffic_selector_1_d2, xor_4_out, mod_mod_1_p7, mod_mod_1_p8
  mod_high mod_high_1 (
    .Enable(traffic_selector_1_f), .Counter(traffic_selector_1_f), .Reset(xor_6_out), .N1(mod_high_1_n1),
    .N0(mod_high_1_n0), .E1(mod_high_1_e1), .E0(mod_high_1_e0));  // open: W1, W0, S1, S0
  high_low high_low_1 (
    .Enable(traffic_selector_1_g), .Counter(traffic_selector_1_g), .Reset(xor_7_out), .N1(high_low_1_n1),
    .N0(high_low_1_n0), .E1(high_low_1_e1), .E0(high_low_1_e0));  // open: W1, W0, S1, S0
  // high_mod high_mod_1: pin names not known; wires that end beside it: traffic_selector_1_h, traffic_selector_1_h, xor_8_out, traffic_selector_1_i, high_mod_1_p5, high_mod_1_p6, high_mod_1_p7, high_mod_1_p8, high_mod_1_p9, high_mod_1_p10
  // high_high high_high_1: pin names not known; wires that end beside it: traffic_selector_1_i, xor_9_out, high_high_1_p3, high_high_1_p4
  or or_1 (out_6, high_mod_1_p9, high_mod_1_p5, high_low_1_n1, mod_high_1_n1, moderate_low_1_p9, moderate_low_1_p5, low_high_1_n1, low_moderate_1_n1, low_low_1_p4);
  red red_1 (.l1(out_9), .l2(out_8), .o(red_1_o));
  LED led_1 (.in(red_1_o));
  yellow yellow_1 (.l1(out_8), .l2(out_9), .o(yellow_1_o));
  LED led_2 (.in(yellow_1_o));
  LED led_3 (.in(green_1_o));
  green green_1 (.l1(out_8), .l2(out_9), .o(green_1_o));
  and and_1 (NORTH, high_mod_1_p10, high_mod_1_p6, high_low_1_n0, mod_high_1_n0, moderate_low_1_p10, moderate_low_1_p6, low_high_1_n0, low_moderate_1_n0, low_low_1_p5);
  red red_2 (.l1(out_6), .l2(NORTH), .o(red_2_o));
  LED led_4 (.in(red_2_o));
  yellow yellow_2 (.l1(out_6), .l2(NORTH), .o(yellow_2_o));
  LED led_5 (.in(yellow_2_o));
  LED led_6 (.in(green_2_o));
  green green_2 (.l1(out_6), .l2(NORTH), .o(green_2_o));
  red red_3 (.l1(out_6), .l2(NORTH), .o(red_3_o));
  LED led_7 (.in(red_3_o));
  yellow yellow_3 (.l1(out_6), .l2(NORTH), .o(yellow_3_o));
  LED led_8 (.in(yellow_3_o));
  green green_3 (.l1(out_6), .l2(NORTH), .o(green_3_o));
  LED led_9 (.in(green_3_o));
  red red_4 (.l1(out_9), .l2(out_8), .o(red_4_o));
  LED led_10 (.in(red_4_o));
  LED led_11 (.in(yellow_4_o));
  LED led_12 (.in(green_4_o));
  or or_2 (out_8, low_low_1_p6, low_moderate_1_e1, low_high_1_e1, moderate_low_1_p7, mod_mod_1_p7, mod_high_1_e1, high_low_1_e1, high_mod_1_p7, high_high_1_p3);
  and and_2 (out_9, low_low_1_p7, low_moderate_1_e0, low_high_1_e0, moderate_low_1_p8, mod_mod_1_p8, mod_high_1_e0, high_low_1_e0, high_mod_1_p8, high_high_1_p4);
  yellow yellow_4 (.l1(out_8), .l2(out_9), .o(yellow_4_o));
  green green_4 (.l1(out_8), .l2(out_9), .o(green_4_o));

  assign out_10 = out_8;
  assign out_11 = out_9;
  assign out_13 = NORTH;
  assign SOUTH = out_6;

  // Notes on the sheet:
  //   INSTRUCTIONS:
  //   1. Click on the RESET/reset button to reset the circuit.
  //   2. Adjust the Traffic NS and Traffic EW inputs for low (00), moderate (01) and high (10) traffic.
  //   3. Run the simulation under Simulate tab and enable ticks setting the clock's frequency to 1Hz for the simulation to work.
  //   4. The traffic selector module directs it to the specific module and produces the required outputs with red being 00 yellow being 01 and green being 10.
  //   WEST
  //   OVERALL CIRCUIT
  //   TRAFFIC CONTROL AND COORDINATION SIMULATOR
  //   EAST
  //   Team ID : S1-T9
  //   Dhruv Sandilya, 231CS122
  //   Sai Samanyu K, 231CS152
  //   Vrishank Honnavalli, 231CS165
endmodule

module lsb (
  input  A,
  input  B,
  input  C,
  input  D,
  output a_2,
  output b_2,
  output c_2,
  output d_2,
  output e,
  output f,
  output g
);

  wire and_1_out, and_2_out, and_3_out, and_4_out, and_5_out, and_6_out, and_7_out, and_8_out, and_9_out,
       and_10_out, and_11_out, and_12_out, and_13_out, and_14_out, and_15_out, and_16_out, and_17_out,
       and_18_out, and_19_out, and_20_out, and_21_out, and_22_out, and_23_out, and_24_out, and_25_out,
       and_26_out, and_27_out, and_28_out, and_29_out, and_30_out, and_31_out, not_1_out, not_2_out,
       not_3_out, not_4_out, not_5_out, not_6_out, not_7_out, not_8_out, not_9_out, not_10_out, not_11_out,
       not_12_out, not_13_out, not_14_out, not_15_out, not_16_out, not_17_out, not_18_out, not_19_out,
       not_20_out, not_21_out, not_22_out, not_23_out, not_24_out, not_25_out, not_26_out, not_27_out,
       not_28_out, not_29_out, not_30_out, not_31_out, not_32_out, not_33_out, not_34_out, not_35_out,
       not_36_out, not_37_out, not_38_out, not_39_out, not_40_out, not_41_out, not_42_out, not_43_out,
       not_44_out;

  not not_1 (not_1_out, B);
  and and_1 (and_1_out, not_1_out, not_2_out);
  not not_2 (not_2_out, D);
  not not_3 (not_3_out, A);
  and and_2 (and_2_out, not_3_out, C);
  and and_3 (and_3_out, B, D);
  and and_4 (and_4_out, A, not_4_out);
  not not_4 (not_4_out, C);
  not not_5 (not_5_out, B);
  not not_6 (not_6_out, C);
  and and_5 (and_5_out, not_6_out, not_7_out);
  not not_7 (not_7_out, D);
  not not_8 (not_8_out, A);
  and and_6 (and_6_out, not_8_out, C, D);
  and and_7 (and_7_out, A, not_9_out);
  not not_9 (not_9_out, C);
  and and_8 (and_8_out, A, not_10_out);
  not not_10 (not_10_out, D);
  not not_11 (not_11_out, A);
  and and_9 (and_9_out, not_11_out, not_12_out);
  not not_12 (not_12_out, C);
  and and_10 (and_10_out, B, C);
  and and_11 (and_11_out, A, not_13_out);
  not not_13 (not_13_out, B);
  not not_14 (not_14_out, B);
  and and_12 (and_12_out, not_14_out, not_15_out);
  not not_15 (not_15_out, D);
  not not_16 (not_16_out, A);
  not not_17 (not_17_out, B);
  and and_13 (and_13_out, not_16_out, not_17_out, C);
  not not_18 (not_18_out, A);
  and and_14 (and_14_out, not_18_out, C, not_19_out);
  not not_19 (not_19_out, D);
  not not_20 (not_20_out, C);
  and and_15 (and_15_out, B, not_20_out, D);
  and and_16 (and_16_out, A, not_21_out, not_22_out);
  not not_21 (not_21_out, C);
  not not_22 (not_22_out, D);
  and and_17 (and_17_out, A, B, D);
  not not_23 (not_23_out, B);
  and and_18 (and_18_out, not_23_out, not_24_out);
  not not_24 (not_24_out, D);
  not not_25 (not_25_out, A);
  and and_19 (and_19_out, not_25_out, C, not_26_out);
  not not_26 (not_26_out, D);
  not not_27 (not_27_out, C);
  and and_20 (and_20_out, A, not_27_out, not_28_out);
  not not_28 (not_28_out, D);
  not not_29 (not_29_out, A);
  and and_21 (and_21_out, not_29_out, not_30_out, not_31_out);
  not not_30 (not_30_out, C);
  not not_31 (not_31_out, D);
  not not_32 (not_32_out, A);
  and and_22 (and_22_out, not_32_out, B, not_33_out);
  not not_33 (not_33_out, C);
  not not_34 (not_34_out, A);
  and and_23 (and_23_out, not_34_out, B, not_35_out);
  not not_35 (not_35_out, D);
  and and_24 (and_24_out, A, not_36_out, not_37_out);
  not not_36 (not_36_out, B);
  not not_37 (not_37_out, C);
  not not_38 (not_38_out, B);
  and and_25 (and_25_out, A, not_38_out, not_39_out);
  not not_39 (not_39_out, D);
  and and_26 (and_26_out, A, B, C);
  not not_40 (not_40_out, A);
  and and_27 (and_27_out, not_40_out, not_41_out, C);
  not not_41 (not_41_out, B);
  and and_28 (and_28_out, B, not_42_out);
  not not_42 (not_42_out, C);
  and and_29 (and_29_out, B, not_43_out);
  not not_43 (not_43_out, D);
  and and_30 (and_30_out, A, not_44_out);
  not not_44 (not_44_out, C);
  and and_31 (and_31_out, A, B);
  or or_1 (a_2, and_1_out, and_2_out, and_3_out, and_4_out);
  or or_2 (b_2, not_5_out, and_5_out, and_6_out, and_7_out, and_8_out);
  or or_3 (c_2, and_9_out, D, and_10_out, and_11_out);
  or or_4 (e, and_18_out, and_19_out, and_20_out);
  or or_5 (g, and_27_out, and_28_out, and_29_out, and_30_out, and_31_out);
  or or_6 (d_2, and_12_out, and_13_out, and_14_out, and_15_out, and_16_out, and_17_out);
  or or_7 (f, and_21_out, and_22_out, and_23_out, and_24_out, and_25_out, and_26_out);
endmodule

module msb (
  input  A,
  input  B,
  input  C,
  input  D,
  output a_2,
  output b_2,
  output c_2,
  output d_2,
  output e,
  output f,
  output g
);

  wire and_1_out, and_2_out, and_3_out, and_4_out, not_1_out, not_2_out, not_3_out, not_4_out, not_5_out,
       not_6_out, not_7_out, not_8_out, not_9_out, not_10_out, not_11_out, not_12_out;

  not not_1 (not_1_out, A);
  not not_2 (not_2_out, B);
  and and_1 (and_1_out, not_2_out, not_3_out);
  not not_3 (not_3_out, C);
  not not_4 (not_4_out, A);
  not not_5 (not_5_out, B);
  and and_2 (and_2_out, not_5_out, not_6_out);
  not not_6 (not_6_out, C);
  not not_7 (not_7_out, A);
  not not_8 (not_8_out, B);
  and and_3 (and_3_out, not_8_out, not_9_out);
  not not_9 (not_9_out, C);
  not not_10 (not_10_out, A);
  not not_11 (not_11_out, B);
  and and_4 (and_4_out, not_11_out, not_12_out);
  not not_12 (not_12_out, C);
  or or_1 (a_2, not_1_out, and_1_out);
  or or_2 (d_2, not_4_out, and_2_out);
  or or_3 (e, not_7_out, and_3_out);
  or or_4 (f, not_10_out, and_4_out);

  assign b_2 = 1'b1;
  assign c_2 = 1'b1;
  assign g = 1'b0;
endmodule

module NS_light (
  input  A,
  input  B,
  input  C,
  input  D,
  output a_2,
  output b_2
);

  wire and_1_out, and_2_out, and_3_out, not_1_out, not_2_out, not_3_out, not_4_out, not_5_out, not_6_out;

  not not_1 (not_1_out, A);
  and and_1 (and_1_out, not_1_out, D);
  not not_2 (not_2_out, A);
  and and_2 (and_2_out, not_2_out, C);
  not not_3 (not_3_out, A);
  and and_3 (and_3_out, not_3_out, B);
  not not_4 (not_4_out, B);
  and and_4 (b_2, not_4_out, not_5_out, not_6_out);
  not not_5 (not_5_out, C);
  not not_6 (not_6_out, D);
  or or_1 (a_2, and_1_out, and_2_out, and_3_out);
endmodule

module Light (
  input  A,
  input  B,
  input  C,
  input  D,
  output a_2,
  output b_2
);

  wire and_1_out, and_2_out, and_3_out, and_4_out, not_1_out, not_2_out, not_3_out, not_4_out, not_5_out,
       not_6_out;

  not not_1 (not_1_out, A);
  and and_1 (and_1_out, not_1_out, not_2_out);
  not not_2 (not_2_out, B);
  not not_3 (not_3_out, A);
  and and_2 (and_2_out, not_3_out, not_4_out);
  not not_4 (not_4_out, C);
  not not_5 (not_5_out, A);
  and and_3 (and_3_out, not_5_out, not_6_out);
  not not_6 (not_6_out, D);
  and and_4 (and_4_out, A, B, C, D);
  and and_5 (b_2, B, C, D);
  or or_1 (a_2, and_1_out, and_2_out, and_3_out, and_4_out);
endmodule

module EW_Light (
  input  A,
  input  B,
  input  C,
  input  D,
  output a_2,
  output b_2
);

  wire and_1_out, and_2_out, and_3_out, not_1_out, not_2_out, not_3_out;

  and and_1 (and_1_out, A, D);
  and and_2 (and_2_out, A, C);
  and and_3 (and_3_out, A, B);
  not not_1 (not_1_out, B);
  not not_2 (not_2_out, C);
  and and_4 (b_2, not_1_out, not_2_out, not_3_out);
  not not_3 (not_3_out, D);
  or or_1 (a_2, and_1_out, and_2_out, and_3_out);
endmodule

module ns_lsb_low_high (
  input  A,
  input  B,
  input  C,
  input  D,
  input  E,
  output a_2,
  output b_2,
  output c_2,
  output d_2,
  output e_2,
  output f,
  output g
);

  wire and_1_out, and_2_out, and_3_out, and_4_out, and_5_out, and_6_out, and_7_out, and_8_out, and_9_out,
       and_10_out, and_11_out, and_12_out, and_13_out, and_14_out, and_15_out, and_16_out, and_17_out,
       and_18_out, and_19_out, and_20_out, and_21_out, and_22_out, and_23_out, and_24_out, and_25_out,
       and_26_out, and_27_out, and_28_out, and_29_out, and_30_out, and_31_out, and_32_out, and_33_out,
       and_34_out, and_35_out, and_36_out, and_37_out, and_38_out, and_39_out, and_40_out, and_41_out,
       and_42_out, and_43_out, and_44_out, and_45_out, and_46_out, and_47_out, and_48_out, and_49_out,
       and_50_out, and_51_out, and_52_out, and_53_out, and_54_out, and_55_out, and_56_out, not_1_out,
       not_2_out, not_3_out, not_4_out, not_5_out, not_6_out, not_7_out, not_8_out, not_9_out, not_10_out,
       not_11_out, not_12_out, not_13_out, not_14_out, not_15_out, not_16_out, not_17_out, not_18_out,
       not_19_out, not_20_out, not_21_out, not_22_out, not_23_out, not_24_out, not_25_out, not_26_out,
       not_27_out, not_28_out, not_29_out, not_30_out, not_31_out, not_32_out, not_33_out, not_34_out,
       not_35_out, not_36_out, not_37_out, not_38_out, not_39_out, not_40_out, not_41_out, not_42_out,
       not_43_out, not_44_out, not_45_out, not_46_out, not_47_out, not_48_out, not_49_out, not_50_out,
       not_51_out, not_52_out, not_53_out, not_54_out, not_55_out, not_56_out, not_57_out, not_58_out,
       not_59_out, not_60_out, not_61_out, not_62_out, not_63_out, not_64_out, not_65_out, not_66_out,
       not_67_out, not_68_out, not_69_out, not_70_out, not_71_out, not_72_out, not_73_out, not_74_out,
       not_75_out, not_76_out, not_77_out, not_78_out, not_79_out, not_80_out, not_81_out, not_82_out,
       not_83_out, not_84_out, not_85_out, not_86_out, not_87_out, not_88_out, not_89_out, not_90_out,
       not_91_out, not_92_out, not_93_out, not_94_out, not_95_out, not_96_out, not_97_out, not_98_out,
       not_99_out, not_100_out, not_101_out;

  not not_1 (not_1_out, A);
  not not_2 (not_2_out, C);
  not not_3 (not_3_out, E);
  not not_4 (not_4_out, B);
  not not_5 (not_5_out, A);
  not not_6 (not_6_out, A);
  not not_7 (not_7_out, D);
  not not_8 (not_8_out, D);
  not not_9 (not_9_out, B);
  not not_10 (not_10_out, E);
  not not_11 (not_11_out, C);
  not not_12 (not_12_out, E);
  not not_13 (not_13_out, A);
  not not_14 (not_14_out, C);
  not not_15 (not_15_out, A);
  not not_16 (not_16_out, D);
  not not_17 (not_17_out, E);
  not not_18 (not_18_out, B);
  not not_19 (not_19_out, C);
  not not_20 (not_20_out, B);
  not not_21 (not_21_out, C);
  not not_22 (not_22_out, B);
  not not_23 (not_23_out, C);
  not not_24 (not_24_out, A);
  not not_25 (not_25_out, D);
  not not_26 (not_26_out, A);
  not not_27 (not_27_out, E);
  not not_28 (not_28_out, D);
  not not_29 (not_29_out, E);
  not not_30 (not_30_out, B);
  not not_31 (not_31_out, D);
  not not_32 (not_32_out, C);
  not not_33 (not_33_out, D);
  not not_34 (not_34_out, A);
  not not_35 (not_35_out, B);
  not not_36 (not_36_out, C);
  not not_37 (not_37_out, D);
  not not_38 (not_38_out, A);
  not not_39 (not_39_out, C);
  not not_40 (not_40_out, E);
  not not_41 (not_41_out, B);
  not not_42 (not_42_out, C);
  not not_43 (not_43_out, E);
  not not_44 (not_44_out, A);
  not not_45 (not_45_out, B);
  not not_46 (not_46_out, C);
  not not_47 (not_47_out, B);
  not not_48 (not_48_out, E);
  not not_49 (not_49_out, C);
  not not_50 (not_50_out, E);
  not not_51 (not_51_out, A);
  not not_52 (not_52_out, D);
  not not_53 (not_53_out, A);
  not not_54 (not_54_out, D);
  not not_55 (not_55_out, E);
  not not_56 (not_56_out, A);
  not not_57 (not_57_out, E);
  not not_58 (not_58_out, B);
  not not_59 (not_59_out, C);
  not not_60 (not_60_out, D);
  not not_61 (not_61_out, A);
  not not_62 (not_62_out, C);
  not not_63 (not_63_out, E);
  not not_64 (not_64_out, B);
  not not_65 (not_65_out, C);
  not not_66 (not_66_out, E);
  not not_67 (not_67_out, B);
  not not_68 (not_68_out, E);
  not not_69 (not_69_out, C);
  not not_70 (not_70_out, E);
  not not_71 (not_71_out, A);
  not not_72 (not_72_out, D);
  not not_73 (not_73_out, E);
  not not_74 (not_74_out, E);
  not not_75 (not_75_out, B);
  not not_76 (not_76_out, D);
  not not_77 (not_77_out, E);
  not not_78 (not_78_out, A);
  not not_79 (not_79_out, B);
  not not_80 (not_80_out, D);
  not not_81 (not_81_out, A);
  not not_82 (not_82_out, B);
  not not_83 (not_83_out, E);
  not not_84 (not_84_out, C);
  not not_85 (not_85_out, D);
  not not_86 (not_86_out, E);
  not not_87 (not_87_out, A);
  not not_88 (not_88_out, B);
  not not_89 (not_89_out, C);
  not not_90 (not_90_out, D);
  not not_91 (not_91_out, B);
  not not_92 (not_92_out, C);
  not not_93 (not_93_out, B);
  not not_94 (not_94_out, E);
  not not_95 (not_95_out, A);
  not not_96 (not_96_out, D);
  not not_97 (not_97_out, D);
  not not_98 (not_98_out, A);
  not not_99 (not_99_out, C);
  not not_100 (not_100_out, E);
  not not_101 (not_101_out, B);
  and and_1 (and_1_out, not_1_out, not_2_out, not_3_out);
  and and_2 (and_2_out, not_4_out, D);
  and and_3 (and_3_out, not_5_out, C, E);
  and and_4 (and_4_out, not_6_out, B, not_7_out);
  and and_5 (and_5_out, B, C, not_8_out);
  and and_6 (and_6_out, A, not_9_out, not_10_out);
  and and_7 (and_7_out, A, not_11_out, E);
  and and_8 (and_8_out, A, D, not_12_out);
  and and_9 (and_9_out, not_13_out, not_14_out);
  and and_10 (and_10_out, not_15_out, not_16_out, not_17_out);
  and and_11 (and_11_out, not_18_out, not_19_out, E);
  and and_12 (and_12_out, not_20_out, not_21_out, D);
  and and_13 (and_13_out, not_22_out, D, E);
  and and_14 (and_14_out, not_23_out, D, E);
  and and_15 (and_15_out, not_24_out, B, not_25_out);
  and and_16 (and_16_out, not_26_out, B, not_27_out);
  and and_17 (and_17_out, B, not_28_out, not_29_out);
  and and_18 (and_18_out, A, C);
  and and_19 (and_19_out, not_30_out, not_31_out);
  and and_20 (and_20_out, not_32_out, not_33_out);
  and and_21 (and_21_out, not_34_out, not_35_out, C);
  and and_22 (and_22_out, B, D);
  and and_23 (and_23_out, A, not_36_out);
  and and_24 (and_24_out, A, not_37_out);
  and and_25 (and_25_out, not_38_out, not_39_out, not_40_out);
  and and_26 (and_26_out, not_41_out, not_42_out, not_43_out);
  and and_27 (and_27_out, not_44_out, not_45_out, not_46_out, D);
  and and_28 (and_28_out, not_47_out, D, not_48_out);
  and and_29 (and_29_out, not_49_out, D, not_50_out);
  and and_30 (and_30_out, not_51_out, C, not_52_out, E);
  and and_31 (and_31_out, not_53_out, B, not_54_out, not_55_out);
  and and_32 (and_32_out, not_56_out, B, C, E);
  and and_33 (and_33_out, A, C, not_57_out);
  and and_34 (and_34_out, A, not_58_out, C, D);
  and and_35 (and_35_out, A, B, not_59_out, not_60_out, E);
  and and_36 (and_36_out, not_61_out, not_62_out, not_63_out);
  and and_37 (and_37_out, not_64_out, not_65_out, not_66_out);
  and and_38 (and_38_out, not_67_out, D, not_68_out);
  and and_39 (and_39_out, not_69_out, D, not_70_out);
  and and_40 (and_40_out, not_71_out, B, not_72_out, not_73_out);
  and and_41 (and_41_out, A, C, not_74_out);
  and and_42 (and_42_out, not_75_out, not_76_out, not_77_out);
  and and_43 (and_43_out, not_78_out, not_79_out, C, not_80_out);
  and and_44 (and_44_out, not_81_out, not_82_out, C, not_83_out);
  and and_45 (and_45_out, B, not_84_out, not_85_out);
  and and_46 (and_46_out, B, D, not_86_out);
  and and_47 (and_47_out, not_87_out, B, C, D);
  and and_48 (and_48_out, A, not_88_out, not_89_out, D);
  and and_49 (and_49_out, A, B, not_90_out);
  and and_50 (and_50_out, not_91_out, not_92_out, D);
  and and_51 (and_51_out, not_93_out, D, not_94_out);
  and and_52 (and_52_out, not_95_out, C, not_96_out);
  and and_53 (and_53_out, B, not_97_out);
  and and_54 (and_54_out, not_98_out, B, C);
  and and_55 (and_55_out, A, not_99_out, not_100_out);
  and and_56 (and_56_out, A, not_101_out, D);
  or or_1 (a_2, and_1_out, and_2_out, and_3_out, and_4_out, and_5_out, and_6_out, and_7_out, and_8_out);
  or or_2 (b_2, and_9_out, and_10_out, and_11_out, and_12_out, and_13_out, and_14_out, and_15_out, and_16_out, and_17_out, and_18_out);
  or or_3 (c_2, and_19_out, and_20_out, E, and_21_out, and_22_out, and_23_out, and_24_out);
  or or_4 (d_2, and_25_out, and_26_out, and_27_out, and_28_out, and_29_out, and_30_out, and_31_out, and_32_out, and_33_out, and_34_out, and_35_out);
  or or_5 (e_2, and_36_out, and_37_out, and_38_out, and_39_out, and_40_out, and_41_out);
  or or_6 (f, and_42_out, and_43_out, and_44_out, and_45_out, and_46_out, and_47_out, and_48_out, and_49_out);
  or or_7 (g, and_50_out, and_51_out, and_52_out, and_53_out, and_54_out, and_55_out, and_56_out);
endmodule

module NS_msb_low (
  input  A,
  input  B,
  input  C,
  input  D,
  input  E,
  output a_2,
  output b_2,
  output c_2,
  output d_2,
  output e_2,
  output f,
  output g
);

  wire and_1_out, and_2_out, and_3_out, and_4_out, and_5_out, and_6_out, and_7_out, and_8_out, and_9_out,
       and_10_out, and_11_out, and_12_out, and_13_out, and_14_out, and_15_out, and_16_out, and_17_out,
       and_18_out, and_19_out, not_1_out, not_2_out, not_3_out, not_4_out, not_5_out, not_6_out, not_7_out,
       not_8_out, not_9_out, not_10_out, not_11_out, not_12_out, not_13_out, not_14_out, not_15_out,
       not_16_out, not_17_out, not_18_out, not_19_out, not_20_out, not_21_out, not_22_out, not_23_out,
       not_24_out, not_25_out, not_26_out, not_27_out, not_28_out;

  not not_1 (not_1_out, A);
  not not_2 (not_2_out, B);
  not not_3 (not_3_out, A);
  not not_4 (not_4_out, C);
  not not_5 (not_5_out, D);
  not not_6 (not_6_out, B);
  not not_7 (not_7_out, B);
  not not_8 (not_8_out, C);
  not not_9 (not_9_out, A);
  not not_10 (not_10_out, B);
  not not_11 (not_11_out, A);
  not not_12 (not_12_out, C);
  not not_13 (not_13_out, D);
  not not_14 (not_14_out, B);
  not not_15 (not_15_out, A);
  not not_16 (not_16_out, B);
  not not_17 (not_17_out, A);
  not not_18 (not_18_out, C);
  not not_19 (not_19_out, D);
  not not_20 (not_20_out, B);
  not not_21 (not_21_out, C);
  not not_22 (not_22_out, D);
  not not_23 (not_23_out, A);
  not not_24 (not_24_out, B);
  not not_25 (not_25_out, A);
  not not_26 (not_26_out, C);
  not not_27 (not_27_out, D);
  and and_1 (and_1_out, A, C);
  and and_2 (and_2_out, A, B);
  and and_3 (and_3_out, not_1_out, not_2_out);
  and and_4 (and_4_out, not_3_out, not_4_out, not_5_out);
  and and_5 (and_5_out, not_6_out, C);
  and and_6 (and_6_out, A, B);
  not not_28 (not_28_out, A);
  and and_7 (and_7_out, not_7_out, not_8_out);
  and and_8 (and_8_out, B, C, D);
  and and_9 (and_9_out, not_9_out, not_10_out);
  and and_10 (and_10_out, not_11_out, not_12_out, not_13_out);
  and and_11 (and_11_out, not_14_out, C);
  and and_12 (and_12_out, A, B);
  and and_13 (and_13_out, not_15_out, not_16_out);
  and and_14 (and_14_out, not_17_out, not_18_out, not_19_out);
  and and_15 (and_15_out, not_20_out, C);
  and and_16 (and_16_out, A, B, not_21_out);
  and and_17 (and_17_out, A, B, not_22_out);
  and and_18 (and_18_out, not_23_out, not_24_out);
  and and_19 (and_19_out, not_25_out, not_26_out, not_27_out);
  or or_1 (g, and_1_out, and_2_out);
  or or_2 (a_2, and_3_out, and_4_out, and_5_out, and_6_out);
  or or_3 (c_2, not_28_out, and_7_out, and_8_out);
  or or_4 (d_2, and_9_out, and_10_out, and_11_out, and_12_out);
  or or_5 (e_2, and_13_out, and_14_out, and_15_out, and_16_out, and_17_out);
  or or_6 (f, and_18_out, and_19_out);

  assign b_2 = 1'b1;
endmodule

module NS_l (
  input  A,
  input  B,
  input  C,
  input  D,
  input  E,
  output a_2,
  output b_2
);

  wire and_1_out, and_2_out, and_3_out, and_4_out, not_1_out, not_2_out, not_3_out, not_4_out, not_5_out,
       not_6_out, not_7_out, not_8_out;

  not not_1 (not_1_out, A);
  not not_2 (not_2_out, A);
  not not_3 (not_3_out, A);
  not not_4 (not_4_out, A);
  not not_5 (not_5_out, B);
  not not_6 (not_6_out, C);
  not not_7 (not_7_out, D);
  not not_8 (not_8_out, E);
  and and_1 (and_1_out, not_1_out, E);
  and and_2 (and_2_out, not_2_out, D);
  and and_3 (and_3_out, not_3_out, C);
  and and_4 (and_4_out, not_4_out, B);
  and and_5 (b_2, not_5_out, not_6_out, not_7_out, not_8_out);
  or or_1 (a_2, and_1_out, and_2_out, and_3_out, and_4_out);
endmodule

module EW_Light_moderate (
  input  A,
  input  B,
  input  C,
  input  D,
  input  E,
  output a_2,
  output b_2
);

  wire and_1_out, and_2_out, and_3_out, and_4_out, not_1_out, not_2_out, not_3_out, not_4_out;

  and and_1 (and_1_out, A, E);
  and and_2 (and_2_out, A, D);
  and and_3 (and_3_out, A, C);
  and and_4 (and_4_out, A, B);
  not not_1 (not_1_out, B);
  not not_2 (not_2_out, C);
  not not_3 (not_3_out, D);
  not not_4 (not_4_out, E);
  or or_1 (a_2, and_1_out, and_2_out, and_3_out, and_4_out);
  and and_5 (b_2, not_1_out, not_2_out, not_3_out, not_4_out);
endmodule

module NS_low (
  input  A,
  input  B,
  input  C,
  input  D,
  output a_2,
  output b_2,
  output c_2,
  output d_2,
  output e,
  output f,
  output g
);

  wire and_1_out, and_2_out, and_3_out, and_4_out, and_5_out, and_6_out, and_7_out, and_8_out, and_9_out,
       and_10_out, and_11_out, and_12_out, and_13_out, and_14_out, and_15_out, and_16_out, not_1_out,
       not_2_out, not_3_out, not_4_out, not_5_out, not_6_out, not_7_out, not_8_out, not_9_out, not_10_out,
       not_11_out, not_12_out, not_13_out, not_14_out, not_15_out, not_16_out, not_17_out, not_18_out,
       not_19_out, not_20_out, not_21_out, not_22_out, not_23_out, not_24_out, not_25_out, not_26_out,
       not_27_out;

  not not_1 (not_1_out, A);
  not not_2 (not_2_out, B);
  and and_1 (and_1_out, not_2_out, not_3_out);
  not not_3 (not_3_out, D);
  and and_2 (and_2_out, B, D);
  not not_4 (not_4_out, A);
  not not_5 (not_5_out, B);
  not not_6 (not_6_out, C);
  and and_3 (and_3_out, not_6_out, not_7_out);
  not not_7 (not_7_out, D);
  and and_4 (and_4_out, C, D);
  not not_8 (not_8_out, A);
  not not_9 (not_9_out, C);
  not not_10 (not_10_out, A);
  not not_11 (not_11_out, B);
  and and_5 (and_5_out, not_11_out, not_12_out);
  not not_12 (not_12_out, D);
  not not_13 (not_13_out, B);
  and and_6 (and_6_out, not_13_out, C);
  and and_7 (and_7_out, C, not_14_out);
  not not_14 (not_14_out, D);
  not not_15 (not_15_out, C);
  and and_8 (and_8_out, B, not_15_out, D);
  not not_16 (not_16_out, A);
  not not_17 (not_17_out, B);
  and and_9 (and_9_out, not_17_out, not_18_out);
  not not_18 (not_18_out, D);
  and and_10 (and_10_out, C, not_19_out);
  not not_19 (not_19_out, D);
  not not_20 (not_20_out, A);
  not not_21 (not_21_out, C);
  and and_11 (and_11_out, not_21_out, not_22_out);
  not not_22 (not_22_out, D);
  and and_12 (and_12_out, B, not_23_out);
  not not_23 (not_23_out, C);
  and and_13 (and_13_out, B, not_24_out);
  not not_24 (not_24_out, D);
  not not_25 (not_25_out, B);
  and and_14 (and_14_out, A, not_25_out, C);
  and and_15 (and_15_out, A, B, not_26_out);
  not not_26 (not_26_out, C);
  and and_16 (and_16_out, A, B, not_27_out);
  not not_27 (not_27_out, D);
  or or_1 (a_2, not_1_out, and_1_out, C, and_2_out);
  or or_2 (b_2, not_4_out, not_5_out, and_3_out, and_4_out);
  or or_3 (c_2, not_8_out, not_9_out, D, B);
  or or_4 (d_2, not_10_out, and_5_out, and_6_out, and_7_out, and_8_out);
  or or_5 (e, not_16_out, and_9_out, and_10_out);
  or or_6 (f, not_20_out, and_11_out, and_12_out, and_13_out);
  or or_7 (g, and_14_out, and_15_out, and_16_out);
endmodule

module EW_low (
  input  A,
  input  B,
  input  C,
  input  D,
  output a_2,
  output b_2,
  output c_2,
  output d_2,
  output e,
  output f,
  output g
);

  wire and_1_out, and_2_out, and_3_out, and_4_out, and_5_out, and_6_out, and_7_out, and_8_out, and_9_out,
       and_10_out, and_11_out, and_12_out, and_13_out, and_14_out, and_15_out, and_16_out, not_1_out,
       not_2_out, not_3_out, not_4_out, not_5_out, not_6_out, not_7_out, not_8_out, not_9_out, not_10_out,
       not_11_out, not_12_out, not_13_out, not_14_out, not_15_out, not_16_out, not_17_out, not_18_out,
       not_19_out, not_20_out, not_21_out, not_22_out, not_23_out, not_24_out;

  not not_1 (not_1_out, B);
  and and_1 (and_1_out, not_1_out, not_2_out);
  not not_2 (not_2_out, D);
  and and_2 (and_2_out, B, D);
  not not_3 (not_3_out, B);
  not not_4 (not_4_out, C);
  and and_3 (and_3_out, not_4_out, not_5_out);
  not not_5 (not_5_out, D);
  and and_4 (and_4_out, C, D);
  not not_6 (not_6_out, C);
  not not_7 (not_7_out, B);
  and and_5 (and_5_out, not_7_out, not_8_out);
  not not_8 (not_8_out, D);
  not not_9 (not_9_out, B);
  and and_6 (and_6_out, not_9_out, C);
  and and_7 (and_7_out, C, not_10_out);
  not not_10 (not_10_out, D);
  and and_8 (and_8_out, B, not_11_out, D);
  not not_11 (not_11_out, C);
  not not_12 (not_12_out, B);
  and and_9 (and_9_out, not_12_out, not_13_out);
  not not_13 (not_13_out, D);
  and and_10 (and_10_out, C, not_14_out);
  not not_14 (not_14_out, D);
  not not_15 (not_15_out, C);
  and and_11 (and_11_out, not_15_out, not_16_out);
  not not_16 (not_16_out, D);
  and and_12 (and_12_out, B, not_17_out);
  not not_17 (not_17_out, C);
  and and_13 (and_13_out, B, not_18_out);
  not not_18 (not_18_out, D);
  not not_19 (not_19_out, A);
  and and_14 (and_14_out, not_19_out, not_20_out, C);
  not not_20 (not_20_out, B);
  not not_21 (not_21_out, A);
  and and_15 (and_15_out, not_21_out, B, not_22_out);
  not not_22 (not_22_out, C);
  not not_23 (not_23_out, A);
  and and_16 (and_16_out, not_23_out, B, not_24_out);
  not not_24 (not_24_out, D);
  or or_1 (a_2, and_1_out, C, and_2_out, A);
  or or_2 (b_2, not_3_out, and_3_out, and_4_out, A);
  or or_3 (c_2, not_6_out, D, B, A);
  or or_4 (d_2, and_5_out, and_6_out, and_7_out, and_8_out, A);
  or or_5 (e, and_9_out, and_10_out, A);
  or or_6 (f, and_11_out, and_12_out, and_13_out, A);
  or or_7 (g, and_14_out, and_15_out, and_16_out);
endmodule

module NS_lsb_moderate (
  input  A,
  input  B,
  input  C,
  input  D,
  input  E,
  output a_2,
  output b_2,
  output c_2,
  output d_2,
  output e_2,
  output f,
  output g
);

  wire and_1_out, and_2_out, and_3_out, and_4_out, and_5_out, and_6_out, and_7_out, and_8_out, and_9_out,
       and_10_out, and_11_out, and_12_out, and_13_out, and_14_out, and_15_out, and_16_out, and_17_out,
       and_18_out, and_19_out, and_20_out, and_21_out, and_22_out, and_23_out, and_24_out, and_25_out,
       and_26_out, and_27_out, and_28_out, and_29_out, not_1_out, not_2_out, not_3_out, not_4_out, not_5_out,
       not_6_out, not_7_out, not_8_out, not_9_out, not_10_out, not_11_out, not_12_out, not_13_out,
       not_14_out, not_15_out, not_16_out, not_17_out, not_18_out, not_19_out, not_20_out, not_21_out,
       not_22_out, not_23_out, not_24_out, not_25_out, not_26_out, not_27_out, not_28_out, not_29_out,
       not_30_out, not_31_out, not_32_out, not_33_out, not_34_out, not_35_out, not_36_out, not_37_out,
       not_38_out, not_39_out, not_40_out, not_41_out, not_42_out, not_43_out, not_44_out, not_45_out,
       not_46_out;

  not not_1 (not_1_out, C);
  not not_2 (not_2_out, D);
  not not_3 (not_3_out, B);
  not not_4 (not_4_out, B);
  not not_5 (not_5_out, E);
  not not_6 (not_6_out, C);
  not not_7 (not_7_out, D);
  not not_8 (not_8_out, E);
  not not_9 (not_9_out, A);
  not not_10 (not_10_out, C);
  not not_11 (not_11_out, D);
  not not_12 (not_12_out, B);
  not not_13 (not_13_out, D);
  not not_14 (not_14_out, C);
  not not_15 (not_15_out, B);
  not not_16 (not_16_out, D);
  not not_17 (not_17_out, E);
  not not_18 (not_18_out, C);
  not not_19 (not_19_out, B);
  not not_20 (not_20_out, E);
  not not_21 (not_21_out, D);
  not not_22 (not_22_out, B);
  not not_23 (not_23_out, C);
  not not_24 (not_24_out, D);
  not not_25 (not_25_out, C);
  not not_26 (not_26_out, B);
  not not_27 (not_27_out, D);
  not not_28 (not_28_out, B);
  not not_29 (not_29_out, C);
  not not_30 (not_30_out, D);
  not not_31 (not_31_out, B);
  not not_32 (not_32_out, D);
  not not_33 (not_33_out, C);
  not not_34 (not_34_out, D);
  not not_35 (not_35_out, B);
  not not_36 (not_36_out, C);
  not not_37 (not_37_out, B);
  not not_38 (not_38_out, B);
  not not_39 (not_39_out, D);
  not not_40 (not_40_out, E);
  not not_41 (not_41_out, A);
  and and_1 (and_1_out, not_1_out, not_2_out);
  and and_2 (and_2_out, not_3_out, D, E);
  and and_3 (and_3_out, not_4_out, C, not_5_out);
  and and_4 (and_4_out, B, not_6_out);
  and and_5 (and_5_out, B, not_7_out, E);
  and and_6 (and_6_out, B, D, not_8_out);
  or or_1 (b_2, not_9_out, not_10_out, not_11_out, B);
  not not_42 (not_42_out, A);
  and and_7 (and_7_out, not_12_out, not_13_out);
  not not_43 (not_43_out, E);
  and and_8 (and_8_out, C, D);
  and and_9 (and_9_out, B, not_14_out);
  not not_44 (not_44_out, A);
  and and_10 (and_10_out, not_15_out, not_16_out, not_17_out);
  and and_11 (and_11_out, not_18_out, E);
  and and_12 (and_12_out, not_19_out, C, D);
  and and_13 (and_13_out, C, D, not_20_out);
  and and_14 (and_14_out, B, not_21_out, E);
  not not_45 (not_45_out, A);
  and and_15 (and_15_out, not_22_out, not_23_out, not_24_out);
  and and_16 (and_16_out, not_25_out, E);
  and and_17 (and_17_out, not_26_out, D, E);
  and and_18 (and_18_out, B, not_27_out, E);
  not not_46 (not_46_out, A);
  and and_19 (and_19_out, not_28_out, not_29_out, not_30_out);
  and and_20 (and_20_out, not_31_out, not_32_out, E);
  and and_21 (and_21_out, not_33_out, not_34_out, E);
  and and_22 (and_22_out, not_35_out, C, D);
  and and_23 (and_23_out, B, not_36_out, D);
  and and_24 (and_24_out, B, D, E);
  and and_25 (and_25_out, A, not_37_out, D, E);
  and and_26 (and_26_out, A, not_38_out, C);
  and and_27 (and_27_out, A, C, D);
  and and_28 (and_28_out, A, B, not_39_out, E);
  and and_29 (and_29_out, A, B, D, not_40_out);
  or or_2 (a_2, not_41_out, and_1_out, and_2_out, and_3_out, and_4_out, and_5_out, and_6_out);
  or or_3 (c_2, not_42_out, and_7_out, not_43_out, and_8_out, and_9_out);
  or or_4 (d_2, not_44_out, and_10_out, and_11_out, and_12_out, and_13_out, and_14_out);
  or or_5 (e_2, not_45_out, and_15_out, and_16_out, and_17_out, and_18_out);
  or or_6 (f, not_46_out, and_19_out, and_20_out, and_21_out, and_22_out, and_23_out, and_24_out);
  or or_7 (g, and_25_out, and_26_out, and_27_out, and_28_out, and_29_out);
endmodule

module NS_msb_moderate (
  input  A,
  input  B,
  input  C,
  input  D,
  input  E,
  output a_2,
  output b_2,
  output c_2,
  output d_2,
  output e_2,
  output f,
  output g
);

  wire and_1_out, and_2_out, and_3_out, and_4_out, and_5_out, and_6_out, and_7_out, and_8_out, not_1_out,
       not_2_out, not_3_out, not_4_out, not_5_out, not_6_out, not_7_out, not_8_out, not_9_out, not_10_out,
       not_11_out, not_12_out, not_13_out, not_14_out, not_15_out, not_16_out, not_17_out, not_18_out,
       not_19_out, not_20_out, not_21_out, not_22_out, not_23_out, not_24_out;

  not not_1 (not_1_out, C);
  not not_2 (not_2_out, D);
  not not_3 (not_3_out, C);
  not not_4 (not_4_out, E);
  not not_5 (not_5_out, C);
  not not_6 (not_6_out, D);
  not not_7 (not_7_out, C);
  not not_8 (not_8_out, E);
  not not_9 (not_9_out, C);
  not not_10 (not_10_out, D);
  not not_11 (not_11_out, C);
  not not_12 (not_12_out, E);
  not not_13 (not_13_out, C);
  not not_14 (not_14_out, D);
  not not_15 (not_15_out, C);
  not not_16 (not_16_out, E);
  not not_17 (not_17_out, A);
  not not_18 (not_18_out, B);
  and and_1 (and_1_out, not_1_out, not_2_out);
  and and_2 (and_2_out, not_3_out, not_4_out);
  not not_19 (not_19_out, A);
  not not_20 (not_20_out, B);
  and and_3 (and_3_out, not_5_out, not_6_out);
  and and_4 (and_4_out, not_7_out, not_8_out);
  not not_21 (not_21_out, A);
  not not_22 (not_22_out, B);
  and and_5 (and_5_out, not_9_out, not_10_out);
  and and_6 (and_6_out, not_11_out, not_12_out);
  not not_23 (not_23_out, A);
  not not_24 (not_24_out, B);
  and and_7 (and_7_out, not_13_out, not_14_out);
  and and_8 (and_8_out, not_15_out, not_16_out);
  or or_1 (a_2, not_17_out, not_18_out, and_1_out, and_2_out);
  or or_2 (d_2, not_19_out, not_20_out, and_3_out, and_4_out);
  or or_3 (e_2, not_21_out, not_22_out, and_5_out, and_6_out);
  or or_4 (f, not_23_out, not_24_out, and_7_out, and_8_out);

  assign b_2 = 1'b1;
  assign c_2 = 1'b1;
  assign g = 1'b0;
endmodule

module ns_lsb_low (
  input  A,
  input  B,
  input  C,
  input  D,
  input  E,
  output a_2,
  output b_2,
  output c_2,
  output d_2,
  output e_2,
  output f,
  output g
);

  wire and_1_out, and_2_out, and_3_out, and_4_out, and_5_out, and_6_out, and_7_out, and_8_out, and_9_out,
       and_10_out, and_11_out, and_12_out, and_13_out, and_14_out, and_15_out, and_16_out, not_1_out,
       not_2_out, not_3_out, not_4_out, not_5_out, not_6_out, not_7_out, not_8_out, not_9_out, not_10_out,
       not_11_out, not_12_out, not_13_out, not_14_out, not_15_out, not_16_out, not_17_out, not_18_out,
       not_19_out, not_20_out, not_21_out, not_22_out, not_23_out, not_24_out, not_25_out, not_26_out,
       not_27_out;

  not not_1 (not_1_out, C);
  not not_2 (not_2_out, E);
  not not_3 (not_3_out, D);
  not not_4 (not_4_out, E);
  not not_5 (not_5_out, D);
  not not_6 (not_6_out, C);
  not not_7 (not_7_out, E);
  not not_8 (not_8_out, C);
  not not_9 (not_9_out, E);
  not not_10 (not_10_out, D);
  not not_11 (not_11_out, C);
  not not_12 (not_12_out, E);
  not not_13 (not_13_out, E);
  not not_14 (not_14_out, D);
  not not_15 (not_15_out, E);
  not not_16 (not_16_out, D);
  not not_17 (not_17_out, E);
  not not_18 (not_18_out, A);
  not not_19 (not_19_out, B);
  not not_20 (not_20_out, C);
  not not_21 (not_21_out, A);
  not not_22 (not_22_out, B);
  not not_23 (not_23_out, D);
  not not_24 (not_24_out, A);
  not not_25 (not_25_out, B);
  not not_26 (not_26_out, E);
  and and_1 (and_1_out, not_1_out, not_2_out);
  and and_2 (and_2_out, C, E);
  not not_27 (not_27_out, C);
  and and_3 (and_3_out, not_3_out, not_4_out);
  and and_4 (and_4_out, D, E);
  or or_1 (c_2, not_5_out, E, C, B, A);
  and and_5 (and_5_out, not_6_out, not_7_out);
  and and_6 (and_6_out, not_8_out, D);
  and and_7 (and_7_out, D, not_9_out);
  and and_8 (and_8_out, C, not_10_out, E);
  and and_9 (and_9_out, not_11_out, not_12_out);
  and and_10 (and_10_out, D, not_13_out);
  and and_11 (and_11_out, not_14_out, not_15_out);
  and and_12 (and_12_out, C, not_16_out);
  and and_13 (and_13_out, C, not_17_out);
  and and_14 (and_14_out, not_18_out, not_19_out, not_20_out, D);
  and and_15 (and_15_out, not_21_out, not_22_out, C, not_23_out);
  and and_16 (and_16_out, not_24_out, not_25_out, C, not_26_out);
  or or_2 (a_2, and_1_out, D, and_2_out, B, A);
  or or_3 (b_2, not_27_out, and_3_out, and_4_out, B, A);
  or or_4 (d_2, and_5_out, and_6_out, and_7_out, and_8_out, B, A);
  or or_5 (e_2, and_9_out, and_10_out, B, A);
  or or_6 (f, and_11_out, and_12_out, and_13_out, B, A);
  or or_7 (g, and_14_out, and_15_out, and_16_out);
endmodule

module NS_msb_low_2 (
  input  A,
  input  B,
  input  C,
  input  D,
  input  E,
  output a_2,
  output b_2,
  output c_2,
  output d_2,
  output e_2,
  output f,
  output g
);


  assign a_2 = 1'b1;
  assign b_2 = 1'b1;
  assign c_2 = 1'b1;
  assign d_2 = 1'b1;
  assign e_2 = 1'b1;
  assign f = 1'b1;
  assign g = 1'b0;
endmodule

module NS_msb_low_1 (
  input  A,
  input  B,
  input  C,
  input  D,
  input  E,
  output a_2,
  output b_2,
  output c_2,
  output d_2,
  output e_2,
  output f,
  output g
);


  assign a_2 = 1'b1;
  assign b_2 = 1'b1;
  assign c_2 = 1'b1;
  assign d_2 = 1'b1;
  assign e_2 = 1'b1;
  assign f = 1'b1;
  assign g = 1'b0;
endmodule

module NS_lsb_low_1 (
  input  A,
  input  B,
  input  C,
  input  D,
  input  E,
  output a_2,
  output b_2,
  output c_2,
  output d_2,
  output e_2,
  output f,
  output g
);

  wire and_1_out, and_2_out, and_3_out, and_4_out, and_5_out, and_6_out, and_7_out, and_8_out, and_9_out,
       and_10_out, and_11_out, and_12_out, and_13_out, and_14_out, and_15_out, and_16_out, not_1_out,
       not_2_out, not_3_out, not_4_out, not_5_out, not_6_out, not_7_out, not_8_out, not_9_out, not_10_out,
       not_11_out, not_12_out, not_13_out, not_14_out, not_15_out, not_16_out, not_17_out, not_18_out,
       not_19_out, not_20_out, not_21_out, not_22_out, not_23_out, not_24_out, not_25_out, not_26_out,
       not_27_out;

  not not_1 (not_1_out, C);
  not not_2 (not_2_out, E);
  not not_3 (not_3_out, D);
  not not_4 (not_4_out, E);
  not not_5 (not_5_out, D);
  not not_6 (not_6_out, C);
  not not_7 (not_7_out, E);
  not not_8 (not_8_out, C);
  not not_9 (not_9_out, E);
  not not_10 (not_10_out, D);
  not not_11 (not_11_out, C);
  not not_12 (not_12_out, E);
  not not_13 (not_13_out, E);
  not not_14 (not_14_out, D);
  not not_15 (not_15_out, E);
  not not_16 (not_16_out, D);
  not not_17 (not_17_out, E);
  not not_18 (not_18_out, A);
  not not_19 (not_19_out, B);
  not not_20 (not_20_out, C);
  not not_21 (not_21_out, A);
  not not_22 (not_22_out, B);
  not not_23 (not_23_out, D);
  not not_24 (not_24_out, A);
  not not_25 (not_25_out, B);
  not not_26 (not_26_out, E);
  and and_1 (and_1_out, not_1_out, not_2_out);
  and and_2 (and_2_out, C, E);
  not not_27 (not_27_out, C);
  and and_3 (and_3_out, not_3_out, not_4_out);
  and and_4 (and_4_out, D, E);
  or or_1 (c_2, not_5_out, E, C, B, A);
  and and_5 (and_5_out, not_6_out, not_7_out);
  and and_6 (and_6_out, not_8_out, D);
  and and_7 (and_7_out, D, not_9_out);
  and and_8 (and_8_out, C, not_10_out, E);
  and and_9 (and_9_out, not_11_out, not_12_out);
  and and_10 (and_10_out, D, not_13_out);
  and and_11 (and_11_out, not_14_out, not_15_out);
  and and_12 (and_12_out, C, not_16_out);
  and and_13 (and_13_out, C, not_17_out);
  and and_14 (and_14_out, not_18_out, not_19_out, not_20_out, D);
  and and_15 (and_15_out, not_21_out, not_22_out, C, not_23_out);
  and and_16 (and_16_out, not_24_out, not_25_out, C, not_26_out);
  or or_2 (a_2, and_1_out, D, and_2_out, B, A);
  or or_3 (b_2, not_27_out, and_3_out, and_4_out, B, A);
  or or_4 (d_2, and_5_out, and_6_out, and_7_out, and_8_out, B, A);
  or or_5 (e_2, and_9_out, and_10_out, B, A);
  or or_6 (f, and_11_out, and_12_out, and_13_out, B, A);
  or or_7 (g, and_14_out, and_15_out, and_16_out);
endmodule

module NS_lsb_high1 (
  input  A,
  input  B,
  input  C,
  input  D,
  input  E,
  output a_2,
  output b_2,
  output c_2,
  output d_2,
  output e_2,
  output f,
  output g
);

  wire and_1_out, and_2_out, and_3_out, and_4_out, and_5_out, and_6_out, and_7_out, and_8_out, and_9_out,
       and_10_out, and_11_out, and_12_out, and_13_out, and_14_out, and_15_out, and_16_out, and_17_out,
       and_18_out, and_19_out, and_20_out, and_21_out, and_22_out, and_23_out, and_24_out, and_25_out,
       and_26_out, and_27_out, and_28_out, and_29_out, and_30_out, and_31_out, and_32_out, and_33_out,
       and_34_out, and_35_out, and_36_out, and_37_out, and_38_out, and_39_out, and_40_out, and_41_out,
       and_42_out, and_43_out, and_44_out, and_45_out, and_46_out, and_47_out, not_1_out, not_2_out,
       not_3_out, not_4_out, not_5_out, not_6_out, not_7_out, not_8_out, not_9_out, not_10_out, not_11_out,
       not_12_out, not_13_out, not_14_out, not_15_out, not_16_out, not_17_out, not_18_out, not_19_out,
       not_20_out, not_21_out, not_22_out, not_23_out, not_24_out, not_25_out, not_26_out, not_27_out,
       not_28_out, not_29_out, not_30_out, not_31_out, not_32_out, not_33_out, not_34_out, not_35_out,
       not_36_out, not_37_out, not_38_out, not_39_out, not_40_out, not_41_out, not_42_out, not_43_out,
       not_44_out, not_45_out, not_46_out, not_47_out, not_48_out, not_49_out, not_50_out, not_51_out,
       not_52_out, not_53_out, not_54_out, not_55_out, not_56_out, not_57_out, not_58_out, not_59_out,
       not_60_out, not_61_out, not_62_out, not_63_out, not_64_out, not_65_out, not_66_out, not_67_out,
       not_68_out, not_69_out, not_70_out, not_71_out, not_72_out, not_73_out, not_74_out, not_75_out,
       not_76_out;

  not not_1 (not_1_out, B);
  not not_2 (not_2_out, D);
  not not_3 (not_3_out, C);
  not not_4 (not_4_out, E);
  not not_5 (not_5_out, A);
  not not_6 (not_6_out, A);
  not not_7 (not_7_out, B);
  not not_8 (not_8_out, C);
  not not_9 (not_9_out, D);
  not not_10 (not_10_out, D);
  not not_11 (not_11_out, E);
  not not_12 (not_12_out, A);
  not not_13 (not_13_out, B);
  not not_14 (not_14_out, A);
  not not_15 (not_15_out, C);
  not not_16 (not_16_out, A);
  not not_17 (not_17_out, D);
  not not_18 (not_18_out, E);
  not not_19 (not_19_out, B);
  not not_20 (not_20_out, D);
  not not_21 (not_21_out, C);
  not not_22 (not_22_out, A);
  not not_23 (not_23_out, D);
  not not_24 (not_24_out, E);
  not not_25 (not_25_out, A);
  not not_26 (not_26_out, B);
  not not_27 (not_27_out, A);
  not not_28 (not_28_out, D);
  not not_29 (not_29_out, B);
  not not_30 (not_30_out, C);
  not not_31 (not_31_out, A);
  not not_32 (not_32_out, B);
  not not_33 (not_33_out, C);
  not not_34 (not_34_out, E);
  not not_35 (not_35_out, A);
  not not_36 (not_36_out, C);
  not not_37 (not_37_out, A);
  not not_38 (not_38_out, E);
  not not_39 (not_39_out, B);
  not not_40 (not_40_out, D);
  not not_41 (not_41_out, A);
  not not_42 (not_42_out, D);
  not not_43 (not_43_out, B);
  not not_44 (not_44_out, E);
  not not_45 (not_45_out, A);
  not not_46 (not_46_out, B);
  not not_47 (not_47_out, C);
  not not_48 (not_48_out, E);
  not not_49 (not_49_out, E);
  not not_50 (not_50_out, D);
  not not_51 (not_51_out, E);
  not not_52 (not_52_out, A);
  not not_53 (not_53_out, B);
  not not_54 (not_54_out, B);
  not not_55 (not_55_out, C);
  not not_56 (not_56_out, D);
  not not_57 (not_57_out, B);
  not not_58 (not_58_out, E);
  not not_59 (not_59_out, A);
  not not_60 (not_60_out, D);
  not not_61 (not_61_out, A);
  not not_62 (not_62_out, E);
  not not_63 (not_63_out, B);
  not not_64 (not_64_out, D);
  not not_65 (not_65_out, E);
  not not_66 (not_66_out, C);
  not not_67 (not_67_out, A);
  not not_68 (not_68_out, D);
  not not_69 (not_69_out, A);
  not not_70 (not_70_out, E);
  not not_71 (not_71_out, B);
  not not_72 (not_72_out, D);
  not not_73 (not_73_out, C);
  not not_74 (not_74_out, D);
  not not_75 (not_75_out, E);
  not not_76 (not_76_out, B);
  and and_1 (and_1_out, not_1_out, not_2_out);
  and and_2 (and_2_out, not_3_out, not_4_out);
  and and_3 (and_3_out, not_5_out, D);
  and and_4 (and_4_out, not_6_out, C, E);
  and and_5 (and_5_out, not_7_out, C, E);
  and and_6 (and_6_out, B, D);
  and and_7 (and_7_out, A, not_8_out, not_9_out);
  and and_8 (and_8_out, A, not_10_out, not_11_out);
  and and_9 (and_9_out, not_12_out, not_13_out);
  and and_10 (and_10_out, not_14_out, not_15_out);
  and and_11 (and_11_out, not_16_out, not_17_out, not_18_out);
  and and_12 (and_12_out, not_19_out, not_20_out);
  and and_13 (and_13_out, not_21_out, D);
  and and_14 (and_14_out, not_22_out, D, E);
  and and_15 (and_15_out, A, not_23_out, E);
  and and_16 (and_16_out, A, C, not_24_out);
  and and_17 (and_17_out, not_25_out, not_26_out);
  and and_18 (and_18_out, not_27_out, not_28_out);
  and and_19 (and_19_out, not_29_out, D);
  and and_20 (and_20_out, B, C);
  and and_21 (and_21_out, A, not_30_out);
  and and_22 (and_22_out, not_31_out, not_32_out);
  and and_23 (and_23_out, not_33_out, not_34_out);
  and and_24 (and_24_out, not_35_out, not_36_out, D);
  and and_25 (and_25_out, not_37_out, D, not_38_out);
  and and_26 (and_26_out, not_39_out, C, not_40_out);
  and and_27 (and_27_out, not_41_out, C, not_42_out, E);
  and and_28 (and_28_out, not_43_out, C, E);
  and and_29 (and_29_out, A, B, not_44_out);
  and and_30 (and_30_out, not_45_out, not_46_out);
  and and_31 (and_31_out, not_47_out, not_48_out);
  and and_32 (and_32_out, B, D, not_49_out);
  and and_33 (and_33_out, A, not_50_out, not_51_out);
  and and_34 (and_34_out, not_52_out, not_53_out);
  and and_35 (and_35_out, not_54_out, not_55_out, not_56_out);
  and and_36 (and_36_out, not_57_out, D, not_58_out);
  and and_37 (and_37_out, not_59_out, C, not_60_out);
  and and_38 (and_38_out, not_61_out, C, not_62_out);
  and and_39 (and_39_out, not_63_out, C, D);
  and and_40 (and_40_out, B, not_64_out, not_65_out);
  and and_41 (and_41_out, A, B, D);
  and and_42 (and_42_out, B, not_66_out, D);
  and and_43 (and_43_out, not_67_out, B, C, not_68_out);
  and and_44 (and_44_out, not_69_out, B, C, not_70_out);
  and and_45 (and_45_out, A, not_71_out, not_72_out);
  and and_46 (and_46_out, A, not_73_out, not_74_out, not_75_out);
  and and_47 (and_47_out, A, not_76_out, C);
  or or_1 (a_2, and_1_out, and_2_out, and_3_out, and_4_out, and_5_out, and_6_out, and_7_out, and_8_out);
  or or_2 (b_2, and_9_out, and_10_out, and_11_out, and_12_out, and_13_out, and_14_out, and_15_out, and_16_out);
  or or_3 (c_2, and_17_out, and_18_out, E, and_19_out, and_20_out, and_21_out);
  or or_4 (d_2, and_22_out, and_23_out, and_24_out, and_25_out, and_26_out, and_27_out, and_28_out, and_29_out);
  or or_5 (e_2, and_30_out, and_31_out, and_32_out, and_33_out);
  or or_6 (f, and_34_out, and_35_out, and_36_out, and_37_out, and_38_out, and_39_out, and_40_out, and_41_out);
  or or_7 (g, and_42_out, and_43_out, and_44_out, and_45_out, and_46_out, and_47_out);
endmodule

module NS_msb_high_1 (
  input  A,
  input  B,
  input  C,
  input  D,
  input  E,
  output a_2,
  output b_2,
  output c_2,
  output d_2,
  output e_2,
  output f,
  output g
);

  wire and_1_out, and_2_out, and_3_out, and_4_out, and_5_out, and_6_out, and_7_out, and_8_out, not_1_out,
       not_2_out, not_3_out, not_4_out, not_5_out, not_6_out, not_7_out, not_8_out, not_9_out, not_10_out,
       not_11_out, not_12_out, not_13_out, not_14_out, not_15_out, not_16_out, not_17_out, not_18_out,
       not_19_out, not_20_out;

  not not_1 (not_1_out, B);
  not not_2 (not_2_out, C);
  not not_3 (not_3_out, D);
  not not_4 (not_4_out, A);
  not not_5 (not_5_out, B);
  not not_6 (not_6_out, C);
  not not_7 (not_7_out, B);
  not not_8 (not_8_out, C);
  not not_9 (not_9_out, D);
  not not_10 (not_10_out, B);
  not not_11 (not_11_out, C);
  not not_12 (not_12_out, D);
  not not_13 (not_13_out, B);
  not not_14 (not_14_out, C);
  not not_15 (not_15_out, D);
  not not_16 (not_16_out, D);
  not not_17 (not_17_out, A);
  and and_1 (and_1_out, not_1_out, not_2_out, not_3_out);
  and and_2 (and_2_out, B, C);
  or or_1 (c_2, not_4_out, not_5_out, not_6_out, D);
  not not_18 (not_18_out, A);
  and and_3 (and_3_out, not_7_out, not_8_out, not_9_out);
  and and_4 (and_4_out, B, C);
  not not_19 (not_19_out, A);
  and and_5 (and_5_out, not_10_out, not_11_out, not_12_out);
  and and_6 (and_6_out, B, C);
  not not_20 (not_20_out, A);
  and and_7 (and_7_out, not_13_out, not_14_out, not_15_out);
  and and_8 (and_8_out, B, C, D);
  and and_9 (g, A, B, C, not_16_out);
  or or_2 (a_2, not_17_out, and_1_out, and_2_out);
  or or_3 (d_2, not_18_out, and_3_out, and_4_out);
  or or_4 (e_2, not_19_out, and_5_out, and_6_out);
  or or_5 (f, not_20_out, and_7_out, and_8_out);

  assign b_2 = 1'b1;
endmodule

module NS_light_high (
  input  A,
  input  B,
  input  C,
  input  D,
  input  E,
  output a_2,
  output b_2
);

  wire and_1_out, and_2_out, and_3_out, not_1_out, not_2_out, not_3_out, not_4_out;

  and and_1 (and_1_out, B, E);
  and and_2 (and_2_out, B, D);
  and and_3 (and_3_out, B, C);
  not not_1 (not_1_out, A);
  not not_2 (not_2_out, C);
  not not_3 (not_3_out, D);
  not not_4 (not_4_out, E);
  or or_1 (a_2, and_1_out, and_2_out, and_3_out, A);
  and and_4 (b_2, not_1_out, not_2_out, not_3_out, not_4_out);
endmodule

module NS_light_low (
  input  A,
  input  B,
  input  C,
  input  D,
  input  E,
  output a_2,
  output b_2
);

  wire and_1_out, and_2_out, and_3_out, not_1_out, not_2_out, not_3_out, not_4_out, not_5_out, not_6_out,
       not_7_out, not_8_out, not_9_out, not_10_out;

  not not_1 (not_1_out, A);
  not not_2 (not_2_out, B);
  not not_3 (not_3_out, A);
  not not_4 (not_4_out, B);
  not not_5 (not_5_out, A);
  not not_6 (not_6_out, B);
  not not_7 (not_7_out, A);
  not not_8 (not_8_out, C);
  not not_9 (not_9_out, D);
  not not_10 (not_10_out, E);
  and and_1 (and_1_out, not_1_out, not_2_out, E);
  and and_2 (and_2_out, not_3_out, not_4_out, D);
  and and_3 (and_3_out, not_5_out, not_6_out, C);
  and and_4 (b_2, not_7_out, not_8_out, not_9_out, not_10_out);
  or or_1 (a_2, and_1_out, and_2_out, and_3_out);
endmodule

module LSB_MODERATE_2 (
  input  A,
  input  B,
  input  C,
  input  D,
  input  E,
  input  F,
  output A_2,
  output b_2,
  output c_2,
  output d_2,
  output e_2,
  output f_2,
  output g
);

  wire and_1_out, and_2_out, and_3_out, and_4_out, and_5_out, and_6_out, and_7_out, and_8_out, and_9_out,
       and_10_out, and_11_out, and_12_out, and_13_out, and_14_out, and_15_out, and_16_out, and_17_out,
       and_18_out, and_19_out, and_20_out, and_21_out, and_22_out, and_23_out, and_24_out, and_25_out,
       and_26_out, and_27_out, and_28_out, and_29_out, not_1_out, not_2_out, not_3_out, not_4_out, not_5_out,
       not_6_out, not_7_out, not_8_out, not_9_out, not_10_out, not_11_out, not_12_out, not_13_out,
       not_14_out, not_15_out, not_16_out, not_17_out, not_18_out, not_19_out, not_20_out, not_21_out,
       not_22_out, not_23_out, not_24_out, not_25_out, not_26_out, not_27_out, not_28_out, not_29_out,
       not_30_out, not_31_out, not_32_out, not_33_out, not_34_out, not_35_out, not_36_out, not_37_out,
       not_38_out, not_39_out, not_40_out, not_41_out, not_42_out, not_43_out, not_44_out, not_45_out,
       not_46_out, not_47_out, not_48_out;

  not not_1 (not_1_out, D);
  not not_2 (not_2_out, F);
  not not_3 (not_3_out, C);
  not not_4 (not_4_out, E);
  not not_5 (not_5_out, E);
  not not_6 (not_6_out, F);
  not not_7 (not_7_out, C);
  not not_8 (not_8_out, E);
  not not_9 (not_9_out, D);
  not not_10 (not_10_out, D);
  not not_11 (not_11_out, F);
  not not_12 (not_12_out, C);
  not not_13 (not_13_out, D);
  not not_14 (not_14_out, C);
  not not_15 (not_15_out, F);
  not not_16 (not_16_out, E);
  not not_17 (not_17_out, E);
  not not_18 (not_18_out, F);
  not not_19 (not_19_out, D);
  not not_20 (not_20_out, F);
  not not_21 (not_21_out, C);
  not not_22 (not_22_out, F);
  not not_23 (not_23_out, E);
  not not_24 (not_24_out, F);
  not not_25 (not_25_out, C);
  not not_26 (not_26_out, E);
  not not_27 (not_27_out, F);
  not not_28 (not_28_out, C);
  not not_29 (not_29_out, E);
  not not_30 (not_30_out, C);
  not not_31 (not_31_out, F);
  not not_32 (not_32_out, D);
  not not_33 (not_33_out, E);
  not not_34 (not_34_out, D);
  not not_35 (not_35_out, F);
  not not_36 (not_36_out, A);
  not not_37 (not_37_out, B);
  not not_38 (not_38_out, C);
  not not_39 (not_39_out, D);
  not not_40 (not_40_out, A);
  not not_41 (not_41_out, B);
  not not_42 (not_42_out, E);
  not not_43 (not_43_out, A);
  not not_44 (not_44_out, B);
  not not_45 (not_45_out, F);
  not not_46 (not_46_out, B);
  not not_47 (not_47_out, E);
  and and_1 (and_1_out, not_1_out, not_2_out);
  and and_2 (and_2_out, not_3_out, E);
  and and_3 (and_3_out, D, F);
  and and_4 (and_4_out, C, not_4_out);
  not not_48 (not_48_out, D);
  and and_5 (and_5_out, not_5_out, not_6_out);
  and and_6 (and_6_out, E, F);
  and and_7 (and_7_out, not_7_out, not_8_out);
  and and_8 (and_8_out, D, E);
  and and_9 (and_9_out, C, not_9_out);
  and and_10 (and_10_out, not_10_out, not_11_out);
  and and_11 (and_11_out, not_12_out, not_13_out, E);
  and and_12 (and_12_out, not_14_out, E, not_15_out);
  and and_13 (and_13_out, D, not_16_out, F);
  and and_14 (and_14_out, C, not_17_out, not_18_out);
  and and_15 (and_15_out, C, D, F);
  and and_16 (and_16_out, not_19_out, not_20_out);
  and and_17 (and_17_out, not_21_out, E, not_22_out);
  and and_18 (and_18_out, C, not_23_out, not_24_out);
  and and_19 (and_19_out, C, D, E, F);
  and and_20 (and_20_out, not_25_out, not_26_out, not_27_out);
  and and_21 (and_21_out, not_28_out, D, not_29_out);
  and and_22 (and_22_out, not_30_out, D, not_31_out);
  and and_23 (and_23_out, C, not_32_out, not_33_out);
  and and_24 (and_24_out, C, not_34_out, not_35_out);
  and and_25 (and_25_out, C, D, E);
  and and_26 (and_26_out, not_36_out, not_37_out, not_38_out, not_39_out, E);
  and and_27 (and_27_out, not_40_out, not_41_out, D, not_42_out);
  and and_28 (and_28_out, not_43_out, not_44_out, D, not_45_out);
  and and_29 (and_29_out, not_46_out, C, not_47_out);
  or or_1 (A_2, and_1_out, and_2_out, and_3_out, and_4_out, B, A);
  or or_2 (b_2, not_48_out, and_5_out, and_6_out, C, B, A);
  or or_3 (c_2, and_7_out, F, and_8_out, and_9_out, B, A);
  or or_4 (d_2, and_10_out, and_11_out, and_12_out, and_13_out, and_14_out, and_15_out, B, A);
  or or_5 (e_2, and_16_out, and_17_out, and_18_out, and_19_out, B, A);
  or or_6 (f_2, and_20_out, and_21_out, and_22_out, and_23_out, and_24_out, and_25_out, B, A);
  or or_7 (g, and_26_out, and_27_out, and_28_out, and_29_out);
endmodule

module ns_MSB_MODERATE_2 (
  input  A,
  input  B,
  input  C,
  input  D,
  input  E,
  input  F,
  output A2,
  output b_2,
  output c_2,
  output d_2,
  output e_2,
  output f_2,
  output g
);

  wire and_1_out, and_2_out, and_3_out, and_4_out, and_5_out, and_6_out, and_7_out, and_8_out, not_1_out,
       not_2_out, not_3_out, not_4_out, not_5_out, not_6_out, not_7_out, not_8_out, not_9_out, not_10_out,
       not_11_out, not_12_out, not_13_out, not_14_out;

  not not_1 (not_1_out, D);
  not not_2 (not_2_out, E);
  not not_3 (not_3_out, D);
  not not_4 (not_4_out, E);
  not not_5 (not_5_out, D);
  not not_6 (not_6_out, E);
  not not_7 (not_7_out, D);
  not not_8 (not_8_out, E);
  not not_9 (not_9_out, B);
  not not_10 (not_10_out, E);
  not not_11 (not_11_out, C);
  and and_1 (and_1_out, not_1_out, not_2_out);
  and and_2 (and_2_out, D, E, F);
  not not_12 (not_12_out, C);
  and and_3 (and_3_out, not_3_out, not_4_out);
  and and_4 (and_4_out, D, E, F);
  not not_13 (not_13_out, C);
  and and_5 (and_5_out, not_5_out, not_6_out);
  and and_6 (and_6_out, D, E, F);
  not not_14 (not_14_out, C);
  and and_7 (and_7_out, not_7_out, not_8_out);
  and and_8 (and_8_out, D, E, F);
  and and_9 (g, A, not_9_out, C, not_10_out);
  or or_1 (A2, not_11_out, and_1_out, and_2_out, B, A);
  or or_2 (d_2, not_12_out, and_3_out, and_4_out, B, A);
  or or_3 (e_2, not_13_out, and_5_out, and_6_out, B, A);
  or or_4 (f_2, not_14_out, and_7_out, and_8_out, B, A);

  assign b_2 = 1'b1;
  assign c_2 = 1'b1;
endmodule

// L-H
module low_high (
  input  Enable,
  input  Counter,
  input  Reset,
  output N1,
  output N0,
  output W1,
  output W0,
  output E1,
  output E0,
  output S1,
  output S0
);

  wire Clk_out, ns_lsb_high1_1_a_2, ns_lsb_high1_1_b_2, ns_lsb_high1_1_c_2, ns_lsb_high1_1_d_2,
       ns_lsb_high1_1_e_2, ns_lsb_high1_1_f, ns_lsb_high1_1_g, ns_lsb_low_1_1_a_2, ns_lsb_low_1_1_b_2,
       ns_lsb_low_1_1_c_2, ns_lsb_low_1_1_d_2, ns_lsb_low_1_1_e_2, ns_lsb_low_1_1_f, ns_lsb_low_1_1_g,
       ns_msb_high_1_1_a_2, ns_msb_high_1_1_b_2, ns_msb_high_1_1_c_2, ns_msb_high_1_1_d_2,
       ns_msb_high_1_1_e_2, ns_msb_high_1_1_f, ns_msb_high_1_1_g, ns_msb_low_1_1_a_2, ns_msb_low_1_1_b_2,
       ns_msb_low_1_1_c_2, ns_msb_low_1_1_d_2, ns_msb_low_1_1_e_2, ns_msb_low_1_1_f, ns_msb_low_1_1_g;
  wire [4:0] counter_1_q;

  Clock Clk (.out(Clk_out));
  Counter #(.width(5), .max('h1e)) counter_1 (
    .load(Enable), .count(Counter), .Q(counter_1_q), .clk(Clk_out), .clr(Reset));  // open: D, carry
  NS_light_low ns_light_low_1 (
    .A(counter_1_q[4]), .B(counter_1_q[3]), .C(counter_1_q[2]), .D(counter_1_q[1]), .E(counter_1_q[0]),
    .a_2(N1), .b_2(N0));
  NS_light_high ns_light_high_1 (
    .A(counter_1_q[4]), .B(counter_1_q[3]), .C(counter_1_q[2]), .D(counter_1_q[1]), .E(counter_1_q[0]),
    .a_2(E1), .b_2(E0));
  NS_lsb_high1 ns_lsb_high1_1 (
    .A(counter_1_q[4]), .B(counter_1_q[3]), .C(counter_1_q[2]), .D(counter_1_q[1]), .E(counter_1_q[0]),
    .a_2(ns_lsb_high1_1_a_2), .b_2(ns_lsb_high1_1_b_2), .c_2(ns_lsb_high1_1_c_2), .d_2(ns_lsb_high1_1_d_2),
    .e_2(ns_lsb_high1_1_e_2), .f(ns_lsb_high1_1_f), .g(ns_lsb_high1_1_g));
  NS_msb_high_1 ns_msb_high_1_1 (
    .A(counter_1_q[4]), .B(counter_1_q[3]), .C(counter_1_q[2]), .D(counter_1_q[1]), .E(counter_1_q[0]),
    .a_2(ns_msb_high_1_1_a_2), .b_2(ns_msb_high_1_1_b_2), .c_2(ns_msb_high_1_1_c_2),
    .d_2(ns_msb_high_1_1_d_2), .e_2(ns_msb_high_1_1_e_2), .f(ns_msb_high_1_1_f), .g(ns_msb_high_1_1_g));
  NS_lsb_low_1 ns_lsb_low_1_1 (
    .A(counter_1_q[4]), .B(counter_1_q[3]), .C(counter_1_q[2]), .D(counter_1_q[1]), .E(counter_1_q[0]),
    .a_2(ns_lsb_low_1_1_a_2), .b_2(ns_lsb_low_1_1_b_2), .c_2(ns_lsb_low_1_1_c_2), .d_2(ns_lsb_low_1_1_d_2),
    .e_2(ns_lsb_low_1_1_e_2), .f(ns_lsb_low_1_1_f), .g(ns_lsb_low_1_1_g));
  NS_msb_low_1 ns_msb_low_1_1 (
    .A(counter_1_q[4]), .B(counter_1_q[3]), .C(counter_1_q[2]), .D(counter_1_q[1]), .E(counter_1_q[0]),
    .a_2(ns_msb_low_1_1_a_2), .b_2(ns_msb_low_1_1_b_2), .c_2(ns_msb_low_1_1_c_2), .d_2(ns_msb_low_1_1_d_2),
    .e_2(ns_msb_low_1_1_e_2), .f(ns_msb_low_1_1_f), .g(ns_msb_low_1_1_g));
  _7_Segment_Display u_7_segment_display_1 (
    .g(ns_msb_high_1_1_g), .f(ns_msb_high_1_1_f), .a(ns_msb_high_1_1_a_2), .b(ns_msb_high_1_1_b_2),
    .e(ns_msb_high_1_1_e_2), .d(ns_msb_high_1_1_d_2), .c(ns_msb_high_1_1_c_2));  // open: dp
  _7_Segment_Display u_7_segment_display_2 (
    .g(ns_lsb_high1_1_g), .f(ns_lsb_high1_1_f), .a(ns_lsb_high1_1_a_2), .b(ns_lsb_high1_1_b_2),
    .e(ns_lsb_high1_1_e_2), .d(ns_lsb_high1_1_d_2), .c(ns_lsb_high1_1_c_2));  // open: dp
  _7_Segment_Display u_7_segment_display_3 (
    .g(ns_msb_low_1_1_g), .f(ns_msb_low_1_1_f), .a(ns_msb_low_1_1_a_2), .b(ns_msb_low_1_1_b_2),
    .e(ns_msb_low_1_1_e_2), .d(ns_msb_low_1_1_d_2), .c(ns_msb_low_1_1_c_2));  // open: dp
  _7_Segment_Display u_7_segment_display_4 (
    .g(ns_lsb_low_1_1_g), .f(ns_lsb_low_1_1_f), .a(ns_lsb_low_1_1_a_2), .b(ns_lsb_low_1_1_b_2),
    .e(ns_lsb_low_1_1_e_2), .d(ns_lsb_low_1_1_d_2), .c(ns_lsb_low_1_1_c_2));  // open: dp

  assign S0 = N0;
  assign S1 = N1;
  assign W0 = E0;
  assign W1 = E1;

  // Notes on the sheet:
  //   low high
  //   WEST
  //   NORTH
  //   SOUTH
  //   EAST
endmodule

module EW_LSB_HIGH_2 (
  input  A,
  input  B,
  input  C,
  input  D,
  input  E,
  input  F,
  output A2,
  output b_2,
  output c_2,
  output d_2,
  output e_2,
  output f_2,
  output g
);

  wire and_1_out, and_2_out, and_3_out, and_4_out, and_5_out, and_6_out, and_7_out, and_8_out, and_9_out,
       and_10_out, and_11_out, and_12_out, and_13_out, and_14_out, and_15_out, and_16_out, and_17_out,
       and_18_out, and_19_out, and_20_out, and_21_out, and_22_out, and_23_out, and_24_out, and_25_out,
       and_26_out, and_27_out, and_28_out, and_29_out, and_30_out, and_31_out, and_32_out, and_33_out,
       and_34_out, and_35_out, and_36_out, and_37_out, and_38_out, and_39_out, and_40_out, and_41_out,
       and_42_out, and_43_out, and_44_out, and_45_out, and_46_out, and_47_out, and_48_out, and_49_out,
       and_50_out, and_51_out, and_52_out, not_1_out, not_2_out, not_3_out, not_4_out, not_5_out, not_6_out,
       not_7_out, not_8_out, not_9_out, not_10_out, not_11_out, not_12_out, not_13_out, not_14_out,
       not_15_out, not_16_out, not_17_out, not_18_out, not_19_out, not_20_out, not_21_out, not_22_out,
       not_23_out, not_24_out, not_25_out, not_26_out, not_27_out, not_28_out, not_29_out, not_30_out,
       not_31_out, not_32_out, not_33_out, not_34_out, not_35_out, not_36_out, not_37_out, not_38_out,
       not_39_out, not_40_out, not_41_out, not_42_out, not_43_out, not_44_out, not_45_out, not_46_out,
       not_47_out, not_48_out, not_49_out, not_50_out, not_51_out, not_52_out, not_53_out, not_54_out,
       not_55_out, not_56_out, not_57_out, not_58_out, not_59_out, not_60_out, not_61_out, not_62_out,
       not_63_out, not_64_out, not_65_out, not_66_out, not_67_out, not_68_out, not_69_out, not_70_out,
       not_71_out, not_72_out, not_73_out, not_74_out, not_75_out, not_76_out, not_77_out, not_78_out;

  not not_1 (not_1_out, B);
  not not_2 (not_2_out, D);
  not not_3 (not_3_out, B);
  not not_4 (not_4_out, C);
  not not_5 (not_5_out, E);
  not not_6 (not_6_out, C);
  not not_7 (not_7_out, F);
  not not_8 (not_8_out, A);
  not not_9 (not_9_out, C);
  not not_10 (not_10_out, B);
  not not_11 (not_11_out, D);
  not not_12 (not_12_out, E);
  not not_13 (not_13_out, E);
  not not_14 (not_14_out, F);
  not not_15 (not_15_out, D);
  not not_16 (not_16_out, C);
  not not_17 (not_17_out, E);
  not not_18 (not_18_out, C);
  not not_19 (not_19_out, E);
  not not_20 (not_20_out, A);
  not not_21 (not_21_out, B);
  not not_22 (not_22_out, B);
  not not_23 (not_23_out, C);
  not not_24 (not_24_out, E);
  not not_25 (not_25_out, A);
  not not_26 (not_26_out, C);
  not not_27 (not_27_out, D);
  not not_28 (not_28_out, F);
  not not_29 (not_29_out, A);
  not not_30 (not_30_out, C);
  not not_31 (not_31_out, E);
  not not_32 (not_32_out, B);
  not not_33 (not_33_out, B);
  not not_34 (not_34_out, D);
  not not_35 (not_35_out, F);
  not not_36 (not_36_out, A);
  not not_37 (not_37_out, B);
  not not_38 (not_38_out, B);
  not not_39 (not_39_out, C);
  not not_40 (not_40_out, E);
  not not_41 (not_41_out, B);
  not not_42 (not_42_out, B);
  not not_43 (not_43_out, D);
  not not_44 (not_44_out, A);
  not not_45 (not_45_out, B);
  not not_46 (not_46_out, B);
  not not_47 (not_47_out, B);
  not not_48 (not_48_out, C);
  not not_49 (not_49_out, A);
  not not_50 (not_50_out, C);
  not not_51 (not_51_out, E);
  not not_52 (not_52_out, B);
  not not_53 (not_53_out, D);
  not not_54 (not_54_out, E);
  not not_55 (not_55_out, A);
  not not_56 (not_56_out, C);
  not not_57 (not_57_out, A);
  not not_58 (not_58_out, C);
  not not_59 (not_59_out, D);
  not not_60 (not_60_out, A);
  not not_61 (not_61_out, A);
  not not_62 (not_62_out, E);
  not not_63 (not_63_out, A);
  not not_64 (not_64_out, E);
  not not_65 (not_65_out, F);
  not not_66 (not_66_out, A);
  not not_67 (not_67_out, B);
  not not_68 (not_68_out, C);
  not not_69 (not_69_out, D);
  not not_70 (not_70_out, E);
  not not_71 (not_71_out, B);
  not not_72 (not_72_out, C);
  not not_73 (not_73_out, D);
  not not_74 (not_74_out, F);
  and and_1 (and_1_out, not_1_out, not_2_out);
  and and_2 (and_2_out, not_3_out, F);
  and and_3 (and_3_out, not_4_out, not_5_out, F);
  and and_4 (and_4_out, not_6_out, E, not_7_out);
  and and_5 (and_5_out, not_8_out, not_9_out, D);
  and and_6 (and_6_out, D, E);
  and and_7 (and_7_out, not_10_out, C);
  and and_8 (and_8_out, C, not_11_out, not_12_out);
  and and_9 (and_9_out, C, not_13_out, not_14_out);
  and and_10 (and_10_out, C, not_15_out, F);
  and and_11 (and_11_out, A, B);
  not not_75 (not_75_out, B);
  not not_76 (not_76_out, D);
  and and_12 (and_12_out, not_16_out, E);
  and and_13 (and_13_out, C, not_17_out);
  not not_77 (not_77_out, B);
  not not_78 (not_78_out, F);
  and and_14 (and_14_out, not_18_out, E);
  and and_15 (and_15_out, C, not_19_out);
  and and_16 (and_16_out, not_20_out, not_21_out);
  and and_17 (and_17_out, not_22_out, F);
  and and_18 (and_18_out, not_23_out, not_24_out, F);
  and and_19 (and_19_out, not_25_out, not_26_out, not_27_out, E, not_28_out);
  and and_20 (and_20_out, not_29_out, not_30_out, D, not_31_out);
  and and_21 (and_21_out, not_32_out, D, E);
  and and_22 (and_22_out, D, E, F);
  and and_23 (and_23_out, not_33_out, C);
  and and_24 (and_24_out, C, not_34_out, F);
  and and_25 (and_25_out, C, D, not_35_out);
  and and_26 (and_26_out, A, B);
  and and_27 (and_27_out, not_36_out, not_37_out);
  and and_28 (and_28_out, not_38_out, F);
  and and_29 (and_29_out, not_39_out, not_40_out, F);
  and and_30 (and_30_out, not_41_out, D, E);
  and and_31 (and_31_out, D, E, F);
  and and_32 (and_32_out, not_42_out, C);
  and and_33 (and_33_out, C, not_43_out, F);
  and and_34 (and_34_out, A, B);
  and and_35 (and_35_out, not_44_out, not_45_out);
  and and_36 (and_36_out, not_46_out, F);
  and and_37 (and_37_out, not_47_out, E);
  and and_38 (and_38_out, not_48_out, E, F);
  and and_39 (and_39_out, not_49_out, not_50_out, D, not_51_out);
  and and_40 (and_40_out, D, F);
  and and_41 (and_41_out, not_52_out, C);
  and and_42 (and_42_out, C, not_53_out, not_54_out);
  and and_43 (and_43_out, C, D, E);
  and and_44 (and_44_out, A, B);
  and and_45 (and_45_out, not_55_out, B, not_56_out, F);
  and and_46 (and_46_out, not_57_out, B, not_58_out, not_59_out, E);
  and and_47 (and_47_out, not_60_out, B, E, F);
  and and_48 (and_48_out, not_61_out, B, D, not_62_out);
  and and_49 (and_49_out, not_63_out, B, C, not_64_out, not_65_out);
  and and_50 (and_50_out, not_66_out, B, C, D);
  and and_51 (and_51_out, A, not_67_out, not_68_out, not_69_out, not_70_out, F);
  and and_52 (and_52_out, A, not_71_out, not_72_out, not_73_out, E, not_74_out);
  or or_1 (A2, and_1_out, and_2_out, and_3_out, and_4_out, and_5_out, and_6_out, and_7_out, and_8_out, and_9_out, and_10_out, and_11_out);
  or or_2 (b_2, not_75_out, not_76_out, and_12_out, and_13_out, A);
  or or_3 (c_2, not_77_out, not_78_out, and_14_out, D, and_15_out, A);
  or or_4 (d_2, and_16_out, and_17_out, and_18_out, and_19_out, and_20_out, and_21_out, and_22_out, and_23_out, and_24_out, and_25_out, and_26_out);
  or or_5 (e_2, and_27_out, and_28_out, and_29_out, and_30_out, and_31_out, and_32_out, and_33_out, and_34_out);
  or or_6 (f_2, and_35_out, and_36_out, and_37_out, and_38_out, and_39_out, and_40_out, and_41_out, and_42_out, and_43_out, and_44_out);
  or or_7 (g, and_45_out, and_46_out, and_47_out, and_48_out, and_49_out, and_50_out, and_51_out, and_52_out);
endmodule

module ewmSB_MODERATE_2 (
  input  A,
  input  B,
  input  C,
  input  D,
  input  E,
  input  F,
  output A2,
  output b_2,
  output c_2,
  output d_2,
  output e_2,
  output f_2,
  output g
);

  wire and_1_out, and_2_out, and_3_out, and_4_out, and_5_out, and_6_out, and_7_out, and_8_out, and_9_out,
       and_10_out, and_11_out, and_12_out, and_13_out, and_14_out, and_15_out, and_16_out, and_17_out,
       and_18_out, and_19_out, and_20_out, and_21_out, and_22_out, and_23_out, and_24_out, and_25_out,
       and_26_out, and_27_out, and_28_out, and_29_out, not_1_out, not_2_out, not_3_out, not_4_out, not_5_out,
       not_6_out, not_7_out, not_8_out, not_9_out, not_10_out, not_11_out, not_12_out, not_13_out,
       not_14_out, not_15_out, not_16_out, not_17_out, not_18_out, not_19_out, not_20_out, not_21_out,
       not_22_out, not_23_out, not_24_out, not_25_out, not_26_out, not_27_out, not_28_out, not_29_out,
       not_30_out, not_31_out, not_32_out, not_33_out, not_34_out, not_35_out, not_36_out, not_37_out,
       not_38_out, not_39_out, not_40_out, not_41_out, not_42_out, not_43_out, not_44_out, not_45_out,
       not_46_out, not_47_out;

  not not_1 (not_1_out, A);
  not not_2 (not_2_out, B);
  not not_3 (not_3_out, A);
  not not_4 (not_4_out, D);
  not not_5 (not_5_out, E);
  not not_6 (not_6_out, F);
  not not_7 (not_7_out, B);
  not not_8 (not_8_out, B);
  not not_9 (not_9_out, C);
  not not_10 (not_10_out, D);
  not not_11 (not_11_out, E);
  not not_12 (not_12_out, F);
  not not_13 (not_13_out, A);
  not not_14 (not_14_out, B);
  not not_15 (not_15_out, A);
  not not_16 (not_16_out, D);
  not not_17 (not_17_out, E);
  not not_18 (not_18_out, F);
  not not_19 (not_19_out, B);
  not not_20 (not_20_out, B);
  not not_21 (not_21_out, C);
  not not_22 (not_22_out, A);
  not not_23 (not_23_out, B);
  not not_24 (not_24_out, A);
  not not_25 (not_25_out, D);
  not not_26 (not_26_out, E);
  not not_27 (not_27_out, F);
  not not_28 (not_28_out, B);
  not not_29 (not_29_out, B);
  not not_30 (not_30_out, C);
  not not_31 (not_31_out, A);
  not not_32 (not_32_out, B);
  not not_33 (not_33_out, A);
  not not_34 (not_34_out, D);
  not not_35 (not_35_out, E);
  not not_36 (not_36_out, F);
  not not_37 (not_37_out, B);
  not not_38 (not_38_out, B);
  not not_39 (not_39_out, C);
  not not_40 (not_40_out, B);
  not not_41 (not_41_out, C);
  not not_42 (not_42_out, D);
  not not_43 (not_43_out, B);
  not not_44 (not_44_out, C);
  not not_45 (not_45_out, E);
  not not_46 (not_46_out, F);
  and and_1 (and_1_out, not_1_out, not_2_out);
  and and_2 (and_2_out, not_3_out, not_4_out, not_5_out, not_6_out);
  and and_3 (and_3_out, not_7_out, E, F);
  and and_4 (and_4_out, not_8_out, D);
  and and_5 (and_5_out, B, not_9_out);
  and and_6 (and_6_out, A, C);
  not not_47 (not_47_out, A);
  and and_7 (and_7_out, not_10_out, not_11_out);
  and and_8 (and_8_out, E, not_12_out);
  and and_9 (and_9_out, D, F);
  and and_10 (and_10_out, not_13_out, not_14_out);
  and and_11 (and_11_out, not_15_out, not_16_out, not_17_out, not_18_out);
  and and_12 (and_12_out, not_19_out, E, F);
  and and_13 (and_13_out, not_20_out, D);
  and and_14 (and_14_out, B, not_21_out);
  and and_15 (and_15_out, A, C);
  and and_16 (and_16_out, not_22_out, not_23_out);
  and and_17 (and_17_out, not_24_out, not_25_out, not_26_out, not_27_out);
  and and_18 (and_18_out, not_28_out, E, F);
  and and_19 (and_19_out, not_29_out, D);
  and and_20 (and_20_out, B, not_30_out);
  and and_21 (and_21_out, A, C);
  and and_22 (and_22_out, not_31_out, not_32_out);
  and and_23 (and_23_out, not_33_out, not_34_out, not_35_out, not_36_out);
  and and_24 (and_24_out, not_37_out, D, F);
  and and_25 (and_25_out, not_38_out, D, E);
  and and_26 (and_26_out, B, not_39_out);
  and and_27 (and_27_out, A, C);
  and and_28 (and_28_out, A, not_40_out, not_41_out, not_42_out, E, F);
  and and_29 (and_29_out, A, not_43_out, not_44_out, D, not_45_out, not_46_out);
  or or_1 (A2, and_1_out, and_2_out, and_3_out, and_4_out, and_5_out, and_6_out);
  or or_2 (c_2, not_47_out, and_7_out, and_8_out, and_9_out, C, B);
  or or_3 (d_2, and_10_out, and_11_out, and_12_out, and_13_out, and_14_out, and_15_out);
  or or_4 (e_2, and_16_out, and_17_out, and_18_out, and_19_out, and_20_out, and_21_out);
  or or_5 (f_2, and_22_out, and_23_out, and_24_out, and_25_out, and_26_out, and_27_out);
  or or_6 (g, and_28_out, and_29_out);

  assign b_2 = 1'b1;
endmodule

module lightlsb_MODERATE_2 (
  input  A,
  input  B,
  input  C,
  input  D,
  input  E,
  input  F,
  output b_2,
  output c_2
);

  wire and_1_out, and_2_out, and_3_out, and_4_out, and_5_out, and_6_out, not_1_out, not_2_out, not_3_out,
       not_4_out, not_5_out, not_6_out, not_7_out;

  or or_1 (b_2, B, A);
  not not_1 (not_1_out, A);
  not not_2 (not_2_out, B);
  not not_3 (not_3_out, C);
  not not_4 (not_4_out, D);
  not not_5 (not_5_out, E);
  not not_6 (not_6_out, F);
  not not_7 (not_7_out, B);
  and and_1 (and_1_out, not_1_out, not_2_out, not_3_out, not_4_out, not_5_out, not_6_out);
  and and_2 (and_2_out, not_7_out, C, D, E, F);
  and and_3 (and_3_out, A, D, F);
  and and_4 (and_4_out, A, D, E);
  and and_5 (and_5_out, A, C);
  and and_6 (and_6_out, A, B);
  or or_2 (c_2, and_1_out, and_2_out, and_3_out, and_4_out, and_5_out, and_6_out);
endmodule

module ewlight_MODERATE_2 (
  input  A,
  input  B,
  input  C,
  input  D,
  input  E,
  input  F,
  output b_2,
  output c_2
);

  wire and_1_out, and_2_out, and_3_out, and_4_out, and_5_out, and_6_out, and_7_out, and_8_out, and_9_out,
       and_10_out, and_11_out, and_12_out, and_13_out, and_14_out, and_15_out, and_16_out, not_1_out,
       not_2_out, not_3_out, not_4_out, not_5_out, not_6_out, not_7_out, not_8_out, not_9_out, not_10_out,
       not_11_out, not_12_out, not_13_out, not_14_out, not_15_out, not_16_out, not_17_out, not_18_out,
       not_19_out, not_20_out, not_21_out, not_22_out;

  not not_1 (not_1_out, A);
  not not_2 (not_2_out, B);
  not not_3 (not_3_out, C);
  not not_4 (not_4_out, A);
  not not_5 (not_5_out, B);
  not not_6 (not_6_out, C);
  not not_7 (not_7_out, A);
  not not_8 (not_8_out, B);
  not not_9 (not_9_out, C);
  not not_10 (not_10_out, B);
  not not_11 (not_11_out, D);
  not not_12 (not_12_out, B);
  not not_13 (not_13_out, E);
  not not_14 (not_14_out, B);
  not not_15 (not_15_out, F);
  not not_16 (not_16_out, A);
  not not_17 (not_17_out, B);
  not not_18 (not_18_out, C);
  not not_19 (not_19_out, D);
  not not_20 (not_20_out, E);
  not not_21 (not_21_out, F);
  not not_22 (not_22_out, B);
  and and_1 (and_1_out, not_1_out, not_2_out, not_3_out, F);
  and and_2 (and_2_out, not_4_out, not_5_out, not_6_out, E);
  and and_3 (and_3_out, not_7_out, not_8_out, not_9_out, D);
  and and_4 (and_4_out, not_10_out, C, not_11_out);
  and and_5 (and_5_out, not_12_out, C, not_13_out);
  and and_6 (and_6_out, not_14_out, C, not_15_out);
  and and_7 (and_7_out, A, D, F);
  and and_8 (and_8_out, A, D, E);
  and and_9 (and_9_out, A, C);
  and and_10 (and_10_out, A, B);
  and and_11 (and_11_out, not_16_out, not_17_out, not_18_out, not_19_out, not_20_out, not_21_out);
  and and_12 (and_12_out, not_22_out, C, D, E, F);
  and and_13 (and_13_out, A, D, F);
  and and_14 (and_14_out, A, D, E);
  and and_15 (and_15_out, A, C);
  and and_16 (and_16_out, A, B);
  or or_1 (b_2, and_1_out, and_2_out, and_3_out, and_4_out, and_5_out, and_6_out, and_7_out, and_8_out, and_9_out, and_10_out);
  or or_2 (c_2, and_11_out, and_12_out, and_13_out, and_14_out, and_15_out, and_16_out);
endmodule

// M-H
module mod_high (
  input  Enable,
  input  Counter,
  input  Reset,
  output N1,
  output N0,
  output W1,
  output W0,
  output E1,
  output E0,
  output S1,
  output S0
);

  wire Clk_out, ew_lsb_high_2_1_a2, ew_lsb_high_2_1_b_2, ew_lsb_high_2_1_c_2, ew_lsb_high_2_1_d_2,
       ew_lsb_high_2_1_e_2, ew_lsb_high_2_1_f_2, ew_lsb_high_2_1_g, ewmsb_moderate_2_1_a2,
       ewmsb_moderate_2_1_b_2, ewmsb_moderate_2_1_c_2, ewmsb_moderate_2_1_d_2, ewmsb_moderate_2_1_e_2,
       ewmsb_moderate_2_1_f_2, ewmsb_moderate_2_1_g, lsb_moderate_2_1_a_2, lsb_moderate_2_1_b_2,
       lsb_moderate_2_1_c_2, lsb_moderate_2_1_d_2, lsb_moderate_2_1_e_2, lsb_moderate_2_1_f_2,
       lsb_moderate_2_1_g, ns_msb_moderate_2_1_a2, ns_msb_moderate_2_1_b_2, ns_msb_moderate_2_1_c_2,
       ns_msb_moderate_2_1_d_2, ns_msb_moderate_2_1_e_2, ns_msb_moderate_2_1_f_2, ns_msb_moderate_2_1_g;
  wire [5:0] counter_1_q;

  Clock Clk (.out(Clk_out));
  Counter #(.width(6), .max('h24)) counter_1 (
    .load(Enable), .count(Counter), .Q(counter_1_q), .clk(Clk_out), .clr(Reset));  // open: D, carry
  EW_LSB_HIGH_2 ew_lsb_high_2_1 (
    .A(counter_1_q[5]), .B(counter_1_q[4]), .C(counter_1_q[3]), .D(counter_1_q[2]), .E(counter_1_q[1]),
    .F(counter_1_q[0]), .A2(ew_lsb_high_2_1_a2), .b_2(ew_lsb_high_2_1_b_2), .c_2(ew_lsb_high_2_1_c_2),
    .d_2(ew_lsb_high_2_1_d_2), .e_2(ew_lsb_high_2_1_e_2), .f_2(ew_lsb_high_2_1_f_2), .g(ew_lsb_high_2_1_g));
  ewmSB_MODERATE_2 ewmsb_moderate_2_1 (
    .A(counter_1_q[5]), .B(counter_1_q[4]), .C(counter_1_q[3]), .D(counter_1_q[2]), .E(counter_1_q[1]),
    .F(counter_1_q[0]), .A2(ewmsb_moderate_2_1_a2), .b_2(ewmsb_moderate_2_1_b_2),
    .c_2(ewmsb_moderate_2_1_c_2), .d_2(ewmsb_moderate_2_1_d_2), .e_2(ewmsb_moderate_2_1_e_2),
    .f_2(ewmsb_moderate_2_1_f_2), .g(ewmsb_moderate_2_1_g));
  ewlight_MODERATE_2 ewlight_moderate_2_1 (
    .A(counter_1_q[5]), .B(counter_1_q[4]), .C(counter_1_q[3]), .D(counter_1_q[2]), .E(counter_1_q[1]),
    .F(counter_1_q[0]), .b_2(N1), .c_2(N0));
  lightlsb_MODERATE_2 lightlsb_moderate_2_1 (
    .A(counter_1_q[5]), .B(counter_1_q[4]), .C(counter_1_q[3]), .D(counter_1_q[2]), .E(counter_1_q[1]),
    .F(counter_1_q[0]), .b_2(E1), .c_2(E0));
  LSB_MODERATE_2 lsb_moderate_2_1 (
    .A(counter_1_q[5]), .B(counter_1_q[4]), .C(counter_1_q[3]), .D(counter_1_q[2]), .E(counter_1_q[1]),
    .F(counter_1_q[0]), .A_2(lsb_moderate_2_1_a_2), .b_2(lsb_moderate_2_1_b_2), .c_2(lsb_moderate_2_1_c_2),
    .d_2(lsb_moderate_2_1_d_2), .e_2(lsb_moderate_2_1_e_2), .f_2(lsb_moderate_2_1_f_2), .g(lsb_moderate_2_1_g));
  ns_MSB_MODERATE_2 ns_msb_moderate_2_1 (
    .A(counter_1_q[5]), .B(counter_1_q[4]), .C(counter_1_q[3]), .D(counter_1_q[2]), .E(counter_1_q[1]),
    .F(counter_1_q[0]), .A2(ns_msb_moderate_2_1_a2), .b_2(ns_msb_moderate_2_1_b_2),
    .c_2(ns_msb_moderate_2_1_c_2), .d_2(ns_msb_moderate_2_1_d_2), .e_2(ns_msb_moderate_2_1_e_2),
    .f_2(ns_msb_moderate_2_1_f_2), .g(ns_msb_moderate_2_1_g));
  _7_Segment_Display u_7_segment_display_1 (
    .g(ewmsb_moderate_2_1_g), .f(ewmsb_moderate_2_1_f_2), .a(ewmsb_moderate_2_1_a2),
    .b(ewmsb_moderate_2_1_b_2), .e(ewmsb_moderate_2_1_e_2), .d(ewmsb_moderate_2_1_d_2),
    .c(ewmsb_moderate_2_1_c_2));  // open: dp
  _7_Segment_Display u_7_segment_display_2 (
    .g(ew_lsb_high_2_1_g), .f(ew_lsb_high_2_1_f_2), .a(ew_lsb_high_2_1_a2), .b(ew_lsb_high_2_1_b_2),
    .e(ew_lsb_high_2_1_e_2), .d(ew_lsb_high_2_1_d_2), .c(ew_lsb_high_2_1_c_2));  // open: dp
  _7_Segment_Display u_7_segment_display_3 (
    .g(ns_msb_moderate_2_1_g), .f(ns_msb_moderate_2_1_f_2), .a(ns_msb_moderate_2_1_a2),
    .b(ns_msb_moderate_2_1_b_2), .e(ns_msb_moderate_2_1_e_2), .d(ns_msb_moderate_2_1_d_2),
    .c(ns_msb_moderate_2_1_c_2));  // open: dp
  _7_Segment_Display u_7_segment_display_4 (
    .g(lsb_moderate_2_1_g), .f(lsb_moderate_2_1_f_2), .a(lsb_moderate_2_1_a_2), .b(lsb_moderate_2_1_b_2),
    .e(lsb_moderate_2_1_e_2), .d(lsb_moderate_2_1_d_2), .c(lsb_moderate_2_1_c_2));  // open: dp

  assign S0 = N0;
  assign S1 = N1;
  assign W0 = E0;
  assign W1 = E1;

  // Notes on the sheet:
  //   mod and high
  //   NORTH
  //   WEST
  //   SOUTH
  //   EAST
endmodule

// H-L
module high_low (
  input  Enable,
  input  Counter,
  input  Reset,
  output N1,
  output N0,
  output W1,
  output W0,
  output E1,
  output E0,
  output S1,
  output S0
);

  wire Clk_out, ns_lsb_high1_1_a_2, ns_lsb_high1_1_b_2, ns_lsb_high1_1_c_2, ns_lsb_high1_1_d_2,
       ns_lsb_high1_1_e_2, ns_lsb_high1_1_f, ns_lsb_high1_1_g, ns_lsb_low_1_1_a_2, ns_lsb_low_1_1_b_2,
       ns_lsb_low_1_1_c_2, ns_lsb_low_1_1_d_2, ns_lsb_low_1_1_e_2, ns_lsb_low_1_1_f, ns_lsb_low_1_1_g,
       ns_msb_high_1_1_a_2, ns_msb_high_1_1_b_2, ns_msb_high_1_1_c_2, ns_msb_high_1_1_d_2,
       ns_msb_high_1_1_e_2, ns_msb_high_1_1_f, ns_msb_high_1_1_g, ns_msb_low_1_1_a_2, ns_msb_low_1_1_b_2,
       ns_msb_low_1_1_c_2, ns_msb_low_1_1_d_2, ns_msb_low_1_1_e_2, ns_msb_low_1_1_f, ns_msb_low_1_1_g;
  wire [4:0] counter_1_q;

  Clock Clk (.out(Clk_out));
  Counter #(.width(5), .max('h1e)) counter_1 (
    .load(Enable), .count(Counter), .Q(counter_1_q), .clk(Clk_out), .clr(Reset));  // open: D, carry
  NS_light_high ns_light_high_1 (
    .A(counter_1_q[4]), .B(counter_1_q[3]), .C(counter_1_q[2]), .D(counter_1_q[1]), .E(counter_1_q[0]),
    .a_2(N1), .b_2(N0));
  NS_light_low ns_light_low_1 (
    .A(counter_1_q[4]), .B(counter_1_q[3]), .C(counter_1_q[2]), .D(counter_1_q[1]), .E(counter_1_q[0]),
    .a_2(E1), .b_2(E0));
  NS_lsb_low_1 ns_lsb_low_1_1 (
    .A(counter_1_q[4]), .B(counter_1_q[3]), .C(counter_1_q[2]), .D(counter_1_q[1]), .E(counter_1_q[0]),
    .a_2(ns_lsb_low_1_1_a_2), .b_2(ns_lsb_low_1_1_b_2), .c_2(ns_lsb_low_1_1_c_2), .d_2(ns_lsb_low_1_1_d_2),
    .e_2(ns_lsb_low_1_1_e_2), .f(ns_lsb_low_1_1_f), .g(ns_lsb_low_1_1_g));
  NS_msb_low_1 ns_msb_low_1_1 (
    .A(counter_1_q[4]), .B(counter_1_q[3]), .C(counter_1_q[2]), .D(counter_1_q[1]), .E(counter_1_q[0]),
    .a_2(ns_msb_low_1_1_a_2), .b_2(ns_msb_low_1_1_b_2), .c_2(ns_msb_low_1_1_c_2), .d_2(ns_msb_low_1_1_d_2),
    .e_2(ns_msb_low_1_1_e_2), .f(ns_msb_low_1_1_f), .g(ns_msb_low_1_1_g));
  NS_lsb_high1 ns_lsb_high1_1 (
    .A(counter_1_q[4]), .B(counter_1_q[3]), .C(counter_1_q[2]), .D(counter_1_q[1]), .E(counter_1_q[0]),
    .a_2(ns_lsb_high1_1_a_2), .b_2(ns_lsb_high1_1_b_2), .c_2(ns_lsb_high1_1_c_2), .d_2(ns_lsb_high1_1_d_2),
    .e_2(ns_lsb_high1_1_e_2), .f(ns_lsb_high1_1_f), .g(ns_lsb_high1_1_g));
  NS_msb_high_1 ns_msb_high_1_1 (
    .A(counter_1_q[4]), .B(counter_1_q[3]), .C(counter_1_q[2]), .D(counter_1_q[1]), .E(counter_1_q[0]),
    .a_2(ns_msb_high_1_1_a_2), .b_2(ns_msb_high_1_1_b_2), .c_2(ns_msb_high_1_1_c_2),
    .d_2(ns_msb_high_1_1_d_2), .e_2(ns_msb_high_1_1_e_2), .f(ns_msb_high_1_1_f), .g(ns_msb_high_1_1_g));
  _7_Segment_Display u_7_segment_display_1 (
    .g(ns_msb_low_1_1_g), .f(ns_msb_low_1_1_f), .a(ns_msb_low_1_1_a_2), .b(ns_msb_low_1_1_b_2),
    .e(ns_msb_low_1_1_e_2), .d(ns_msb_low_1_1_d_2), .c(ns_msb_low_1_1_c_2));  // open: dp
  _7_Segment_Display u_7_segment_display_2 (
    .g(ns_lsb_low_1_1_g), .f(ns_lsb_low_1_1_f), .a(ns_lsb_low_1_1_a_2), .b(ns_lsb_low_1_1_b_2),
    .e(ns_lsb_low_1_1_e_2), .d(ns_lsb_low_1_1_d_2), .c(ns_lsb_low_1_1_c_2));  // open: dp
  _7_Segment_Display u_7_segment_display_3 (
    .g(ns_msb_high_1_1_g), .f(ns_msb_high_1_1_f), .a(ns_msb_high_1_1_a_2), .b(ns_msb_high_1_1_b_2),
    .e(ns_msb_high_1_1_e_2), .d(ns_msb_high_1_1_d_2), .c(ns_msb_high_1_1_c_2));  // open: dp
  _7_Segment_Display u_7_segment_display_4 (
    .g(ns_lsb_high1_1_g), .f(ns_lsb_high1_1_f), .a(ns_lsb_high1_1_a_2), .b(ns_lsb_high1_1_b_2),
    .e(ns_lsb_high1_1_e_2), .d(ns_lsb_high1_1_d_2), .c(ns_lsb_high1_1_c_2));  // open: dp

  assign S0 = N0;
  assign S1 = N1;
  assign W0 = E0;
  assign W1 = E1;

  // Notes on the sheet:
  //   WEST
  //   NORTH
  //   SOUTH
  //   EAST
endmodule

// H-M
module high_mod (
  input  Enable,
  input  Counter,
  input  Reset,
  output N1,
  output N0,
  output WEST,
  output W0,
  output E1,
  output E0,
  output S1,
  output S0
);

  wire Clk_out, ew_lsb_high_2_1_a2, ew_lsb_high_2_1_b_2, ew_lsb_high_2_1_c_2, ew_lsb_high_2_1_d_2,
       ew_lsb_high_2_1_e_2, ew_lsb_high_2_1_f_2, ew_lsb_high_2_1_g, ewmsb_moderate_2_1_a2,
       ewmsb_moderate_2_1_b_2, ewmsb_moderate_2_1_c_2, ewmsb_moderate_2_1_d_2, ewmsb_moderate_2_1_e_2,
       ewmsb_moderate_2_1_f_2, ewmsb_moderate_2_1_g, lsb_moderate_2_1_a_2, lsb_moderate_2_1_b_2,
       lsb_moderate_2_1_c_2, lsb_moderate_2_1_d_2, lsb_moderate_2_1_e_2, lsb_moderate_2_1_f_2,
       lsb_moderate_2_1_g, ns_msb_moderate_2_1_a2, ns_msb_moderate_2_1_b_2, ns_msb_moderate_2_1_c_2,
       ns_msb_moderate_2_1_d_2, ns_msb_moderate_2_1_e_2, ns_msb_moderate_2_1_f_2, ns_msb_moderate_2_1_g;
  wire [5:0] counter_1_q;

  Clock Clk (.out(Clk_out));
  Counter #(.width(6), .max('h24)) counter_1 (
    .load(Enable), .count(Counter), .Q(counter_1_q), .clk(Clk_out), .clr(Reset));  // open: D, carry
  LSB_MODERATE_2 lsb_moderate_2_1 (
    .A(counter_1_q[5]), .B(counter_1_q[4]), .C(counter_1_q[3]), .D(counter_1_q[2]), .E(counter_1_q[1]),
    .F(counter_1_q[0]), .A_2(lsb_moderate_2_1_a_2), .b_2(lsb_moderate_2_1_b_2), .c_2(lsb_moderate_2_1_c_2),
    .d_2(lsb_moderate_2_1_d_2), .e_2(lsb_moderate_2_1_e_2), .f_2(lsb_moderate_2_1_f_2), .g(lsb_moderate_2_1_g));
  ns_MSB_MODERATE_2 ns_msb_moderate_2_1 (
    .A(counter_1_q[5]), .B(counter_1_q[4]), .C(counter_1_q[3]), .D(counter_1_q[2]), .E(counter_1_q[1]),
    .F(counter_1_q[0]), .A2(ns_msb_moderate_2_1_a2), .b_2(ns_msb_moderate_2_1_b_2),
    .c_2(ns_msb_moderate_2_1_c_2), .d_2(ns_msb_moderate_2_1_d_2), .e_2(ns_msb_moderate_2_1_e_2),
    .f_2(ns_msb_moderate_2_1_f_2), .g(ns_msb_moderate_2_1_g));
  lightlsb_MODERATE_2 lightlsb_moderate_2_1 (
    .A(counter_1_q[5]), .B(counter_1_q[4]), .C(counter_1_q[3]), .D(counter_1_q[2]), .E(counter_1_q[1]),
    .F(counter_1_q[0]), .b_2(N1), .c_2(N0));
  ewlight_MODERATE_2 ewlight_moderate_2_1 (
    .A(counter_1_q[5]), .B(counter_1_q[4]), .C(counter_1_q[3]), .D(counter_1_q[2]), .E(counter_1_q[1]),
    .F(counter_1_q[0]), .b_2(E1), .c_2(E0));
  EW_LSB_HIGH_2 ew_lsb_high_2_1 (
    .A(counter_1_q[5]), .B(counter_1_q[4]), .C(counter_1_q[3]), .D(counter_1_q[2]), .E(counter_1_q[1]),
    .F(counter_1_q[0]), .A2(ew_lsb_high_2_1_a2), .b_2(ew_lsb_high_2_1_b_2), .c_2(ew_lsb_high_2_1_c_2),
    .d_2(ew_lsb_high_2_1_d_2), .e_2(ew_lsb_high_2_1_e_2), .f_2(ew_lsb_high_2_1_f_2), .g(ew_lsb_high_2_1_g));
  ewmSB_MODERATE_2 ewmsb_moderate_2_1 (
    .A(counter_1_q[5]), .B(counter_1_q[4]), .C(counter_1_q[3]), .D(counter_1_q[2]), .E(counter_1_q[1]),
    .F(counter_1_q[0]), .A2(ewmsb_moderate_2_1_a2), .b_2(ewmsb_moderate_2_1_b_2),
    .c_2(ewmsb_moderate_2_1_c_2), .d_2(ewmsb_moderate_2_1_d_2), .e_2(ewmsb_moderate_2_1_e_2),
    .f_2(ewmsb_moderate_2_1_f_2), .g(ewmsb_moderate_2_1_g));
  _7_Segment_Display u_7_segment_display_1 (
    .g(ns_msb_moderate_2_1_g), .f(ns_msb_moderate_2_1_f_2), .a(ns_msb_moderate_2_1_a2),
    .b(ns_msb_moderate_2_1_b_2), .e(ns_msb_moderate_2_1_e_2), .d(ns_msb_moderate_2_1_d_2),
    .c(ns_msb_moderate_2_1_c_2));  // open: dp
  _7_Segment_Display u_7_segment_display_2 (
    .g(lsb_moderate_2_1_g), .f(lsb_moderate_2_1_f_2), .a(lsb_moderate_2_1_a_2), .b(lsb_moderate_2_1_b_2),
    .e(lsb_moderate_2_1_e_2), .d(lsb_moderate_2_1_d_2), .c(lsb_moderate_2_1_c_2));  // open: dp
  _7_Segment_Display u_7_segment_display_3 (
    .g(ewmsb_moderate_2_1_g), .f(ewmsb_moderate_2_1_f_2), .a(ewmsb_moderate_2_1_a2),
    .b(ewmsb_moderate_2_1_b_2), .e(ewmsb_moderate_2_1_e_2), .d(ewmsb_moderate_2_1_d_2),
    .c(ewmsb_moderate_2_1_c_2));  // open: dp
  _7_Segment_Display u_7_segment_display_4 (
    .g(ew_lsb_high_2_1_g), .f(ew_lsb_high_2_1_f_2), .a(ew_lsb_high_2_1_a2), .b(ew_lsb_high_2_1_b_2),
    .e(ew_lsb_high_2_1_e_2), .d(ew_lsb_high_2_1_d_2), .c(ew_lsb_high_2_1_c_2));  // open: dp

  assign S0 = N0;
  assign S1 = N1;
  assign W0 = E0;
  assign WEST = E1;

  // Notes on the sheet:
  //   high and moderate
  //   NORTH
  //   SOUTH
  //   EAST
endmodule

// TRAFF.SELECT
module traffic_selector (
  input  A,
  input  B,
  input  C,
  input  D,
  output A2,
  output B2,
  output C2,
  output D2,
  output E,
  output F,
  output G,
  output H,
  output I
);

  wire and_1_out, and_2_out, and_3_out, not_1_out, not_2_out, not_3_out, not_4_out, not_5_out, not_6_out,
       not_7_out, not_8_out, not_9_out, not_10_out, not_11_out, not_12_out, not_13_out, not_14_out,
       not_15_out, not_16_out, not_17_out, not_18_out, not_19_out, not_20_out, not_21_out, not_22_out;

  not not_1 (not_1_out, A);
  not not_2 (not_2_out, B);
  not not_3 (not_3_out, C);
  not not_4 (not_4_out, D);
  not not_5 (not_5_out, A);
  not not_6 (not_6_out, B);
  not not_7 (not_7_out, C);
  not not_8 (not_8_out, A);
  not not_9 (not_9_out, B);
  not not_10 (not_10_out, D);
  not not_11 (not_11_out, A);
  not not_12 (not_12_out, C);
  not not_13 (not_13_out, D);
  and and_1 (and_1_out, C, D);
  and and_2 (and_2_out, B, D);
  and and_3 (and_3_out, A, B);
  not not_14 (not_14_out, A);
  not not_15 (not_15_out, D);
  not not_16 (not_16_out, B);
  not not_17 (not_17_out, C);
  not not_18 (not_18_out, D);
  not not_19 (not_19_out, B);
  not not_20 (not_20_out, C);
  not not_21 (not_21_out, B);
  not not_22 (not_22_out, D);
  and and_4 (A2, not_1_out, not_2_out, not_3_out, not_4_out);
  and and_5 (B2, not_5_out, not_6_out, not_7_out, D);
  and and_6 (C2, not_8_out, not_9_out, C, not_10_out);
  and and_7 (D2, not_11_out, B, not_12_out, not_13_out);
  or or_1 (E, and_1_out, and_2_out, and_3_out);
  and and_8 (F, not_14_out, B, C, not_15_out);
  and and_9 (G, A, not_16_out, not_17_out, not_18_out);
  and and_10 (H, A, not_19_out, not_20_out, D);
  and and_11 (I, A, not_21_out, C, not_22_out);
endmodule

// R
module red (
  input  l1,
  input  l2,
  output o
);

  wire not_1_out, not_2_out;

  not not_1 (not_1_out, l1);
  not not_2 (not_2_out, l2);
  and and_1 (o, not_1_out, not_2_out);
endmodule

// Y
module yellow (
  input  l1,
  input  l2,
  output o
);

  wire not_1_out;

  not not_1 (not_1_out, l1);
  and and_1 (o, not_1_out, l2);
endmodule

// G
module green (
  input  l1,
  input  l2,
  output o
);

  wire not_1_out;

  not not_1 (not_1_out, l2);
  and and_1 (o, l1, not_1_out);
endmodule
