// Logisim project TraCCS-L,M,H.circ as structural Verilog: 24 circuits, main circuit main
module main (
  input  Enable,
  input  Up_Down,
  input  Reset,
  input  Enable_2,
  input  Up_Down_2,
  input  Reset_2,
  input  Enable_3,
  input  Counter,
  input  Reset_3,
  output NORTH,
  output out_11,
  output WEST,
  output out_13,
  output EAST,
  output out_15,
  output SOUTH,
  output out_17,
  output NORTH_2,
  output out_19,
  output WEST_2,
  output out_21,
  output EAST_2,
  output out_23,
  output SOUTH_2,
  output out_25,
  output NORTH_3,
  output out_27,
  output WEST_3,
  output out_29,
  output EAST_3,
  output out_31,
  output SOUTH_3,
  output out_33
);

  wire Clk_2_out, Clk_3_out, Clk_out, ew_low_1_a_2, ew_low_1_b_2, ew_low_1_c_2, ew_low_1_d_2, ew_low_1_e,
       ew_low_1_f, ew_low_1_g, ew_lsb_high_1_a_2, ew_lsb_high_1_b_2, ew_lsb_high_1_c_2, ew_lsb_high_1_d_2,
       ew_lsb_high_1_e_2, ew_lsb_high_1_f_2, ew_lsb_high_1_g, ew_lsb_moderate_1_a_2, ew_lsb_moderate_1_b_2,
       ew_lsb_moderate_1_c_2, ew_lsb_moderate_1_d_2, ew_lsb_moderate_1_e_2, ew_lsb_moderate_1_f,
       ew_lsb_moderate_1_g, ew_msb_high_1_a_2, ew_msb_high_1_b_2, ew_msb_high_1_c_2, ew_msb_high_1_d_2,
       ew_msb_high_1_e_2, ew_msb_high_1_f_2, ew_msb_high_1_g, ew_msb_moderate_1_a_2, ew_msb_moderate_1_b_2,
       ew_msb_moderate_1_c_2, ew_msb_moderate_1_d_2, ew_msb_moderate_1_e_2, ew_msb_moderate_1_f,
       ew_msb_moderate_1_g, ns_low_1_a_2, ns_low_1_b_2, ns_low_1_c_2, ns_low_1_d_2, ns_low_1_e, ns_low_1_f,
       ns_low_1_g, ns_lsb_high_1_a_2, ns_lsb_high_1_b_2, ns_lsb_high_1_c_2, ns_lsb_high_1_d_2,
       ns_lsb_high_1_e_2, ns_lsb_high_1_f_2, ns_lsb_high_1_g, ns_lsb_moderate_1_a_2, ns_lsb_moderate_1_b_2,
       ns_lsb_moderate_1_c_2, ns_lsb_moderate_1_d_2, ns_lsb_moderate_1_e_2, ns_lsb_moderate_1_f,
       ns_lsb_moderate_1_g, ns_msb_high_1_a_2, ns_msb_high_1_b_2, ns_msb_high_1_c_2, ns_msb_high_1_d_2,
       ns_msb_high_1_e_2, ns_msb_high_1_f_2, ns_msb_high_1_g, ns_msb_moderate_1_a_2, ns_msb_moderate_1_b_2,
       ns_msb_moderate_1_c_2, ns_msb_moderate_1_d_2, ns_msb_moderate_1_e_2, ns_msb_moderate_1_f,
       ns_msb_moderate_1_g;
  wire [3:0] counter_1_q;
  wire [4:0] counter_2_q;
  wire [5:0] counter_3_q;

  Clock Clk (.out(Clk_out));
  Clock Clk_2 (.out(Clk_2_out));
  Clock Clk_3 (.out(Clk_3_out));
  Counter #(.width(4), .max('hf)) counter_1 (
    .load(Enable), .count(Up_Down), .Q(counter_1_q), .clk(Clk_out), .clr(Reset));  // open: D, carry
  Counter #(.width(5), .max('h1d)) counter_2 (
    .load(Enable_2), .count(Up_Down_2), .Q(counter_2_q), .clk(Clk_2_out), .clr(Reset_2));  // open: D, carry
  Counter #(.width(6), .max('h2b)) counter_3 (
    .load(Enable_3), .count(Counter), .Q(counter_3_q), .clk(Clk_3_out), .clr(Reset_3));  // open: D, carry
  NS_light_low ns_light_low_1 (
    .A(counter_1_q[3]), .B(counter_1_q[2]), .C(counter_1_q[1]), .D(counter_1_q[0]), .a_2(NORTH), .b_2(out_11));
  EW_Light_low ew_light_low_1 (
    .A(counter_1_q[3]), .B(counter_1_q[2]), .C(counter_1_q[1]), .D(counter_1_q[0]), .a_2(EAST), .b_2(out_13));
  NS_light_moderate ns_light_moderate_1 (
    .A(counter_2_q[4]), .B(counter_2_q[3]), .C(counter_2_q[2]), .D(counter_2_q[1]), .E(counter_2_q[0]),
    .a_2(NORTH_2), .b_2(out_19));
  EW_Light_moderate ew_light_moderate_1 (
    .A(counter_2_q[4]), .B(counter_2_q[3]), .C(counter_2_q[2]), .D(counter_2_q[1]), .E(counter_2_q[0]),
    .a_2(EAST_2), .b_2(out_21));
  EW_lsb_moderate ew_lsb_moderate_1 (
    .A(counter_2_q[4]), .B(counter_2_q[3]), .C(counter_2_q[2]), .D(counter_2_q[1]), .E(counter_2_q[0]),
    .a_2(ew_lsb_moderate_1_a_2), .b_2(ew_lsb_moderate_1_b_2), .c_2(ew_lsb_moderate_1_c_2),
    .d_2(ew_lsb_moderate_1_d_2), .e_2(ew_lsb_moderate_1_e_2), .f(ew_lsb_moderate_1_f), .g(ew_lsb_moderate_1_g));
  EW_msb_moderate ew_msb_moderate_1 (
    .A(counter_2_q[4]), .B(counter_2_q[3]), .C(counter_2_q[2]), .D(counter_2_q[1]), .E(counter_2_q[0]),
    .a_2(ew_msb_moderate_1_a_2), .b_2(ew_msb_moderate_1_b_2), .c_2(ew_msb_moderate_1_c_2),
    .d_2(ew_msb_moderate_1_d_2), .e_2(ew_msb_moderate_1_e_2), .f(ew_msb_moderate_1_f), .g(ew_msb_moderate_1_g));
  NS_low ns_low_1 (
    .A(counter_1_q[3]), .B(counter_1_q[2]), .C(counter_1_q[1]), .D(counter_1_q[0]), .a_2(ns_low_1_a_2),
    .b_2(ns_low_1_b_2), .c_2(ns_low_1_c_2), .d_2(ns_low_1_d_2), .e(ns_low_1_e), .f(ns_low_1_f), .g(ns_low_1_g));
  EW_low ew_low_1 (
    .A(counter_1_q[3]), .B(counter_1_q[2]), .C(counter_1_q[1]), .D(counter_1_q[0]), .a_2(ew_low_1_a_2),
    .b_2(ew_low_1_b_2), .c_2(ew_low_1_c_2), .d_2(ew_low_1_d_2), .e(ew_low_1_e), .f(ew_low_1_f), .g(ew_low_1_g));
  NS_lsb_moderate ns_lsb_moderate_1 (
    .A(counter_2_q[4]), .B(counter_2_q[3]), .C(counter_2_q[2]), .D(counter_2_q[1]), .E(counter_2_q[0]),
    .a_2(ns_lsb_moderate_1_a_2), .b_2(ns_lsb_moderate_1_b_2), .c_2(ns_lsb_moderate_1_c_2),
    .d_2(ns_lsb_moderate_1_d_2), .e_2(ns_lsb_moderate_1_e_2), .f(ns_lsb_moderate_1_f), .g(ns_lsb_moderate_1_g));
  NS_msb_moderate ns_msb_moderate_1 (
    .A(counter_2_q[4]), .B(counter_2_q[3]), .C(counter_2_q[2]), .D(counter_2_q[1]), .E(counter_2_q[0]),
    .a_2(ns_msb_moderate_1_a_2), .b_2(ns_msb_moderate_1_b_2), .c_2(ns_msb_moderate_1_c_2),
    .d_2(ns_msb_moderate_1_d_2), .e_2(ns_msb_moderate_1_e_2), .f(ns_msb_moderate_1_f), .g(ns_msb_moderate_1_g));
  NS_lsb_high ns_lsb_high_1 (
    .A(counter_3_q[5]), .B(counter_3_q[4]), .C(counter_3_q[3]), .D(counter_3_q[2]), .E(counter_3_q[1]),
    .F(counter_3_q[0]), .a_2(ns_lsb_high_1_a_2), .b_2(ns_lsb_high_1_b_2), .c_2(ns_lsb_high_1_c_2),
    .d_2(ns_lsb_high_1_d_2), .e_2(ns_lsb_high_1_e_2), .f_2(ns_lsb_high_1_f_2), .g(ns_lsb_high_1_g));
  NS_msb_high ns_msb_high_1 (
    .A(counter_3_q[5]), .B(counter_3_q[4]), .C(counter_3_q[3]), .D(counter_3_q[2]), .E(counter_3_q[1]),
    .F(counter_3_q[0]), .a_2(ns_msb_high_1_a_2), .b_2(ns_msb_high_1_b_2), .c_2(ns_msb_high_1_c_2),
    .d_2(ns_msb_high_1_d_2), .e_2(ns_msb_high_1_e_2), .f_2(ns_msb_high_1_f_2), .g(ns_msb_high_1_g));
  NS_light_high ns_light_high_1 (
    .A(counter_3_q[5]), .B(counter_3_q[4]), .C(counter_3_q[3]), .D(counter_3_q[2]), .E(counter_3_q[1]),
    .F(counter_3_q[0]), .a_2(NORTH_3), .b_2(out_27));
  EW_Light_high ew_light_high_1 (
    .A(counter_3_q[5]), .B(counter_3_q[4]), .C(counter_3_q[3]), .D(counter_3_q[2]), .E(counter_3_q[1]),
    .F(counter_3_q[0]), .a_2(EAST_3), .b_2(out_29));
  EW_lsb_high ew_lsb_high_1 (
    .A(counter_3_q[5]), .B(counter_3_q[4]), .C(counter_3_q[3]), .D(counter_3_q[2]), .E(counter_3_q[1]),
    .F(counter_3_q[0]), .a_2(ew_lsb_high_1_a_2), .b_2(ew_lsb_high_1_b_2), .c_2(ew_lsb_high_1_c_2),
    .d_2(ew_lsb_high_1_d_2), .e_2(ew_lsb_high_1_e_2), .f_2(ew_lsb_high_1_f_2), .g(ew_lsb_high_1_g));
  EW_msb_high ew_msb_high_1 (
    .A(counter_3_q[5]), .B(counter_3_q[4]), .C(counter_3_q[3]), .D(counter_3_q[2]), .E(counter_3_q[1]),
    .F(counter_3_q[0]), .a_2(ew_msb_high_1_a_2), .b_2(ew_msb_high_1_b_2), .c_2(ew_msb_high_1_c_2),
    .d_2(ew_msb_high_1_d_2), .e_2(ew_msb_high_1_e_2), .f_2(ew_msb_high_1_f_2), .g(ew_msb_high_1_g));
  _7_Segment_Display u_7_segment_display_1 (
    .g(ns_msb_moderate_1_g), .f(ns_msb_moderate_1_f), .a(ns_msb_moderate_1_a_2), .b(ns_msb_moderate_1_b_2),
    .e(ns_msb_moderate_1_e_2), .d(ns_msb_moderate_1_d_2), .c(ns_msb_moderate_1_c_2));  // open: dp
  _7_Segment_Display u_7_segment_display_2 (
    .g(ns_msb_high_1_g), .f(ns_msb_high_1_f_2), .a(ns_msb_high_1_a_2), .b(ns_msb_high_1_b_2),
    .e(ns_msb_high_1_e_2), .d(ns_msb_high_1_d_2), .c(ns_msb_high_1_c_2));  // open: dp
  _7_Segment_Display u_7_segment_display_3 (
    .g(ns_low_1_g), .f(ns_low_1_f), .a(ns_low_1_a_2), .b(ns_low_1_b_2), .e(ns_low_1_e), .d(ns_low_1_d_2),
    .c(ns_low_1_c_2));  // open: dp
  _7_Segment_Display u_7_segment_display_4 (
    .g(ns_lsb_moderate_1_g), .f(ns_lsb_moderate_1_f), .a(ns_lsb_moderate_1_a_2), .b(ns_lsb_moderate_1_b_2),
    .e(ns_lsb_moderate_1_e_2), .d(ns_lsb_moderate_1_d_2), .c(ns_lsb_moderate_1_c_2));  // open: dp
  _7_Segment_Display u_7_segment_display_5 (
    .g(ns_lsb_high_1_g), .f(ns_lsb_high_1_f_2), .a(ns_lsb_high_1_a_2), .b(ns_lsb_high_1_b_2),
    .e(ns_lsb_high_1_e_2), .d(ns_lsb_high_1_d_2), .c(ns_lsb_high_1_c_2));  // open: dp
  _7_Segment_Display u_7_segment_display_6 (
    .g(ew_low_1_g), .f(ew_low_1_f), .a(ew_low_1_a_2), .b(ew_low_1_b_2), .e(ew_low_1_e), .d(ew_low_1_d_2),
    .c(ew_low_1_c_2));  // open: dp
  _7_Segment_Display u_7_segment_display_7 (
    .g(ew_msb_moderate_1_g), .f(ew_msb_moderate_1_f), .a(ew_msb_moderate_1_a_2), .b(ew_msb_moderate_1_b_2),
    .e(ew_msb_moderate_1_e_2), .d(ew_msb_moderate_1_d_2), .c(ew_msb_moderate_1_c_2));  // open: dp
  _7_Segment_Display u_7_segment_display_8 (
    .g(ew_msb_high_1_g), .f(ew_msb_high_1_f_2), .a(ew_msb_high_1_a_2), .b(ew_msb_high_1_b_2),
    .e(ew_msb_high_1_e_2), .d(ew_msb_high_1_d_2), .c(ew_msb_high_1_c_2));  // open: dp
  _7_Segment_Display u_7_segment_display_9 (
    .g(ew_lsb_moderate_1_g), .f(ew_lsb_moderate_1_f), .a(ew_lsb_moderate_1_a_2), .b(ew_lsb_moderate_1_b_2),
    .e(ew_lsb_moderate_1_e_2), .d(ew_lsb_moderate_1_d_2), .c(ew_lsb_moderate_1_c_2));  // open: dp
  _7_Segment_Display u_7_segment_display_10 (
    .g(ew_lsb_high_1_g), .f(ew_lsb_high_1_f_2), .a(ew_lsb_high_1_a_2), .b(ew_lsb_high_1_b_2),
    .e(ew_lsb_high_1_e_2), .d(ew_lsb_high_1_d_2), .c(ew_lsb_high_1_c_2));  // open: dp

  assign out_15 = out_13;
  assign out_17 = out_11;
  assign out_23 = out_21;
  assign out_25 = out_19;
  assign out_31 = out_29;
  assign out_33 = out_27;
  assign SOUTH = NORTH;
  assign SOUTH_2 = NORTH_2;
  assign SOUTH_3 = NORTH_3;
  assign WEST = EAST;
  assign WEST_2 = EAST_2;
  assign WEST_3 = EAST_3;

  // Notes on the sheet:
  //   HIGH TRAFFIC
  //   LOW TRAFFIC
  //   MODERATE TRAFFIC
endmodule

module lsb (
  input  A,
  input  B,
  input  C,
  input  D,
  output a_2,
  output b_2,
  output c_2,
  output d_2,
  output e,
  output f,
  output g
);

  wire and_1_out, and_2_out, and_3_out, and_4_out, and_5_out, and_6_out, and_7_out, and_8_out, and_9_out,
       and_10_out, and_11_out, and_12_out, and_13_out, and_14_out, and_15_out, and_16_out, and_17_out,
       and_18_out, and_19_out, and_20_out, and_21_out, and_22_out, and_23_out, and_24_out, and_25_out,
       and_26_out, and_27_out, and_28_out, and_29_out, and_30_out, and_31_out, not_1_out, not_2_out,
       not_3_out, not_4_out, not_5_out, not_6_out, not_7_out, not_8_out, not_9_out, not_10_out, not_11_out,
       not_12_out, not_13_out, not_14_out, not_15_out, not_16_out, not_17_out, not_18_out, not_19_out,
       not_20_out, not_21_out, not_22_out, not_23_out, not_24_out, not_25_out, not_26_out, not_27_out,
       not_28_out, not_29_out, not_30_out, not_31_out, not_32_out, not_33_out, not_34_out, not_35_out,
       not_36_out, not_37_out, not_38_out, not_39_out, not_40_out, not_41_out, not_42_out, not_43_out,
       not_44_out;

  not not_1 (not_1_out, B);
  and and_1 (and_1_out, not_1_out, not_2_out);
  not not_2 (not_2_out, D);
  not not_3 (not_3_out, A);
  and and_2 (and_2_out, not_3_out, C);
  and and_3 (and_3_out, B, D);
  and and_4 (and_4_out, A, not_4_out);
  not not_4 (not_4_out, C);
  not not_5 (not_5_out, B);
  not not_6 (not_6_out, C);
  and and_5 (and_5_out, not_6_out, not_7_out);
  not not_7 (not_7_out, D);
  not not_8 (not_8_out, A);
  and and_6 (and_6_out, not_8_out, C, D);
  and and_7 (and_7_out, A, not_9_out);
  not not_9 (not_9_out, C);
  and and_8 (and_8_out, A, not_10_out);
  not not_10 (not_10_out, D);
  not not_11 (not_11_out, A);
  and and_9 (and_9_out, not_11_out, not_12_out);
  not not_12 (not_12_out, C);
  and and_10 (and_10_out, B, C);
  and and_11 (and_11_out, A, not_13_out);
  not not_13 (not_13_out, B);
  not not_14 (not_14_out, B);
  and and_12 (and_12_out, not_14_out, not_15_out);
  not not_15 (not_15_out, D);
  not not_16 (not_16_out, A);
  and and_13 (and_13_out, not_16_out, not_17_out, C);
  not not_17 (not_17_out, B);
  not not_18 (not_18_out, A);
  and and_14 (and_14_out, not_18_out, C, not_19_out);
  not not_19 (not_19_out, D);
  not not_20 (not_20_out, C);
  and and_15 (and_15_out, B, not_20_out, D);
  and and_16 (and_16_out, A, not_21_out, not_22_out);
  not not_21 (not_21_out, C);
  not not_22 (not_22_out, D);
  and and_17 (and_17_out, A, B, D);
  not not_23 (not_23_out, B);
  and and_18 (and_18_out, not_23_out, not_24_out);
  not not_24 (not_24_out, D);
  not not_25 (not_25_out, A);
  and and_19 (and_19_out, not_25_out, C, not_26_out);
  not not_26 (not_26_out, D);
  and and_20 (and_20_out, A, not_27_out, not_28_out);
  not not_27 (not_27_out, C);
  not not_28 (not_28_out, D);
  not not_29 (not_29_out, A);
  and and_21 (and_21_out, not_29_out, not_30_out, not_31_out);
  not not_30 (not_30_out, C);
  not not_31 (not_31_out, D);
  not not_32 (not_32_out, A);
  and and_22 (and_22_out, not_32_out, B, not_33_out);
  not not_33 (not_33_out, C);
  not not_34 (not_34_out, A);
  and and_23 (and_23_out, not_34_out, B, not_35_out);
  not not_35 (not_35_out, D);
  not not_36 (not_36_out, B);
  and and_24 (and_24_out, A, not_36_out, not_37_out);
  not not_37 (not_37_out, C);
  and and_25 (and_25_out, A, not_38_out, not_39_out);
  not not_38 (not_38_out, B);
  not not_39 (not_39_out, D);
  and and_26 (and_26_out, A, B, C);
  not not_40 (not_40_out, A);
  and and_27 (and_27_out, not_40_out, not_41_out, C);
  not not_41 (not_41_out, B);
  and and_28 (and_28_out, B, not_42_out);
  not not_42 (not_42_out, C);
  and and_29 (and_29_out, B, not_43_out);
  not not_43 (not_43_out, D);
  and and_30 (and_30_out, A, not_44_out);
  not not_44 (not_44_out, C);
  and and_31 (and_31_out, A, B);
  or or_1 (a_2, and_1_out, and_2_out, and_3_out, and_4_out);
  or or_2 (b_2, not_5_out, and_5_out, and_6_out, and_7_out, and_8_out);
  or or_3 (c_2, and_9_out, D, and_10_out, and_11_out);
  or or_4 (e, and_18_out, and_19_out, and_20_out);
  or or_5 (g, and_27_out, and_28_out, and_29_out, and_30_out, and_31_out);
  or or_6 (d_2, and_12_out, and_13_out, and_14_out, and_15_out, and_16_out, and_17_out);
  or or_7 (f, and_21_out, and_22_out, and_23_out, and_24_out, and_25_out, and_26_out);
endmodule

module msb (
  input  A,
  input  B,
  input  C,
  input  D,
  output a_2,
  output b_2,
  output c_2,
  output d_2,
  output e,
  output f,
  output g
);

  wire and_1_out, and_2_out, and_3_out, and_4_out, not_1_out, not_2_out, not_3_out, not_4_out, not_5_out,
       not_6_out, not_7_out, not_8_out, not_9_out, not_10_out, not_11_out, not_12_out;

  not not_1 (not_1_out, A);
  not not_2 (not_2_out, B);
  and and_1 (and_1_out, not_2_out, not_3_out);
  not not_3 (not_3_out, C);
  not not_4 (not_4_out, A);
  not not_5 (not_5_out, B);
  and and_2 (and_2_out, not_5_out, not_6_out);
  not not_6 (not_6_out, C);
  not not_7 (not_7_out, A);
  not not_8 (not_8_out, B);
  and and_3 (and_3_out, not_8_out, not_9_out);
  not not_9 (not_9_out, C);
  not not_10 (not_10_out, A);
  not not_11 (not_11_out, B);
  and and_4 (and_4_out, not_11_out, not_12_out);
  not not_12 (not_12_out, C);
  or or_1 (a_2, not_1_out, and_1_out);
  or or_2 (d_2, not_4_out, and_2_out);
  or or_3 (e, not_7_out, and_3_out);
  or or_4 (f, not_10_out, and_4_out);

  assign b_2 = 1'b1;
  assign c_2 = 1'b1;
  assign g = 1'b0;
endmodule

module NS_light_low (
  input  A,
  input  B,
  input  C,
  input  D,
  output a_2,
  output b_2
);

  wire and_1_out, and_2_out, and_3_out, not_1_out, not_2_out, not_3_out, not_4_out, not_5_out, not_6_out;

  not not_1 (not_1_out, A);
  and and_1 (and_1_out, not_1_out, D);
  not not_2 (not_2_out, A);
  and and_2 (and_2_out, not_2_out, C);
  not not_3 (not_3_out, A);
  and and_3 (and_3_out, not_3_out, B);
  not not_4 (not_4_out, B);
  and and_4 (b_2, not_4_out, not_5_out, not_6_out);
  not not_5 (not_5_out, C);
  not not_6 (not_6_out, D);
  or or_1 (a_2, and_1_out, and_2_out, and_3_out);
endmodule

module EW_Light_low (
  input  A,
  input  B,
  input  C,
  input  D,
  output a_2,
  output b_2
);

  wire and_1_out, and_2_out, and_3_out, not_1_out, not_2_out, not_3_out;

  and and_1 (and_1_out, A, D);
  and and_2 (and_2_out, A, C);
  and and_3 (and_3_out, A, B);
  not not_1 (not_1_out, B);
  not not_2 (not_2_out, C);
  and and_4 (b_2, not_1_out, not_2_out, not_3_out);
  not not_3 (not_3_out, D);
  or or_1 (a_2, and_1_out, and_2_out, and_3_out);
endmodule

module lsb_moderate (
  input  A,
  input  B,
  input  C,
  input  D,
  input  E,
  output a_2,
  output b_2,
  output c_2,
  output d_2,
  output e_2,
  output f,
  output g
);

  wire and_1_out, and_2_out, and_3_out, and_4_out, and_5_out, and_6_out, and_7_out, and_8_out, and_9_out,
       and_10_out, and_11_out, and_12_out, and_13_out, and_14_out, and_15_out, and_16_out, and_17_out,
       and_18_out, and_19_out, and_20_out, and_21_out, and_22_out, and_23_out, and_24_out, and_25_out,
       and_26_out, and_27_out, and_28_out, and_29_out, and_30_out, and_31_out, and_32_out, and_33_out,
       and_34_out, and_35_out, and_36_out, and_37_out, and_38_out, and_39_out, and_40_out, and_41_out,
       and_42_out, and_43_out, and_44_out, and_45_out, and_46_out, and_47_out, and_48_out, and_49_out,
       and_50_out, and_51_out, and_52_out, and_53_out, and_54_out, and_55_out, and_56_out, not_1_out,
       not_2_out, not_3_out, not_4_out, not_5_out, not_6_out, not_7_out, not_8_out, not_9_out, not_10_out,
       not_11_out, not_12_out, not_13_out, not_14_out, not_15_out, not_16_out, not_17_out, not_18_out,
       not_19_out, not_20_out, not_21_out, not_22_out, not_23_out, not_24_out, not_25_out, not_26_out,
       not_27_out, not_28_out, not_29_out, not_30_out, not_31_out, not_32_out, not_33_out, not_34_out,
       not_35_out, not_36_out, not_37_out, not_38_out, not_39_out, not_40_out, not_41_out, not_42_out,
       not_43_out, not_44_out, not_45_out, not_46_out, not_47_out, not_48_out, not_49_out, not_50_out,
       not_51_out, not_52_out, not_53_out, not_54_out, not_55_out, not_56_out, not_57_out, not_58_out,
       not_59_out, not_60_out, not_61_out, not_62_out, not_63_out, not_64_out, not_65_out, not_66_out,
       not_67_out, not_68_out, not_69_out, not_70_out, not_71_out, not_72_out, not_73_out, not_74_out,
       not_75_out, not_76_out, not_77_out, not_78_out, not_79_out, not_80_out, not_81_out, not_82_out,
       not_83_out, not_84_out, not_85_out, not_86_out, not_87_out, not_88_out, not_89_out, not_90_out,
       not_91_out, not_92_out, not_93_out, not_94_out, not_95_out, not_96_out, not_97_out, not_98_out,
       not_99_out, not_100_out, not_101_out;

  not not_1 (not_1_out, A);
  not not_2 (not_2_out, C);
  not not_3 (not_3_out, E);
  not not_4 (not_4_out, B);
  not not_5 (not_5_out, A);
  not not_6 (not_6_out, A);
  not not_7 (not_7_out, D);
  not not_8 (not_8_out, D);
  not not_9 (not_9_out, B);
  not not_10 (not_10_out, E);
  not not_11 (not_11_out, C);
  not not_12 (not_12_out, E);
  not not_13 (not_13_out, A);
  not not_14 (not_14_out, C);
  not not_15 (not_15_out, A);
  not not_16 (not_16_out, D);
  not not_17 (not_17_out, E);
  not not_18 (not_18_out, B);
  not not_19 (not_19_out, C);
  not not_20 (not_20_out, B);
  not not_21 (not_21_out, C);
  not not_22 (not_22_out, B);
  not not_23 (not_23_out, C);
  not not_24 (not_24_out, A);
  not not_25 (not_25_out, D);
  not not_26 (not_26_out, A);
  not not_27 (not_27_out, E);
  not not_28 (not_28_out, D);
  not not_29 (not_29_out, E);
  not not_30 (not_30_out, B);
  not not_31 (not_31_out, D);
  not not_32 (not_32_out, C);
  not not_33 (not_33_out, D);
  not not_34 (not_34_out, A);
  not not_35 (not_35_out, B);
  not not_36 (not_36_out, C);
  not not_37 (not_37_out, D);
  not not_38 (not_38_out, A);
  not not_39 (not_39_out, C);
  not not_40 (not_40_out, E);
  not not_41 (not_41_out, B);
  not not_42 (not_42_out, C);
  not not_43 (not_43_out, E);
  not not_44 (not_44_out, A);
  not not_45 (not_45_out, B);
  not not_46 (not_46_out, C);
  not not_47 (not_47_out, B);
  not not_48 (not_48_out, E);
  not not_49 (not_49_out, C);
  not not_50 (not_50_out, E);
  not not_51 (not_51_out, A);
  not not_52 (not_52_out, D);
  not not_53 (not_53_out, A);
  not not_54 (not_54_out, D);
  not not_55 (not_55_out, E);
  not not_56 (not_56_out, A);
  not not_57 (not_57_out, E);
  not not_58 (not_58_out, B);
  not not_59 (not_59_out, C);
  not not_60 (not_60_out, D);
  not not_61 (not_61_out, A);
  not not_62 (not_62_out, C);
  not not_63 (not_63_out, E);
  not not_64 (not_64_out, B);
  not not_65 (not_65_out, C);
  not not_66 (not_66_out, E);
  not not_67 (not_67_out, B);
  not not_68 (not_68_out, E);
  not not_69 (not_69_out, C);
  not not_70 (not_70_out, E);
  not not_71 (not_71_out, A);
  not not_72 (not_72_out, D);
  not not_73 (not_73_out, E);
  not not_74 (not_74_out, E);
  not not_75 (not_75_out, B);
  not not_76 (not_76_out, D);
  not not_77 (not_77_out, E);
  not not_78 (not_78_out, A);
  not not_79 (not_79_out, B);
  not not_80 (not_80_out, D);
  not not_81 (not_81_out, A);
  not not_82 (not_82_out, B);
  not not_83 (not_83_out, E);
  not not_84 (not_84_out, C);
  not not_85 (not_85_out, D);
  not not_86 (not_86_out, E);
  not not_87 (not_87_out, A);
  not not_88 (not_88_out, B);
  not not_89 (not_89_out, C);
  not not_90 (not_90_out, D);
  not not_91 (not_91_out, B);
  not not_92 (not_92_out, C);
  not not_93 (not_93_out, B);
  not not_94 (not_94_out, E);
  not not_95 (not_95_out, A);
  not not_96 (not_96_out, D);
  not not_97 (not_97_out, D);
  not not_98 (not_98_out, A);
  not not_99 (not_99_out, C);
  not not_100 (not_100_out, E);
  not not_101 (not_101_out, B);
  and and_1 (and_1_out, not_1_out, not_2_out, not_3_out);
  and and_2 (and_2_out, not_4_out, D);
  and and_3 (and_3_out, not_5_out, C, E);
  and and_4 (and_4_out, not_6_out, B, not_7_out);
  and and_5 (and_5_out, B, C, not_8_out);
  and and_6 (and_6_out, A, not_9_out, not_10_out);
  and and_7 (and_7_out, A, not_11_out, E);
  and and_8 (and_8_out, A, D, not_12_out);
  and and_9 (and_9_out, not_13_out, not_14_out);
  and and_10 (and_10_out, not_15_out, not_16_out, not_17_out);
  and and_11 (and_11_out, not_18_out, not_19_out, E);
  and and_12 (and_12_out, not_20_out, not_21_out, D);
  and and_13 (and_13_out, not_22_out, D, E);
  and and_14 (and_14_out, not_23_out, D, E);
  and and_15 (and_15_out, not_24_out, B, not_25_out);
  and and_16 (and_16_out, not_26_out, B, not_27_out);
  and and_17 (and_17_out, B, not_28_out, not_29_out);
  and and_18 (and_18_out, A, C);
  and and_19 (and_19_out, not_30_out, not_31_out);
  and and_20 (and_20_out, not_32_out, not_33_out);
  and and_21 (and_21_out, not_34_out, not_35_out, C);
  and and_22 (and_22_out, B, D);
  and and_23 (and_23_out, A, not_36_out);
  and and_24 (and_24_out, A, not_37_out);
  and and_25 (and_25_out, not_38_out, not_39_out, not_40_out);
  and and_26 (and_26_out, not_41_out, not_42_out, not_43_out);
  and and_27 (and_27_out, not_44_out, not_45_out, not_46_out, D);
  and and_28 (and_28_out, not_47_out, D, not_48_out);
  and and_29 (and_29_out, not_49_out, D, not_50_out);
  and and_30 (and_30_out, not_51_out, C, not_52_out, E);
  and and_31 (and_31_out, not_53_out, B, not_54_out, not_55_out);
  and and_32 (and_32_out, not_56_out, B, C, E);
  and and_33 (and_33_out, A, C, not_57_out);
  and and_34 (and_34_out, A, not_58_out, C, D);
  and and_35 (and_35_out, A, B, not_59_out, not_60_out, E);
  and and_36 (and_36_out, not_61_out, not_62_out, not_63_out);
  and and_37 (and_37_out, not_64_out, not_65_out, not_66_out);
  and and_38 (and_38_out, not_67_out, D, not_68_out);
  and and_39 (and_39_out, not_69_out, D, not_70_out);
  and and_40 (and_40_out, not_71_out, B, not_72_out, not_73_out);
  and and_41 (and_41_out, A, C, not_74_out);
  and and_42 (and_42_out, not_75_out, not_76_out, not_77_out);
  and and_43 (and_43_out, not_78_out, not_79_out, C, not_80_out);
  and and_44 (and_44_out, not_81_out, not_82_out, C, not_83_out);
  and and_45 (and_45_out, B, not_84_out, not_85_out);
  and and_46 (and_46_out, B, D, not_86_out);
  and and_47 (and_47_out, not_87_out, B, C, D);
  and and_48 (and_48_out, A, not_88_out, not_89_out, D);
  and and_49 (and_49_out, A, B, not_90_out);
  and and_50 (and_50_out, not_91_out, not_92_out, D);
  and and_51 (and_51_out, not_93_out, D, not_94_out);
  and and_52 (and_52_out, not_95_out, C, not_96_out);
  and and_53 (and_53_out, B, not_97_out);
  and and_54 (and_54_out, not_98_out, B, C);
  and and_55 (and_55_out, A, not_99_out, not_100_out);
  and and_56 (and_56_out, A, not_101_out, D);
  or or_1 (a_2, and_1_out, and_2_out, and_3_out, and_4_out, and_5_out, and_6_out, and_7_out, and_8_out);
  or or_2 (b_2, and_9_out, and_10_out, and_11_out, and_12_out, and_13_out, and_14_out, and_15_out, and_16_out, and_17_out, and_18_out);
  or or_3 (c_2, and_19_out, and_20_out, E, and_21_out, and_22_out, and_23_out, and_24_out);
  or or_4 (d_2, and_25_out, and_26_out, and_27_out, and_28_out, and_29_out, and_30_out, and_31_out, and_32_out, and_33_out, and_34_out, and_35_out);
  or or_5 (e_2, and_36_out, and_37_out, and_38_out, and_39_out, and_40_out, and_41_out);
  or or_6 (f, and_42_out, and_43_out, and_44_out, and_45_out, and_46_out, and_47_out, and_48_out, and_49_out);
  or or_7 (g, and_50_out, and_51_out, and_52_out, and_53_out, and_54_out, and_55_out, and_56_out);
endmodule

module msb_moderate (
  input  A,
  input  B,
  input  C,
  input  D,
  input  E,
  output a_2,
  output b_2,
  output c_2,
  output d_2,
  output e_2,
  output f,
  output g
);

  wire and_1_out, and_2_out, and_3_out, and_4_out, and_5_out, and_6_out, and_7_out, and_8_out, and_9_out,
       and_10_out, and_11_out, and_12_out, and_13_out, and_14_out, and_15_out, and_16_out, and_17_out,
       and_18_out, and_19_out, not_1_out, not_2_out, not_3_out, not_4_out, not_5_out, not_6_out, not_7_out,
       not_8_out, not_9_out, not_10_out, not_11_out, not_12_out, not_13_out, not_14_out, not_15_out,
       not_16_out, not_17_out, not_18_out, not_19_out, not_20_out, not_21_out, not_22_out, not_23_out,
       not_24_out, not_25_out, not_26_out, not_27_out, not_28_out;

  not not_1 (not_1_out, A);
  not not_2 (not_2_out, B);
  not not_3 (not_3_out, A);
  not not_4 (not_4_out, C);
  not not_5 (not_5_out, D);
  not not_6 (not_6_out, B);
  not not_7 (not_7_out, B);
  not not_8 (not_8_out, C);
  not not_9 (not_9_out, A);
  not not_10 (not_10_out, B);
  not not_11 (not_11_out, A);
  not not_12 (not_12_out, C);
  not not_13 (not_13_out, D);
  not not_14 (not_14_out, B);
  not not_15 (not_15_out, A);
  not not_16 (not_16_out, B);
  not not_17 (not_17_out, A);
  not not_18 (not_18_out, C);
  not not_19 (not_19_out, D);
  not not_20 (not_20_out, B);
  not not_21 (not_21_out, C);
  not not_22 (not_22_out, D);
  not not_23 (not_23_out, A);
  not not_24 (not_24_out, B);
  not not_25 (not_25_out, A);
  not not_26 (not_26_out, C);
  not not_27 (not_27_out, D);
  and and_1 (and_1_out, A, C);
  and and_2 (and_2_out, A, B);
  and and_3 (and_3_out, not_1_out, not_2_out);
  and and_4 (and_4_out, not_3_out, not_4_out, not_5_out);
  and and_5 (and_5_out, not_6_out, C);
  and and_6 (and_6_out, A, B);
  not not_28 (not_28_out, A);
  and and_7 (and_7_out, not_7_out, not_8_out);
  and and_8 (and_8_out, B, C, D);
  and and_9 (and_9_out, not_9_out, not_10_out);
  and and_10 (and_10_out, not_11_out, not_12_out, not_13_out);
  and and_11 (and_11_out, not_14_out, C);
  and and_12 (and_12_out, A, B);
  and and_13 (and_13_out, not_15_out, not_16_out);
  and and_14 (and_14_out, not_17_out, not_18_out, not_19_out);
  and and_15 (and_15_out, not_20_out, C);
  and and_16 (and_16_out, A, B, not_21_out);
  and and_17 (and_17_out, A, B, not_22_out);
  and and_18 (and_18_out, not_23_out, not_24_out);
  and and_19 (and_19_out, not_25_out, not_26_out, not_27_out);
  or or_1 (g, and_1_out, and_2_out);
  or or_2 (a_2, and_3_out, and_4_out, and_5_out, and_6_out);
  or or_3 (c_2, not_28_out, and_7_out, and_8_out);
  or or_4 (d_2, and_9_out, and_10_out, and_11_out, and_12_out);
  or or_5 (e_2, and_13_out, and_14_out, and_15_out, and_16_out, and_17_out);
  or or_6 (f, and_18_out, and_19_out);

  assign b_2 = 1'b1;
endmodule

module NS_light_moderate (
  input  A,
  input  B,
  input  C,
  input  D,
  input  E,
  output a_2,
  output b_2
);

  wire and_1_out, and_2_out, and_3_out, and_4_out, and_5_out, and_6_out, and_7_out, and_8_out, not_1_out,
       not_2_out, not_3_out, not_4_out, not_5_out, not_6_out, not_7_out, not_8_out, not_9_out, not_10_out,
       not_11_out, not_12_out, not_13_out, not_14_out, not_15_out, not_16_out, not_17_out, not_18_out;

  not not_1 (not_1_out, A);
  not not_2 (not_2_out, B);
  not not_3 (not_3_out, A);
  not not_4 (not_4_out, B);
  not not_5 (not_5_out, A);
  not not_6 (not_6_out, B);
  not not_7 (not_7_out, A);
  not not_8 (not_8_out, C);
  not not_9 (not_9_out, A);
  not not_10 (not_10_out, D);
  not not_11 (not_11_out, A);
  not not_12 (not_12_out, E);
  not not_13 (not_13_out, A);
  not not_14 (not_14_out, B);
  not not_15 (not_15_out, C);
  not not_16 (not_16_out, D);
  not not_17 (not_17_out, E);
  not not_18 (not_18_out, A);
  and and_1 (and_1_out, not_1_out, not_2_out, E);
  and and_2 (and_2_out, not_3_out, not_4_out, D);
  and and_3 (and_3_out, not_5_out, not_6_out, C);
  and and_4 (and_4_out, not_7_out, B, not_8_out);
  and and_5 (and_5_out, not_9_out, B, not_10_out);
  and and_6 (and_6_out, not_11_out, B, not_12_out);
  and and_7 (and_7_out, not_13_out, not_14_out, not_15_out, not_16_out, not_17_out);
  and and_8 (and_8_out, not_18_out, B, C, D, E);
  or or_1 (a_2, and_1_out, and_2_out, and_3_out, and_4_out, and_5_out, and_6_out);
  or or_2 (b_2, and_7_out, and_8_out);
endmodule

module EW_Light_moderate (
  input  A,
  input  B,
  input  C,
  input  D,
  input  E,
  output a_2,
  output b_2
);

  wire and_1_out, and_2_out, not_1_out, not_2_out, not_3_out, not_4_out, not_5_out, not_6_out;

  not not_1 (not_1_out, A);
  not not_2 (not_2_out, B);
  not not_3 (not_3_out, C);
  not not_4 (not_4_out, D);
  not not_5 (not_5_out, E);
  not not_6 (not_6_out, A);
  and and_1 (and_1_out, not_1_out, not_2_out, not_3_out, not_4_out, not_5_out);
  and and_2 (and_2_out, not_6_out, B, C, D, E);
  or or_1 (b_2, and_1_out, and_2_out);

  assign a_2 = A;
endmodule

module NS_low (
  input  A,
  input  B,
  input  C,
  input  D,
  output a_2,
  output b_2,
  output c_2,
  output d_2,
  output e,
  output f,
  output g
);

  wire and_1_out, and_2_out, and_3_out, and_4_out, and_5_out, and_6_out, and_7_out, and_8_out, and_9_out,
       and_10_out, and_11_out, and_12_out, and_13_out, and_14_out, and_15_out, and_16_out, not_1_out,
       not_2_out, not_3_out, not_4_out, not_5_out, not_6_out, not_7_out, not_8_out, not_9_out, not_10_out,
       not_11_out, not_12_out, not_13_out, not_14_out, not_15_out, not_16_out, not_17_out, not_18_out,
       not_19_out, not_20_out, not_21_out, not_22_out, not_23_out, not_24_out, not_25_out, not_26_out,
       not_27_out;

  not not_1 (not_1_out, A);
  not not_2 (not_2_out, B);
  and and_1 (and_1_out, not_2_out, not_3_out);
  not not_3 (not_3_out, D);
  and and_2 (and_2_out, B, D);
  not not_4 (not_4_out, A);
  not not_5 (not_5_out, B);
  not not_6 (not_6_out, C);
  and and_3 (and_3_out, not_6_out, not_7_out);
  not not_7 (not_7_out, D);
  and and_4 (and_4_out, C, D);
  not not_8 (not_8_out, A);
  not not_9 (not_9_out, C);
  not not_10 (not_10_out, A);
  not not_11 (not_11_out, B);
  and and_5 (and_5_out, not_11_out, not_12_out);
  not not_12 (not_12_out, D);
  not not_13 (not_13_out, B);
  and and_6 (and_6_out, not_13_out, C);
  and and_7 (and_7_out, C, not_14_out);
  not not_14 (not_14_out, D);
  and and_8 (and_8_out, B, not_15_out, D);
  not not_15 (not_15_out, C);
  not not_16 (not_16_out, A);
  not not_17 (not_17_out, B);
  and and_9 (and_9_out, not_17_out, not_18_out);
  not not_18 (not_18_out, D);
  and and_10 (and_10_out, C, not_19_out);
  not not_19 (not_19_out, D);
  not not_20 (not_20_out, A);
  not not_21 (not_21_out, C);
  and and_11 (and_11_out, not_21_out, not_22_out);
  not not_22 (not_22_out, D);
  and and_12 (and_12_out, B, not_23_out);
  not not_23 (not_23_out, C);
  and and_13 (and_13_out, B, not_24_out);
  not not_24 (not_24_out, D);
  not not_25 (not_25_out, B);
  and and_14 (and_14_out, A, not_25_out, C);
  and and_15 (and_15_out, A, B, not_26_out);
  not not_26 (not_26_out, C);
  and and_16 (and_16_out, A, B, not_27_out);
  not not_27 (not_27_out, D);
  or or_1 (a_2, not_1_out, and_1_out, C, and_2_out);
  or or_2 (b_2, not_4_out, not_5_out, and_3_out, and_4_out);
  or or_3 (c_2, not_8_out, not_9_out, D, B);
  or or_4 (d_2, not_10_out, and_5_out, and_6_out, and_7_out, and_8_out);
  or or_5 (e, not_16_out, and_9_out, and_10_out);
  or or_6 (f, not_20_out, and_11_out, and_12_out, and_13_out);
  or or_7 (g, and_14_out, and_15_out, and_16_out);
endmodule

module EW_low (
  input  A,
  input  B,
  input  C,
  input  D,
  output a_2,
  output b_2,
  output c_2,
  output d_2,
  output e,
  output f,
  output g
);

  wire and_1_out, and_2_out, and_3_out, and_4_out, and_5_out, and_6_out, and_7_out, and_8_out, and_9_out,
       and_10_out, and_11_out, and_12_out, and_13_out, and_14_out, and_15_out, and_16_out, not_1_out,
       not_2_out, not_3_out, not_4_out, not_5_out, not_6_out, not_7_out, not_8_out, not_9_out, not_10_out,
       not_11_out, not_12_out, not_13_out, not_14_out, not_15_out, not_16_out, not_17_out, not_18_out,
       not_19_out, not_20_out, not_21_out, not_22_out, not_23_out, not_24_out;

  not not_1 (not_1_out, B);
  and and_1 (and_1_out, not_1_out, not_2_out);
  not not_2 (not_2_out, D);
  and and_2 (and_2_out, B, D);
  not not_3 (not_3_out, B);
  not not_4 (not_4_out, C);
  and and_3 (and_3_out, not_4_out, not_5_out);
  not not_5 (not_5_out, D);
  and and_4 (and_4_out, C, D);
  not not_6 (not_6_out, C);
  not not_7 (not_7_out, B);
  and and_5 (and_5_out, not_7_out, not_8_out);
  not not_8 (not_8_out, D);
  not not_9 (not_9_out, B);
  and and_6 (and_6_out, not_9_out, C);
  and and_7 (and_7_out, C, not_10_out);
  not not_10 (not_10_out, D);
  and and_8 (and_8_out, B, not_11_out, D);
  not not_11 (not_11_out, C);
  not not_12 (not_12_out, B);
  and and_9 (and_9_out, not_12_out, not_13_out);
  not not_13 (not_13_out, D);
  and and_10 (and_10_out, C, not_14_out);
  not not_14 (not_14_out, D);
  not not_15 (not_15_out, C);
  and and_11 (and_11_out, not_15_out, not_16_out);
  not not_16 (not_16_out, D);
  and and_12 (and_12_out, B, not_17_out);
  not not_17 (not_17_out, C);
  and and_13 (and_13_out, B, not_18_out);
  not not_18 (not_18_out, D);
  not not_19 (not_19_out, A);
  and and_14 (and_14_out, not_19_out, not_20_out, C);
  not not_20 (not_20_out, B);
  not not_21 (not_21_out, A);
  and and_15 (and_15_out, not_21_out, B, not_22_out);
  not not_22 (not_22_out, C);
  not not_23 (not_23_out, A);
  and and_16 (and_16_out, not_23_out, B, not_24_out);
  not not_24 (not_24_out, D);
  or or_1 (a_2, and_1_out, C, and_2_out, A);
  or or_2 (b_2, not_3_out, and_3_out, and_4_out, A);
  or or_3 (c_2, not_6_out, D, B, A);
  or or_4 (d_2, and_5_out, and_6_out, and_7_out, and_8_out, A);
  or or_5 (e, and_9_out, and_10_out, A);
  or or_6 (f, and_11_out, and_12_out, and_13_out, A);
  or or_7 (g, and_14_out, and_15_out, and_16_out);
endmodule

module NS_lsb_moderate (
  input  A,
  input  B,
  input  C,
  input  D,
  input  E,
  output a_2,
  output b_2,
  output c_2,
  output d_2,
  output e_2,
  output f,
  output g
);

  wire and_1_out, and_2_out, and_3_out, and_4_out, and_5_out, and_6_out, and_7_out, and_8_out, and_9_out,
       and_10_out, and_11_out, and_12_out, and_13_out, and_14_out, and_15_out, and_16_out, and_17_out,
       and_18_out, and_19_out, and_20_out, and_21_out, and_22_out, and_23_out, and_24_out, and_25_out,
       and_26_out, and_27_out, and_28_out, and_29_out, not_1_out, not_2_out, not_3_out, not_4_out, not_5_out,
       not_6_out, not_7_out, not_8_out, not_9_out, not_10_out, not_11_out, not_12_out, not_13_out,
       not_14_out, not_15_out, not_16_out, not_17_out, not_18_out, not_19_out, not_20_out, not_21_out,
       not_22_out, not_23_out, not_24_out, not_25_out, not_26_out, not_27_out, not_28_out, not_29_out,
       not_30_out, not_31_out, not_32_out, not_33_out, not_34_out, not_35_out, not_36_out, not_37_out,
       not_38_out, not_39_out, not_40_out, not_41_out, not_42_out, not_43_out;

  not not_1 (not_1_out, B);
  not not_2 (not_2_out, D);
  not not_3 (not_3_out, B);
  not not_4 (not_4_out, E);
  not not_5 (not_5_out, B);
  not not_6 (not_6_out, E);
  not not_7 (not_7_out, C);
  not not_8 (not_8_out, D);
  not not_9 (not_9_out, A);
  not not_10 (not_10_out, C);
  not not_11 (not_11_out, B);
  not not_12 (not_12_out, D);
  not not_13 (not_13_out, C);
  not not_14 (not_14_out, D);
  not not_15 (not_15_out, B);
  not not_16 (not_16_out, C);
  not not_17 (not_17_out, E);
  not not_18 (not_18_out, B);
  not not_19 (not_19_out, D);
  not not_20 (not_20_out, B);
  not not_21 (not_21_out, C);
  not not_22 (not_22_out, E);
  not not_23 (not_23_out, B);
  not not_24 (not_24_out, D);
  not not_25 (not_25_out, B);
  not not_26 (not_26_out, C);
  not not_27 (not_27_out, B);
  not not_28 (not_28_out, B);
  not not_29 (not_29_out, D);
  not not_30 (not_30_out, C);
  not not_31 (not_31_out, D);
  not not_32 (not_32_out, B);
  not not_33 (not_33_out, B);
  not not_34 (not_34_out, C);
  not not_35 (not_35_out, D);
  not not_36 (not_36_out, D);
  not not_37 (not_37_out, E);
  not not_38 (not_38_out, A);
  and and_1 (and_1_out, not_1_out, not_2_out, E);
  and and_2 (and_2_out, not_3_out, D, not_4_out);
  and and_3 (and_3_out, not_5_out, C);
  and and_4 (and_4_out, C, not_6_out);
  and and_5 (and_5_out, B, not_7_out, not_8_out);
  and and_6 (and_6_out, B, D, E);
  or or_1 (b_2, not_9_out, not_10_out, D, B);
  not not_39 (not_39_out, A);
  not not_40 (not_40_out, E);
  and and_7 (and_7_out, not_11_out, D);
  and and_8 (and_8_out, B, not_12_out);
  not not_41 (not_41_out, A);
  and and_9 (and_9_out, not_13_out, not_14_out, E);
  and and_10 (and_10_out, not_15_out, not_16_out, D, not_17_out);
  and and_11 (and_11_out, not_18_out, C, not_19_out);
  and and_12 (and_12_out, not_20_out, C, E);
  and and_13 (and_13_out, B, not_21_out, E);
  and and_14 (and_14_out, B, C, not_22_out);
  not not_42 (not_42_out, A);
  and and_15 (and_15_out, not_23_out, not_24_out, E);
  and and_16 (and_16_out, not_25_out, C, E);
  and and_17 (and_17_out, B, not_26_out, E);
  and and_18 (and_18_out, B, C, D);
  not not_43 (not_43_out, A);
  and and_19 (and_19_out, not_27_out, D, E);
  and and_20 (and_20_out, not_28_out, C, not_29_out);
  and and_21 (and_21_out, C, E);
  and and_22 (and_22_out, B, not_30_out, not_31_out);
  and and_23 (and_23_out, B, C, D);
  and and_24 (and_24_out, A, not_32_out, E);
  and and_25 (and_25_out, A, not_33_out, not_34_out, D);
  and and_26 (and_26_out, A, D, E);
  and and_27 (and_27_out, A, C, not_35_out);
  and and_28 (and_28_out, A, B, not_36_out, not_37_out);
  and and_29 (and_29_out, A, B, C);
  or or_2 (a_2, not_38_out, and_1_out, and_2_out, and_3_out, and_4_out, and_5_out, and_6_out);
  or or_3 (c_2, not_39_out, not_40_out, and_7_out, C, and_8_out);
  or or_4 (d_2, not_41_out, and_9_out, and_10_out, and_11_out, and_12_out, and_13_out, and_14_out);
  or or_5 (e_2, not_42_out, and_15_out, and_16_out, and_17_out, and_18_out);
  or or_6 (f, not_43_out, and_19_out, and_20_out, and_21_out, and_22_out, and_23_out);
  or or_7 (g, and_24_out, and_25_out, and_26_out, and_27_out, and_28_out, and_29_out);
endmodule

module NS_msb_moderate (
  input  A,
  input  B,
  input  C,
  input  D,
  input  E,
  output a_2,
  output b_2,
  output c_2,
  output d_2,
  output e_2,
  output f,
  output g
);

  wire and_2_out, and_3_out, and_4_out, and_5_out, not_1_out, not_2_out, not_3_out, not_4_out, not_5_out,
       not_6_out, not_7_out, not_8_out, not_9_out, not_10_out, not_11_out, not_12_out, not_13_out,
       not_14_out, not_15_out, not_16_out, not_17_out, not_18_out, not_19_out, not_20_out;

  not not_1 (not_1_out, C);
  not not_2 (not_2_out, D);
  not not_3 (not_3_out, E);
  not not_4 (not_4_out, C);
  not not_5 (not_5_out, D);
  not not_6 (not_6_out, E);
  not not_7 (not_7_out, C);
  not not_8 (not_8_out, D);
  not not_9 (not_9_out, E);
  not not_10 (not_10_out, C);
  not not_11 (not_11_out, D);
  not not_12 (not_12_out, E);
  and and_1 (g, A, B, C, D);
  not not_13 (not_13_out, A);
  not not_14 (not_14_out, B);
  and and_2 (and_2_out, not_1_out, not_2_out, not_3_out);
  not not_15 (not_15_out, A);
  not not_16 (not_16_out, B);
  and and_3 (and_3_out, not_4_out, not_5_out, not_6_out);
  not not_17 (not_17_out, A);
  not not_18 (not_18_out, B);
  and and_4 (and_4_out, not_7_out, not_8_out, not_9_out);
  not not_19 (not_19_out, A);
  not not_20 (not_20_out, B);
  and and_5 (and_5_out, not_10_out, not_11_out, not_12_out);
  or or_1 (a_2, not_13_out, not_14_out, and_2_out);
  or or_2 (d_2, not_15_out, not_16_out, and_3_out);
  or or_3 (e_2, not_17_out, not_18_out, and_4_out);
  or or_4 (f, not_19_out, not_20_out, and_5_out);

  assign b_2 = 1'b1;
  assign c_2 = 1'b1;
endmodule

module EW_lsb_moderate (
  input  A,
  input  B,
  input  C,
  input  D,
  input  E,
  output a_2,
  output b_2,
  output c_2,
  output d_2,
  output e_2,
  output f,
  output g
);

  wire and_1_out, and_2_out, and_3_out, and_4_out, and_5_out, and_6_out, and_7_out, and_8_out, and_9_out,
       and_10_out, and_11_out, and_12_out, and_13_out, and_14_out, and_15_out, and_16_out, and_17_out,
       and_18_out, and_19_out, and_20_out, and_21_out, and_22_out, and_23_out, and_24_out, and_25_out,
       and_26_out, and_27_out, and_28_out, and_29_out, not_1_out, not_2_out, not_3_out, not_4_out, not_5_out,
       not_6_out, not_7_out, not_8_out, not_9_out, not_10_out, not_11_out, not_12_out, not_13_out,
       not_14_out, not_15_out, not_16_out, not_17_out, not_18_out, not_19_out, not_20_out, not_21_out,
       not_22_out, not_23_out, not_24_out, not_25_out, not_26_out, not_27_out, not_28_out, not_29_out,
       not_30_out, not_31_out, not_32_out, not_33_out, not_34_out, not_35_out, not_36_out, not_37_out,
       not_38_out, not_39_out, not_40_out, not_41_out, not_42_out, not_43_out, not_44_out, not_45_out;

  not not_1 (not_1_out, C);
  not not_2 (not_2_out, E);
  not not_3 (not_3_out, B);
  not not_4 (not_4_out, D);
  not not_5 (not_5_out, D);
  not not_6 (not_6_out, E);
  not not_7 (not_7_out, B);
  not not_8 (not_8_out, D);
  not not_9 (not_9_out, C);
  not not_10 (not_10_out, C);
  not not_11 (not_11_out, E);
  not not_12 (not_12_out, B);
  not not_13 (not_13_out, C);
  not not_14 (not_14_out, B);
  not not_15 (not_15_out, E);
  not not_16 (not_16_out, D);
  not not_17 (not_17_out, D);
  not not_18 (not_18_out, E);
  not not_19 (not_19_out, C);
  not not_20 (not_20_out, E);
  not not_21 (not_21_out, B);
  not not_22 (not_22_out, E);
  not not_23 (not_23_out, D);
  not not_24 (not_24_out, E);
  not not_25 (not_25_out, B);
  not not_26 (not_26_out, D);
  not not_27 (not_27_out, E);
  not not_28 (not_28_out, B);
  not not_29 (not_29_out, D);
  not not_30 (not_30_out, B);
  not not_31 (not_31_out, E);
  not not_32 (not_32_out, C);
  not not_33 (not_33_out, D);
  not not_34 (not_34_out, C);
  not not_35 (not_35_out, E);
  not not_36 (not_36_out, A);
  not not_37 (not_37_out, B);
  not not_38 (not_38_out, C);
  not not_39 (not_39_out, A);
  not not_40 (not_40_out, D);
  not not_41 (not_41_out, A);
  not not_42 (not_42_out, E);
  not not_43 (not_43_out, A);
  not not_44 (not_44_out, D);
  and and_1 (and_1_out, not_1_out, not_2_out);
  and and_2 (and_2_out, not_3_out, D);
  and and_3 (and_3_out, C, E);
  and and_4 (and_4_out, B, not_4_out);
  not not_45 (not_45_out, C);
  and and_5 (and_5_out, not_5_out, not_6_out);
  and and_6 (and_6_out, D, E);
  and and_7 (and_7_out, not_7_out, not_8_out);
  and and_8 (and_8_out, C, D);
  and and_9 (and_9_out, B, not_9_out);
  and and_10 (and_10_out, not_10_out, not_11_out);
  and and_11 (and_11_out, not_12_out, not_13_out, D);
  and and_12 (and_12_out, not_14_out, D, not_15_out);
  and and_13 (and_13_out, C, not_16_out, E);
  and and_14 (and_14_out, B, not_17_out, not_18_out);
  and and_15 (and_15_out, B, C, E);
  and and_16 (and_16_out, not_19_out, not_20_out);
  and and_17 (and_17_out, not_21_out, D, not_22_out);
  and and_18 (and_18_out, B, not_23_out, not_24_out);
  and and_19 (and_19_out, B, C, D, E);
  and and_20 (and_20_out, not_25_out, not_26_out, not_27_out);
  and and_21 (and_21_out, not_28_out, C, not_29_out);
  and and_22 (and_22_out, not_30_out, C, not_31_out);
  and and_23 (and_23_out, B, not_32_out, not_33_out);
  and and_24 (and_24_out, B, not_34_out, not_35_out);
  and and_25 (and_25_out, B, C, D);
  and and_26 (and_26_out, not_36_out, not_37_out, not_38_out, D);
  and and_27 (and_27_out, not_39_out, C, not_40_out);
  and and_28 (and_28_out, not_41_out, C, not_42_out);
  and and_29 (and_29_out, not_43_out, B, not_44_out);
  or or_1 (a_2, and_1_out, and_2_out, and_3_out, and_4_out, A);
  or or_2 (b_2, not_45_out, and_5_out, and_6_out, B, A);
  or or_3 (c_2, and_7_out, E, and_8_out, and_9_out, A);
  or or_4 (d_2, and_10_out, and_11_out, and_12_out, and_13_out, and_14_out, and_15_out, A);
  or or_5 (e_2, and_16_out, and_17_out, and_18_out, and_19_out, A);
  or or_6 (f, and_20_out, and_21_out, and_22_out, and_23_out, and_24_out, and_25_out, A);
  or or_7 (g, and_26_out, and_27_out, and_28_out, and_29_out);
endmodule

module EW_msb_moderate (
  input  A,
  input  B,
  input  C,
  input  D,
  input  E,
  output a_2,
  output b_2,
  output c_2,
  output d_2,
  output e_2,
  output f,
  output g
);

  wire and_1_out, and_2_out, and_3_out, and_4_out, and_5_out, and_6_out, and_7_out, and_8_out, not_1_out,
       not_2_out, not_3_out, not_4_out, not_5_out, not_6_out, not_7_out, not_8_out, not_9_out, not_10_out,
       not_11_out, not_12_out;

  not not_1 (not_1_out, C);
  not not_2 (not_2_out, D);
  not not_3 (not_3_out, C);
  not not_4 (not_4_out, D);
  not not_5 (not_5_out, C);
  not not_6 (not_6_out, D);
  not not_7 (not_7_out, C);
  not not_8 (not_8_out, D);
  not not_9 (not_9_out, B);
  and and_1 (and_1_out, not_1_out, not_2_out);
  and and_2 (and_2_out, C, D, E);
  not not_10 (not_10_out, B);
  and and_3 (and_3_out, not_3_out, not_4_out);
  and and_4 (and_4_out, C, D, E);
  not not_11 (not_11_out, B);
  and and_5 (and_5_out, not_5_out, not_6_out);
  and and_6 (and_6_out, C, D, E);
  not not_12 (not_12_out, B);
  and and_7 (and_7_out, not_7_out, not_8_out);
  and and_8 (and_8_out, C, D, E);
  or or_1 (a_2, not_9_out, and_1_out, and_2_out, A);
  or or_2 (d_2, not_10_out, and_3_out, and_4_out, A);
  or or_3 (e_2, not_11_out, and_5_out, and_6_out, A);
  or or_4 (f, not_12_out, and_7_out, and_8_out, A);

  assign b_2 = 1'b1;
  assign c_2 = 1'b1;
  assign g = 1'b0;
endmodule

module NS_lsb_high (
  input  A,
  input  B,
  input  C,
  input  D,
  input  E,
  input  F,
  output a_2,
  output b_2,
  output c_2,
  output d_2,
  output e_2,
  output f_2,
  output g
);

  wire and_1_out, and_2_out, and_3_out, and_4_out, and_5_out, and_6_out, and_7_out, and_8_out, and_9_out,
       and_10_out, and_11_out, and_12_out, and_13_out, and_14_out, and_15_out, and_16_out, and_17_out,
       and_18_out, and_19_out, and_20_out, and_21_out, and_22_out, and_23_out, and_24_out, and_25_out,
       and_26_out, and_27_out, and_28_out, and_29_out, and_30_out, and_31_out, and_32_out, and_33_out,
       and_34_out, and_35_out, and_36_out, and_37_out, and_38_out, and_39_out, and_40_out, and_41_out,
       and_42_out, and_43_out, and_44_out, and_45_out, and_46_out, and_47_out, and_48_out, and_49_out,
       and_50_out, and_51_out, and_52_out, and_53_out, and_54_out, and_55_out, and_56_out, and_57_out,
       and_58_out, and_59_out, and_60_out, and_61_out, and_62_out, and_63_out, and_64_out, and_65_out,
       and_66_out, and_67_out, and_68_out, and_69_out, and_70_out, and_71_out, and_72_out, and_73_out,
       and_74_out, not_1_out, not_2_out, not_3_out, not_4_out, not_5_out, not_6_out, not_7_out, not_8_out,
       not_9_out, not_10_out, not_11_out, not_12_out, not_13_out, not_14_out, not_15_out, not_16_out,
       not_17_out, not_18_out, not_19_out, not_20_out, not_21_out, not_22_out, not_23_out, not_24_out,
       not_25_out, not_26_out, not_27_out, not_28_out, not_29_out, not_30_out, not_31_out, not_32_out,
       not_33_out, not_34_out, not_35_out, not_36_out, not_37_out, not_38_out, not_39_out, not_40_out,
       not_41_out, not_42_out, not_43_out, not_44_out, not_45_out, not_46_out, not_47_out, not_48_out,
       not_49_out, not_50_out, not_51_out, not_52_out, not_53_out, not_54_out, not_55_out, not_56_out,
       not_57_out, not_58_out, not_59_out, not_60_out, not_61_out, not_62_out, not_63_out, not_64_out,
       not_65_out, not_66_out, not_67_out, not_68_out, not_69_out, not_70_out, not_71_out, not_72_out,
       not_73_out, not_74_out, not_75_out, not_76_out, not_77_out, not_78_out, not_79_out, not_80_out,
       not_81_out, not_82_out, not_83_out, not_84_out, not_85_out, not_86_out, not_87_out, not_88_out,
       not_89_out, not_90_out, not_91_out, not_92_out, not_93_out, not_94_out, not_95_out, not_96_out,
       not_97_out, not_98_out, not_99_out, not_100_out, not_101_out, not_102_out, not_103_out, not_104_out,
       not_105_out, not_106_out, not_107_out, not_108_out, not_109_out, not_110_out, not_111_out,
       not_112_out, not_113_out, not_114_out, not_115_out, not_116_out, not_117_out, not_118_out,
       not_119_out, not_120_out, not_121_out;

  not not_1 (not_1_out, A);
  not not_2 (not_2_out, B);
  not not_3 (not_3_out, A);
  not not_4 (not_4_out, E);
  not not_5 (not_5_out, B);
  not not_6 (not_6_out, D);
  not not_7 (not_7_out, F);
  not not_8 (not_8_out, B);
  not not_9 (not_9_out, E);
  not not_10 (not_10_out, A);
  not not_11 (not_11_out, C);
  not not_12 (not_12_out, D);
  not not_13 (not_13_out, F);
  not not_14 (not_14_out, C);
  not not_15 (not_15_out, A);
  not not_16 (not_16_out, B);
  not not_17 (not_17_out, A);
  not not_18 (not_18_out, C);
  not not_19 (not_19_out, A);
  not not_20 (not_20_out, D);
  not not_21 (not_21_out, E);
  not not_22 (not_22_out, B);
  not not_23 (not_23_out, D);
  not not_24 (not_24_out, B);
  not not_25 (not_25_out, E);
  not not_26 (not_26_out, F);
  not not_27 (not_27_out, C);
  not not_28 (not_28_out, A);
  not not_29 (not_29_out, B);
  not not_30 (not_30_out, E);
  not not_31 (not_31_out, B);
  not not_32 (not_32_out, F);
  not not_33 (not_33_out, E);
  not not_34 (not_34_out, F);
  not not_35 (not_35_out, D);
  not not_36 (not_36_out, B);
  not not_37 (not_37_out, E);
  not not_38 (not_38_out, C);
  not not_39 (not_39_out, E);
  not not_40 (not_40_out, D);
  not not_41 (not_41_out, A);
  not not_42 (not_42_out, B);
  not not_43 (not_43_out, E);
  not not_44 (not_44_out, C);
  not not_45 (not_45_out, D);
  not not_46 (not_46_out, A);
  not not_47 (not_47_out, B);
  not not_48 (not_48_out, A);
  not not_49 (not_49_out, C);
  not not_50 (not_50_out, E);
  not not_51 (not_51_out, B);
  not not_52 (not_52_out, D);
  not not_53 (not_53_out, F);
  not not_54 (not_54_out, A);
  not not_55 (not_55_out, D);
  not not_56 (not_56_out, B);
  not not_57 (not_57_out, C);
  not not_58 (not_58_out, D);
  not not_59 (not_59_out, C);
  not not_60 (not_60_out, F);
  not not_61 (not_61_out, A);
  not not_62 (not_62_out, F);
  not not_63 (not_63_out, B);
  not not_64 (not_64_out, E);
  not not_65 (not_65_out, B);
  not not_66 (not_66_out, E);
  not not_67 (not_67_out, F);
  not not_68 (not_68_out, C);
  not not_69 (not_69_out, E);
  not not_70 (not_70_out, A);
  not not_71 (not_71_out, B);
  not not_72 (not_72_out, A);
  not not_73 (not_73_out, C);
  not not_74 (not_74_out, D);
  not not_75 (not_75_out, A);
  not not_76 (not_76_out, C);
  not not_77 (not_77_out, E);
  not not_78 (not_78_out, A);
  not not_79 (not_79_out, E);
  not not_80 (not_80_out, F);
  not not_81 (not_81_out, B);
  not not_82 (not_82_out, D);
  not not_83 (not_83_out, F);
  not not_84 (not_84_out, C);
  not not_85 (not_85_out, F);
  not not_86 (not_86_out, A);
  not not_87 (not_87_out, F);
  not not_88 (not_88_out, C);
  not not_89 (not_89_out, F);
  not not_90 (not_90_out, A);
  not not_91 (not_91_out, B);
  not not_92 (not_92_out, A);
  not not_93 (not_93_out, C);
  not not_94 (not_94_out, E);
  not not_95 (not_95_out, C);
  not not_96 (not_96_out, E);
  not not_97 (not_97_out, F);
  not not_98 (not_98_out, A);
  not not_99 (not_99_out, F);
  not not_100 (not_100_out, B);
  not not_101 (not_101_out, C);
  not not_102 (not_102_out, E);
  not not_103 (not_103_out, B);
  not not_104 (not_104_out, F);
  not not_105 (not_105_out, B);
  not not_106 (not_106_out, D);
  not not_107 (not_107_out, E);
  not not_108 (not_108_out, B);
  not not_109 (not_109_out, F);
  not not_110 (not_110_out, D);
  not not_111 (not_111_out, D);
  not not_112 (not_112_out, F);
  not not_113 (not_113_out, C);
  not not_114 (not_114_out, D);
  not not_115 (not_115_out, B);
  not not_116 (not_116_out, E);
  not not_117 (not_117_out, B);
  not not_118 (not_118_out, F);
  not not_119 (not_119_out, E);
  not not_120 (not_120_out, D);
  not not_121 (not_121_out, F);
  and and_1 (and_1_out, not_1_out, not_2_out);
  and and_2 (and_2_out, not_3_out, not_4_out);
  and and_3 (and_3_out, not_5_out, not_6_out, not_7_out);
  and and_4 (and_4_out, not_8_out, D, F);
  and and_5 (and_5_out, C, not_9_out);
  and and_6 (and_6_out, not_10_out, C, F);
  and and_7 (and_7_out, B, not_11_out, not_12_out);
  and and_8 (and_8_out, B, D, not_13_out);
  and and_9 (and_9_out, B, C, D);
  and and_10 (and_10_out, A, not_14_out, E);
  and and_11 (and_11_out, not_15_out, not_16_out);
  and and_12 (and_12_out, not_17_out, not_18_out);
  and and_13 (and_13_out, not_19_out, not_20_out, not_21_out);
  and and_14 (and_14_out, not_22_out, not_23_out);
  and and_15 (and_15_out, not_24_out, not_25_out, not_26_out);
  and and_16 (and_16_out, not_27_out, E, F);
  and and_17 (and_17_out, not_28_out, D, E);
  and and_18 (and_18_out, not_29_out, C, not_30_out);
  and and_19 (and_19_out, not_31_out, C, not_32_out);
  and and_20 (and_20_out, B, not_33_out, F);
  and and_21 (and_21_out, B, E, not_34_out);
  and and_22 (and_22_out, A, C, not_35_out);
  and and_23 (and_23_out, A, B, D);
  and and_24 (and_24_out, not_36_out, not_37_out);
  and and_25 (and_25_out, not_38_out, not_39_out);
  and and_26 (and_26_out, not_40_out, F);
  and and_27 (and_27_out, not_41_out, E);
  and and_28 (and_28_out, not_42_out, D);
  and and_29 (and_29_out, D, not_43_out);
  and and_30 (and_30_out, B, not_44_out, not_45_out);
  and and_31 (and_31_out, A, C);
  and and_32 (and_32_out, not_46_out, not_47_out);
  and and_33 (and_33_out, not_48_out, not_49_out, not_50_out);
  and and_34 (and_34_out, not_51_out, not_52_out, not_53_out);
  and and_35 (and_35_out, not_54_out, not_55_out, F);
  and and_36 (and_36_out, not_56_out, not_57_out, not_58_out, E);
  and and_37 (and_37_out, not_59_out, E, not_60_out);
  and and_38 (and_38_out, not_61_out, D, not_62_out);
  and and_39 (and_39_out, not_63_out, D, not_64_out, F);
  and and_40 (and_40_out, not_65_out, C, D, F);
  and and_41 (and_41_out, B, not_66_out, not_67_out);
  and and_42 (and_42_out, A, B, not_68_out, D, E);
  and and_43 (and_43_out, A, B, C, not_69_out);
  and and_44 (and_44_out, not_70_out, not_71_out);
  and and_45 (and_45_out, not_72_out, not_73_out, not_74_out);
  and and_46 (and_46_out, not_75_out, not_76_out, not_77_out);
  and and_47 (and_47_out, not_78_out, not_79_out, not_80_out);
  and and_48 (and_48_out, not_81_out, not_82_out, not_83_out);
  and and_49 (and_49_out, not_84_out, E, not_85_out);
  and and_50 (and_50_out, not_86_out, D, not_87_out);
  and and_51 (and_51_out, B, not_88_out, not_89_out);
  and and_52 (and_52_out, A, B, D, E);
  and and_53 (and_53_out, A, B, C, D);
  and and_54 (and_54_out, not_90_out, not_91_out);
  and and_55 (and_55_out, not_92_out, not_93_out, not_94_out);
  and and_56 (and_56_out, not_95_out, not_96_out, not_97_out);
  and and_57 (and_57_out, not_98_out, D, not_99_out);
  and and_58 (and_58_out, not_100_out, not_101_out, D, not_102_out);
  and and_59 (and_59_out, not_103_out, D, not_104_out);
  and and_60 (and_60_out, not_105_out, C, not_106_out, not_107_out);
  and and_61 (and_61_out, not_108_out, C, not_109_out);
  and and_62 (and_62_out, C, D, E);
  and and_63 (and_63_out, B, not_110_out, E);
  and and_64 (and_64_out, A, B, C, D);
  and and_65 (and_65_out, B, C, not_111_out);
  and and_66 (and_66_out, B, C, not_112_out);
  and and_67 (and_67_out, B, C, E);
  and and_68 (and_68_out, A, not_113_out, not_114_out, E);
  and and_69 (and_69_out, A, not_115_out, D, not_116_out);
  and and_70 (and_70_out, A, not_117_out, D, not_118_out);
  and and_71 (and_71_out, A, C, not_119_out);
  and and_72 (and_72_out, A, C, D);
  and and_73 (and_73_out, A, B, not_120_out, not_121_out);
  and and_74 (and_74_out, A, B, E);
  or or_1 (a_2, and_1_out, and_2_out, and_3_out, and_4_out, and_5_out, and_6_out, and_7_out, and_8_out, and_9_out, and_10_out);
  or or_2 (b_2, and_11_out, and_12_out, and_13_out, and_14_out, and_15_out, and_16_out, and_17_out, and_18_out, and_19_out, and_20_out, and_21_out, and_22_out, and_23_out);
  or or_3 (c_2, and_24_out, and_25_out, and_26_out, and_27_out, and_28_out, and_29_out, and_30_out, and_31_out);
  or or_4 (e_2, and_44_out, and_45_out, and_46_out, and_47_out, and_48_out, and_49_out, and_50_out, and_51_out, and_52_out, and_53_out);
  or or_5 (f_2, and_54_out, and_55_out, and_56_out, and_57_out, and_58_out, and_59_out, and_60_out, and_61_out, and_62_out, and_63_out, and_64_out);
  or or_6 (g, and_65_out, and_66_out, and_67_out, and_68_out, and_69_out, and_70_out, and_71_out, and_72_out, and_73_out, and_74_out);
  or or_7 (d_2, and_32_out, and_33_out, and_34_out, and_35_out, and_36_out, and_37_out, and_38_out, and_39_out, and_40_out, and_41_out, and_42_out, and_43_out);
endmodule

module NS_msb_high (
  input  A,
  input  B,
  input  C,
  input  D,
  input  E,
  input  F,
  output a_2,
  output b_2,
  output c_2,
  output d_2,
  output e_2,
  output f_2,
  output g
);

  wire and_1_out, and_2_out, and_3_out, and_4_out, and_5_out, and_6_out, and_7_out, and_8_out, and_9_out,
       and_10_out, and_11_out, and_12_out, and_13_out, and_14_out, not_1_out, not_2_out, not_3_out,
       not_4_out, not_5_out, not_6_out, not_7_out, not_8_out, not_9_out, not_10_out, not_11_out, not_12_out,
       not_13_out, not_14_out, not_15_out, not_16_out, not_17_out, not_18_out, not_19_out, not_20_out,
       not_21_out, not_22_out, not_23_out, not_24_out, not_25_out, not_26_out, not_27_out, not_28_out,
       not_29_out, not_30_out;

  not not_1 (not_1_out, B);
  not not_2 (not_2_out, B);
  not not_3 (not_3_out, C);
  not not_4 (not_4_out, D);
  not not_5 (not_5_out, E);
  not not_6 (not_6_out, A);
  not not_7 (not_7_out, C);
  not not_8 (not_8_out, E);
  not not_9 (not_9_out, B);
  not not_10 (not_10_out, B);
  not not_11 (not_11_out, C);
  not not_12 (not_12_out, D);
  not not_13 (not_13_out, E);
  not not_14 (not_14_out, B);
  not not_15 (not_15_out, B);
  not not_16 (not_16_out, C);
  not not_17 (not_17_out, D);
  not not_18 (not_18_out, E);
  not not_19 (not_19_out, B);
  not not_20 (not_20_out, C);
  not not_21 (not_21_out, D);
  not not_22 (not_22_out, E);
  not not_23 (not_23_out, B);
  not not_24 (not_24_out, D);
  not not_25 (not_25_out, E);
  not not_26 (not_26_out, F);
  not not_27 (not_27_out, A);
  and and_1 (and_1_out, not_1_out, C, E);
  and and_2 (and_2_out, not_2_out, C, D);
  and and_3 (and_3_out, B, not_3_out, not_4_out, not_5_out);
  or or_1 (c_2, not_6_out, not_7_out, not_8_out, D, B);
  not not_28 (not_28_out, A);
  and and_4 (and_4_out, not_9_out, C, E);
  and and_5 (and_5_out, not_10_out, C, D);
  and and_6 (and_6_out, B, not_11_out, not_12_out, not_13_out);
  not not_29 (not_29_out, A);
  and and_7 (and_7_out, not_14_out, C, E);
  and and_8 (and_8_out, not_15_out, C, D);
  and and_9 (and_9_out, B, not_16_out, not_17_out, not_18_out);
  not not_30 (not_30_out, A);
  and and_10 (and_10_out, not_19_out, C, D);
  and and_11 (and_11_out, B, not_20_out, not_21_out, not_22_out);
  and and_12 (and_12_out, A, not_23_out, C, not_24_out, E);
  and and_13 (and_13_out, A, C, D, not_25_out, not_26_out);
  and and_14 (and_14_out, A, B, C, D);
  or or_2 (a_2, not_27_out, and_1_out, and_2_out, and_3_out);
  or or_3 (d_2, not_28_out, and_4_out, and_5_out, and_6_out);
  or or_4 (e_2, not_29_out, and_7_out, and_8_out, and_9_out);
  or or_5 (f_2, not_30_out, and_10_out, and_11_out);
  or or_6 (g, and_12_out, and_13_out, and_14_out);

  assign b_2 = 1'b1;
endmodule

module EW_lsb_high (
  input  A,
  input  B,
  input  C,
  input  D,
  input  E,
  input  F,
  output a_2,
  output b_2,
  output c_2,
  output d_2,
  output e_2,
  output f_2,
  output g
);

  wire and_1_out, and_2_out, and_3_out, and_4_out, and_5_out, and_6_out, and_7_out, and_8_out, and_9_out,
       and_10_out, and_11_out, and_12_out, and_13_out, and_14_out, and_15_out, and_16_out, and_17_out,
       and_18_out, and_19_out, and_20_out, and_21_out, and_22_out, and_23_out, and_24_out, and_25_out,
       and_26_out, and_27_out, and_28_out, and_29_out, and_30_out, and_31_out, and_32_out, and_33_out,
       and_34_out, and_35_out, and_36_out, and_37_out, and_38_out, and_39_out, and_40_out, and_41_out,
       and_42_out, and_43_out, and_44_out, and_45_out, and_46_out, and_47_out, and_48_out, not_1_out,
       not_2_out, not_3_out, not_4_out, not_5_out, not_6_out, not_7_out, not_8_out, not_9_out, not_10_out,
       not_11_out, not_12_out, not_13_out, not_14_out, not_15_out, not_16_out, not_17_out, not_18_out,
       not_19_out, not_20_out, not_21_out, not_22_out, not_23_out, not_24_out, not_25_out, not_26_out,
       not_27_out, not_28_out, not_29_out, not_30_out, not_31_out, not_32_out, not_33_out, not_34_out,
       not_35_out, not_36_out, not_37_out, not_38_out, not_39_out, not_40_out, not_41_out, not_42_out,
       not_43_out, not_44_out, not_45_out, not_46_out, not_47_out, not_48_out, not_49_out, not_50_out,
       not_51_out, not_52_out, not_53_out, not_54_out, not_55_out, not_56_out, not_57_out, not_58_out,
       not_59_out, not_60_out, not_61_out, not_62_out, not_63_out, not_64_out, not_65_out, not_66_out,
       not_67_out, not_68_out, not_69_out, not_70_out, not_71_out;

  not not_1 (not_1_out, D);
  not not_2 (not_2_out, F);
  not not_3 (not_3_out, C);
  not not_4 (not_4_out, B);
  not not_5 (not_5_out, E);
  not not_6 (not_6_out, D);
  not not_7 (not_7_out, F);
  not not_8 (not_8_out, B);
  not not_9 (not_9_out, D);
  not not_10 (not_10_out, B);
  not not_11 (not_11_out, E);
  not not_12 (not_12_out, F);
  not not_13 (not_13_out, D);
  not not_14 (not_14_out, C);
  not not_15 (not_15_out, E);
  not not_16 (not_16_out, F);
  not not_17 (not_17_out, C);
  not not_18 (not_18_out, E);
  not not_19 (not_19_out, D);
  not not_20 (not_20_out, D);
  not not_21 (not_21_out, F);
  not not_22 (not_22_out, B);
  not not_23 (not_23_out, C);
  not not_24 (not_24_out, D);
  not not_25 (not_25_out, C);
  not not_26 (not_26_out, F);
  not not_27 (not_27_out, B);
  not not_28 (not_28_out, E);
  not not_29 (not_29_out, E);
  not not_30 (not_30_out, F);
  not not_31 (not_31_out, F);
  not not_32 (not_32_out, D);
  not not_33 (not_33_out, F);
  not not_34 (not_34_out, C);
  not not_35 (not_35_out, F);
  not not_36 (not_36_out, E);
  not not_37 (not_37_out, F);
  not not_38 (not_38_out, F);
  not not_39 (not_39_out, C);
  not not_40 (not_40_out, E);
  not not_41 (not_41_out, F);
  not not_42 (not_42_out, B);
  not not_43 (not_43_out, C);
  not not_44 (not_44_out, E);
  not not_45 (not_45_out, C);
  not not_46 (not_46_out, F);
  not not_47 (not_47_out, D);
  not not_48 (not_48_out, E);
  not not_49 (not_49_out, D);
  not not_50 (not_50_out, F);
  not not_51 (not_51_out, A);
  not not_52 (not_52_out, C);
  not not_53 (not_53_out, D);
  not not_54 (not_54_out, A);
  not not_55 (not_55_out, B);
  not not_56 (not_56_out, E);
  not not_57 (not_57_out, A);
  not not_58 (not_58_out, B);
  not not_59 (not_59_out, F);
  not not_60 (not_60_out, A);
  not not_61 (not_61_out, B);
  not not_62 (not_62_out, E);
  not not_63 (not_63_out, A);
  not not_64 (not_64_out, B);
  not not_65 (not_65_out, B);
  not not_66 (not_66_out, E);
  not not_67 (not_67_out, F);
  not not_68 (not_68_out, A);
  not not_69 (not_69_out, C);
  not not_70 (not_70_out, D);
  not not_71 (not_71_out, F);
  and and_1 (and_1_out, not_1_out, not_2_out);
  and and_2 (and_2_out, not_3_out, E);
  and and_3 (and_3_out, not_4_out, D, F);
  and and_4 (and_4_out, C, not_5_out);
  and and_5 (and_5_out, B, not_6_out);
  and and_6 (and_6_out, B, not_7_out);
  and and_7 (and_7_out, B, E);
  and and_8 (and_8_out, not_8_out, not_9_out);
  and and_9 (and_9_out, not_10_out, not_11_out, not_12_out);
  and and_10 (and_10_out, not_13_out, F);
  and and_11 (and_11_out, not_14_out, E, F);
  and and_12 (and_12_out, C, not_15_out);
  and and_13 (and_13_out, C, not_16_out);
  and and_14 (and_14_out, B, E);
  and and_15 (and_15_out, B, D);
  and and_16 (and_16_out, not_17_out, not_18_out);
  and and_17 (and_17_out, D, E);
  and and_18 (and_18_out, C, not_19_out);
  and and_19 (and_19_out, not_20_out, not_21_out);
  and and_20 (and_20_out, not_22_out, not_23_out, not_24_out, E);
  and and_21 (and_21_out, not_25_out, E, not_26_out);
  and and_22 (and_22_out, not_27_out, D, not_28_out, F);
  and and_23 (and_23_out, C, not_29_out, not_30_out);
  and and_24 (and_24_out, C, D, F);
  and and_25 (and_25_out, B, not_31_out);
  and and_26 (and_26_out, B, D, E);
  and and_27 (and_27_out, B, C);
  and and_28 (and_28_out, not_32_out, not_33_out);
  and and_29 (and_29_out, not_34_out, E, not_35_out);
  and and_30 (and_30_out, C, not_36_out, not_37_out);
  and and_31 (and_31_out, B, not_38_out);
  and and_32 (and_32_out, B, D, E);
  and and_33 (and_33_out, B, C);
  and and_34 (and_34_out, not_39_out, not_40_out, not_41_out);
  and and_35 (and_35_out, not_42_out, not_43_out, D, not_44_out);
  and and_36 (and_36_out, not_45_out, D, not_46_out);
  and and_37 (and_37_out, C, not_47_out, not_48_out);
  and and_38 (and_38_out, C, not_49_out, not_50_out);
  and and_39 (and_39_out, C, D, E);
  and and_40 (and_40_out, B, E);
  and and_41 (and_41_out, B, C);
  and and_42 (and_42_out, not_51_out, not_52_out, not_53_out, E);
  and and_43 (and_43_out, not_54_out, not_55_out, D, not_56_out);
  and and_44 (and_44_out, not_57_out, not_58_out, D, not_59_out);
  and and_45 (and_45_out, not_60_out, not_61_out, C, not_62_out);
  and and_46 (and_46_out, not_63_out, not_64_out, C, D);
  and and_47 (and_47_out, not_65_out, C, D, not_66_out, not_67_out);
  and and_48 (and_48_out, not_68_out, B, not_69_out, not_70_out, not_71_out);
  or or_1 (a_2, and_1_out, and_2_out, and_3_out, and_4_out, and_5_out, and_6_out, and_7_out, A);
  or or_2 (b_2, and_8_out, and_9_out, and_10_out, and_11_out, and_12_out, and_13_out, and_14_out, and_15_out, A);
  or or_3 (c_2, and_16_out, F, and_17_out, and_18_out, B, A);
  or or_4 (d_2, and_19_out, and_20_out, and_21_out, and_22_out, and_23_out, and_24_out, and_25_out, and_26_out, and_27_out, A);
  or or_5 (e_2, and_28_out, and_29_out, and_30_out, and_31_out, and_32_out, and_33_out, A);
  or or_6 (f_2, and_34_out, and_35_out, and_36_out, and_37_out, and_38_out, and_39_out, and_40_out, and_41_out, A);
  or or_7 (g, and_42_out, and_43_out, and_44_out, and_45_out, and_46_out, and_47_out, and_48_out);
endmodule

module EW_msb_high (
  input  A,
  input  B,
  input  C,
  input  D,
  input  E,
  input  F,
  output a_2,
  output b_2,
  output c_2,
  output d_2,
  output e_2,
  output f_2,
  output g
);

  wire and_1_out, and_2_out, and_3_out, and_4_out, and_5_out, and_6_out, and_7_out, and_8_out, and_9_out,
       and_10_out, and_11_out, and_12_out, and_13_out, and_14_out, and_15_out, and_16_out, not_1_out,
       not_2_out, not_3_out, not_4_out, not_5_out, not_6_out, not_7_out, not_8_out, not_9_out, not_10_out,
       not_11_out, not_12_out, not_13_out, not_14_out, not_15_out, not_16_out, not_17_out, not_18_out,
       not_19_out, not_20_out, not_21_out, not_22_out, not_23_out, not_24_out, not_25_out, not_26_out,
       not_27_out, not_28_out, not_29_out;

  not not_1 (not_1_out, B);
  not not_2 (not_2_out, C);
  not not_3 (not_3_out, B);
  not not_4 (not_4_out, D);
  not not_5 (not_5_out, E);
  not not_6 (not_6_out, C);
  not not_7 (not_7_out, B);
  not not_8 (not_8_out, D);
  not not_9 (not_9_out, B);
  not not_10 (not_10_out, C);
  not not_11 (not_11_out, B);
  not not_12 (not_12_out, D);
  not not_13 (not_13_out, E);
  not not_14 (not_14_out, C);
  not not_15 (not_15_out, B);
  not not_16 (not_16_out, C);
  not not_17 (not_17_out, B);
  not not_18 (not_18_out, D);
  not not_19 (not_19_out, E);
  not not_20 (not_20_out, C);
  not not_21 (not_21_out, B);
  not not_22 (not_22_out, C);
  not not_23 (not_23_out, B);
  not not_24 (not_24_out, D);
  not not_25 (not_25_out, E);
  not not_26 (not_26_out, C);
  not not_27 (not_27_out, A);
  not not_28 (not_28_out, C);
  not not_29 (not_29_out, E);
  and and_1 (and_1_out, not_1_out, not_2_out);
  and and_2 (and_2_out, not_3_out, not_4_out, not_5_out);
  and and_3 (and_3_out, not_6_out, D);
  and and_4 (and_4_out, B, C);
  or or_1 (c_2, not_7_out, not_8_out, E, C, A);
  and and_5 (and_5_out, not_9_out, not_10_out);
  and and_6 (and_6_out, not_11_out, not_12_out, not_13_out);
  and and_7 (and_7_out, not_14_out, D);
  and and_8 (and_8_out, B, C);
  and and_9 (and_9_out, not_15_out, not_16_out);
  and and_10 (and_10_out, not_17_out, not_18_out, not_19_out);
  and and_11 (and_11_out, not_20_out, D);
  and and_12 (and_12_out, B, C);
  and and_13 (and_13_out, not_21_out, not_22_out);
  and and_14 (and_14_out, not_23_out, not_24_out, not_25_out);
  and and_15 (and_15_out, not_26_out, D, E);
  and and_16 (and_16_out, B, C);
  and and_17 (g, not_27_out, B, not_28_out, D, not_29_out);
  or or_2 (a_2, and_1_out, and_2_out, and_3_out, and_4_out, A);
  or or_3 (d_2, and_5_out, and_6_out, and_7_out, and_8_out, A);
  or or_4 (e_2, and_9_out, and_10_out, and_11_out, and_12_out, A);
  or or_5 (f_2, and_13_out, and_14_out, and_15_out, and_16_out, A);

  assign b_2 = 1'b1;
endmodule

module NS_light_high (
  input  A,
  input  B,
  input  C,
  input  D,
  input  E,
  input  F,
  output a_2,
  output b_2
);

  wire and_1_out, and_2_out, and_3_out, and_4_out, and_5_out, and_6_out, and_7_out, and_8_out, not_1_out,
       not_2_out, not_3_out, not_4_out, not_5_out, not_6_out, not_7_out, not_8_out, not_9_out, not_10_out,
       not_11_out, not_12_out, not_13_out, not_14_out, not_15_out, not_16_out, not_17_out, not_18_out,
       not_19_out, not_20_out, not_21_out, not_22_out, not_23_out;

  not not_1 (not_1_out, A);
  not not_2 (not_2_out, B);
  not not_3 (not_3_out, A);
  not not_4 (not_4_out, B);
  not not_5 (not_5_out, A);
  not not_6 (not_6_out, B);
  not not_7 (not_7_out, A);
  not not_8 (not_8_out, B);
  not not_9 (not_9_out, A);
  not not_10 (not_10_out, C);
  not not_11 (not_11_out, D);
  not not_12 (not_12_out, A);
  not not_13 (not_13_out, C);
  not not_14 (not_14_out, E);
  not not_15 (not_15_out, A);
  not not_16 (not_16_out, B);
  not not_17 (not_17_out, C);
  not not_18 (not_18_out, D);
  not not_19 (not_19_out, E);
  not not_20 (not_20_out, F);
  not not_21 (not_21_out, A);
  not not_22 (not_22_out, C);
  not not_23 (not_23_out, F);
  and and_1 (and_1_out, not_1_out, not_2_out, F);
  and and_2 (and_2_out, not_3_out, not_4_out, E);
  and and_3 (and_3_out, not_5_out, not_6_out, D);
  and and_4 (and_4_out, not_7_out, not_8_out, C);
  and and_5 (and_5_out, not_9_out, B, not_10_out, not_11_out);
  and and_6 (and_6_out, not_12_out, B, not_13_out, not_14_out);
  and and_7 (and_7_out, not_15_out, not_16_out, not_17_out, not_18_out, not_19_out, not_20_out);
  and and_8 (and_8_out, not_21_out, B, not_22_out, D, E, not_23_out);
  or or_1 (a_2, and_1_out, and_2_out, and_3_out, and_4_out, and_5_out, and_6_out);
  or or_2 (b_2, and_7_out, and_8_out);
endmodule

module EW_Light_high (
  input  A,
  input  B,
  input  C,
  input  D,
  input  E,
  input  F,
  output a_2,
  output b_2
);

  wire and_1_out, and_2_out, and_3_out, and_4_out, not_1_out, not_2_out, not_3_out, not_4_out, not_5_out,
       not_6_out, not_7_out, not_8_out, not_9_out;

  and and_1 (and_1_out, B, D, E, F);
  and and_2 (and_2_out, B, C);
  not not_1 (not_1_out, A);
  not not_2 (not_2_out, B);
  not not_3 (not_3_out, C);
  not not_4 (not_4_out, D);
  not not_5 (not_5_out, E);
  not not_6 (not_6_out, F);
  not not_7 (not_7_out, A);
  not not_8 (not_8_out, C);
  not not_9 (not_9_out, F);
  or or_1 (a_2, and_1_out, and_2_out, A);
  and and_3 (and_3_out, not_1_out, not_2_out, not_3_out, not_4_out, not_5_out, not_6_out);
  and and_4 (and_4_out, not_7_out, B, not_8_out, D, E, not_9_out);
  or or_2 (b_2, and_3_out, and_4_out);
endmodule

// L-L
module low_low (
  input  Enable,
  input  Counter,
  input  Reset,
  output N1,
  output N0,
  output W1,
  output W0,
  output E1,
  output E0,
  output S1,
  output S0
);

  wire Clk_out, ew_low_1_a_2, ew_low_1_b_2, ew_low_1_c_2, ew_low_1_d_2, ew_low_1_e, ew_low_1_f, ew_low_1_g,
       ns_low_1_a_2, ns_low_1_b_2, ns_low_1_c_2, ns_low_1_d_2, ns_low_1_e, ns_low_1_f, ns_low_1_g;
  wire [3:0] counter_1_q;

  Clock Clk (.out(Clk_out));
  Counter #(.width(4), .max('hf)) counter_1 (
    .load(Enable), .count(Counter), .Q(counter_1_q), .clk(Clk_out), .clr(Reset));  // open: D, carry
  NS_light_low ns_light_low_1 (
    .A(counter_1_q[3]), .B(counter_1_q[2]), .C(counter_1_q[1]), .D(counter_1_q[0]), .a_2(N1), .b_2(N0));
  EW_Light_low ew_light_low_1 (
    .A(counter_1_q[3]), .B(counter_1_q[2]), .C(counter_1_q[1]), .D(counter_1_q[0]), .a_2(E1), .b_2(E0));
  NS_low ns_low_1 (
    .A(counter_1_q[3]), .B(counter_1_q[2]), .C(counter_1_q[1]), .D(counter_1_q[0]), .a_2(ns_low_1_a_2),
    .b_2(ns_low_1_b_2), .c_2(ns_low_1_c_2), .d_2(ns_low_1_d_2), .e(ns_low_1_e), .f(ns_low_1_f), .g(ns_low_1_g));
  EW_low ew_low_1 (
    .A(counter_1_q[3]), .B(counter_1_q[2]), .C(counter_1_q[1]), .D(counter_1_q[0]), .a_2(ew_low_1_a_2),
    .b_2(ew_low_1_b_2), .c_2(ew_low_1_c_2), .d_2(ew_low_1_d_2), .e(ew_low_1_e), .f(ew_low_1_f), .g(ew_low_1_g));
  _7_Segment_Display u_7_segment_display_1 (
    .g(ns_low_1_g), .f(ns_low_1_f), .a(ns_low_1_a_2), .b(ns_low_1_b_2), .e(ns_low_1_e), .d(ns_low_1_d_2),
    .c(ns_low_1_c_2));  // open: dp
  _7_Segment_Display u_7_segment_display_2 (
    .g(ew_low_1_g), .f(ew_low_1_f), .a(ew_low_1_a_2), .b(ew_low_1_b_2), .e(ew_low_1_e), .d(ew_low_1_d_2),
    .c(ew_low_1_c_2));  // open: dp

  assign S0 = N0;
  assign S1 = N1;
  assign W0 = E0;
  assign W1 = E1;

  // Notes on the sheet:
  //   LOW TRAFFIC
  //   WEST
  //   NORTH
  //   SOUTH
  //   EAST
endmodule

// M-M
module mod_mod (
  input  Enable,
  input  Counter,
  input  Reset,
  output N1,
  output N0,
  output W1,
  output W0,
  output E1,
  output E0,
  output S1,
  output S0
);

  wire Clk_out, ew_lsb_moderate_1_a_2, ew_lsb_moderate_1_b_2, ew_lsb_moderate_1_c_2, ew_lsb_moderate_1_d_2,
       ew_lsb_moderate_1_e_2, ew_lsb_moderate_1_f, ew_lsb_moderate_1_g, ew_msb_moderate_1_a_2,
       ew_msb_moderate_1_b_2, ew_msb_moderate_1_c_2, ew_msb_moderate_1_d_2, ew_msb_moderate_1_e_2,
       ew_msb_moderate_1_f, ew_msb_moderate_1_g, ns_lsb_moderate_1_a_2, ns_lsb_moderate_1_b_2,
       ns_lsb_moderate_1_c_2, ns_lsb_moderate_1_d_2, ns_lsb_moderate_1_e_2, ns_lsb_moderate_1_f,
       ns_lsb_moderate_1_g, ns_msb_moderate_1_a_2, ns_msb_moderate_1_b_2, ns_msb_moderate_1_c_2,
       ns_msb_moderate_1_d_2, ns_msb_moderate_1_e_2, ns_msb_moderate_1_f, ns_msb_moderate_1_g;
  wire [4:0] counter_1_q;

  Clock Clk (.out(Clk_out));
  Counter #(.width(5), .max('h1d)) counter_1 (
    .load(Enable), .count(Counter), .Q(counter_1_q), .clk(Clk_out), .clr(Reset));  // open: D, carry
  NS_light_moderate ns_light_moderate_1 (
    .A(counter_1_q[4]), .B(counter_1_q[3]), .C(counter_1_q[2]), .D(counter_1_q[1]), .E(counter_1_q[0]),
    .a_2(N1), .b_2(N0));
  EW_Light_moderate ew_light_moderate_1 (
    .A(counter_1_q[4]), .B(counter_1_q[3]), .C(counter_1_q[2]), .D(counter_1_q[1]), .E(counter_1_q[0]),
    .a_2(E1), .b_2(E0));
  EW_lsb_moderate ew_lsb_moderate_1 (
    .A(counter_1_q[4]), .B(counter_1_q[3]), .C(counter_1_q[2]), .D(counter_1_q[1]), .E(counter_1_q[0]),
    .a_2(ew_lsb_moderate_1_a_2), .b_2(ew_lsb_moderate_1_b_2), .c_2(ew_lsb_moderate_1_c_2),
    .d_2(ew_lsb_moderate_1_d_2), .e_2(ew_lsb_moderate_1_e_2), .f(ew_lsb_moderate_1_f), .g(ew_lsb_moderate_1_g));
  EW_msb_moderate ew_msb_moderate_1 (
    .A(counter_1_q[4]), .B(counter_1_q[3]), .C(counter_1_q[2]), .D(counter_1_q[1]), .E(counter_1_q[0]),
    .a_2(ew_msb_moderate_1_a_2), .b_2(ew_msb_moderate_1_b_2), .c_2(ew_msb_moderate_1_c_2),
    .d_2(ew_msb_moderate_1_d_2), .e_2(ew_msb_moderate_1_e_2), .f(ew_msb_moderate_1_f), .g(ew_msb_moderate_1_g));
  NS_lsb_moderate ns_lsb_moderate_1 (
    .A(counter_1_q[4]), .B(counter_1_q[3]), .C(counter_1_q[2]), .D(counter_1_q[1]), .E(counter_1_q[0]),
    .a_2(ns_lsb_moderate_1_a_2), .b_2(ns_lsb_moderate_1_b_2), .c_2(ns_lsb_moderate_1_c_2),
    .d_2(ns_lsb_moderate_1_d_2), .e_2(ns_lsb_moderate_1_e_2), .f(ns_lsb_moderate_1_f), .g(ns_lsb_moderate_1_g));
  NS_msb_moderate ns_msb_moderate_1 (
    .A(counter_1_q[4]), .B(counter_1_q[3]), .C(counter_1_q[2]), .D(counter_1_q[1]), .E(counter_1_q[0]),
    .a_2(ns_msb_moderate_1_a_2), .b_2(ns_msb_moderate_1_b_2), .c_2(ns_msb_moderate_1_c_2),
    .d_2(ns_msb_moderate_1_d_2), .e_2(ns_msb_moderate_1_e_2), .f(ns_msb_moderate_1_f), .g(ns_msb_moderate_1_g));
  _7_Segment_Display u_7_segment_display_1 (
    .g(ns_msb_moderate_1_g), .f(ns_msb_moderate_1_f), .a(ns_msb_moderate_1_a_2), .b(ns_msb_moderate_1_b_2),
    .e(ns_msb_moderate_1_e_2), .d(ns_msb_moderate_1_d_2), .c(ns_msb_moderate_1_c_2));  // open: dp
  _7_Segment_Display u_7_segment_display_2 (
    .g(ns_lsb_moderate_1_g), .f(ns_lsb_moderate_1_f), .a(ns_lsb_moderate_1_a_2), .b(ns_lsb_moderate_1_b_2),
    .e(ns_lsb_moderate_1_e_2), .d(ns_lsb_moderate_1_d_2), .c(ns_lsb_moderate_1_c_2));  // open: dp
  _7_Segment_Display u_7_segment_display_3 (
    .g(ew_msb_moderate_1_g), .f(ew_msb_moderate_1_f), .a(ew_msb_moderate_1_a_2), .b(ew_msb_moderate_1_b_2),
    .e(ew_msb_moderate_1_e_2), .d(ew_msb_moderate_1_d_2), .c(ew_msb_moderate_1_c_2));  // open: dp
  _7_Segment_Display u_7_segment_display_4 (
    .g(ew_lsb_moderate_1_g), .f(ew_lsb_moderate_1_f), .a(ew_lsb_moderate_1_a_2), .b(ew_lsb_moderate_1_b_2),
    .e(ew_lsb_moderate_1_e_2), .d(ew_lsb_moderate_1_d_2), .c(ew_lsb_moderate_1_c_2));  // open: dp

  assign S0 = N0;
  assign S1 = N1;
  assign W0 = E0;
  assign W1 = E1;

  // Notes on the sheet:
  //   MODERATE TRAFFIC
  //   WEST
  //   NORTH
  //   SOUTH
  //   EAST
endmodule

// H-H
module high_high (
  input  Enable,
  input  Counter,
  input  Reset,
  output N1,
  output N0,
  output W1,
  output W0,
  output E1,
  output E0,
  output S1,
  output S0
);

  wire Clk_out, ew_lsb_high_1_a_2, ew_lsb_high_1_b_2, ew_lsb_high_1_c_2, ew_lsb_high_1_d_2,
       ew_lsb_high_1_e_2, ew_lsb_high_1_f_2, ew_lsb_high_1_g, ew_msb_high_1_a_2, ew_msb_high_1_b_2,
       ew_msb_high_1_c_2, ew_msb_high_1_d_2, ew_msb_high_1_e_2, ew_msb_high_1_f_2, ew_msb_high_1_g,
       ns_lsb_high_1_a_2, ns_lsb_high_1_b_2, ns_lsb_high_1_c_2, ns_lsb_high_1_d_2, ns_lsb_high_1_e_2,
       ns_lsb_high_1_f_2, ns_lsb_high_1_g, ns_msb_high_1_a_2, ns_msb_high_1_b_2, ns_msb_high_1_c_2,
       ns_msb_high_1_d_2, ns_msb_high_1_e_2, ns_msb_high_1_f_2, ns_msb_high_1_g;
  wire [5:0] counter_1_q;

  Clock Clk (.out(Clk_out));
  Counter #(.width(6), .max('h2b)) counter_1 (
    .load(Enable), .count(Counter), .Q(counter_1_q), .clk(Clk_out), .clr(Reset));  // open: D, carry
  NS_lsb_high ns_lsb_high_1 (
    .A(counter_1_q[5]), .B(counter_1_q[4]), .C(counter_1_q[3]), .D(counter_1_q[2]), .E(counter_1_q[1]),
    .F(counter_1_q[0]), .a_2(ns_lsb_high_1_a_2), .b_2(ns_lsb_high_1_b_2), .c_2(ns_lsb_high_1_c_2),
    .d_2(ns_lsb_high_1_d_2), .e_2(ns_lsb_high_1_e_2), .f_2(ns_lsb_high_1_f_2), .g(ns_lsb_high_1_g));
  NS_msb_high ns_msb_high_1 (
    .A(counter_1_q[5]), .B(counter_1_q[4]), .C(counter_1_q[3]), .D(counter_1_q[2]), .E(counter_1_q[1]),
    .F(counter_1_q[0]), .a_2(ns_msb_high_1_a_2), .b_2(ns_msb_high_1_b_2), .c_2(ns_msb_high_1_c_2),
    .d_2(ns_msb_high_1_d_2), .e_2(ns_msb_high_1_e_2), .f_2(ns_msb_high_1_f_2), .g(ns_msb_high_1_g));
  NS_light_high ns_light_high_1 (
    .A(counter_1_q[5]), .B(counter_1_q[4]), .C(counter_1_q[3]), .D(counter_1_q[2]), .E(counter_1_q[1]),
    .F(counter_1_q[0]), .a_2(N1), .b_2(N0));
  EW_Light_high ew_light_high_1 (
    .A(counter_1_q[5]), .B(counter_1_q[4]), .C(counter_1_q[3]), .D(counter_1_q[2]), .E(counter_1_q[1]),
    .F(counter_1_q[0]), .a_2(E1), .b_2(E0));
  EW_lsb_high ew_lsb_high_1 (
    .A(counter_1_q[5]), .B(counter_1_q[4]), .C(counter_1_q[3]), .D(counter_1_q[2]), .E(counter_1_q[1]),
    .F(counter_1_q[0]), .a_2(ew_lsb_high_1_a_2), .b_2(ew_lsb_high_1_b_2), .c_2(ew_lsb_high_1_c_2),
    .d_2(ew_lsb_high_1_d_2), .e_2(ew_lsb_high_1_e_2), .f_2(ew_lsb_high_1_f_2), .g(ew_lsb_high_1_g));
  EW_msb_high ew_msb_high_1 (
    .A(counter_1_q[5]), .B(counter_1_q[4]), .C(counter_1_q[3]), .D(counter_1_q[2]), .E(counter_1_q[1]),
    .F(counter_1_q[0]), .a_2(ew_msb_high_1_a_2), .b_2(ew_msb_high_1_b_2), .c_2(ew_msb_high_1_c_2),
    .d_2(ew_msb_high_1_d_2), .e_2(ew_msb_high_1_e_2), .f_2(ew_msb_high_1_f_2), .g(ew_msb_high_1_g));
  _7_Segment_Display u_7_segment_display_1 (
    .g(ns_msb_high_1_g), .f(ns_msb_high_1_f_2), .a(ns_msb_high_1_a_2), .b(ns_msb_high_1_b_2),
    .e(ns_msb_high_1_e_2), .d(ns_msb_high_1_d_2), .c(ns_msb_high_1_c_2));  // open: dp
  _7_Segment_Display u_7_segment_display_2 (
    .g(ns_lsb_high_1_g), .f(ns_lsb_high_1_f_2), .a(ns_lsb_high_1_a_2), .b(ns_lsb_high_1_b_2),
    .e(ns_lsb_high_1_e_2), .d(ns_lsb_high_1_d_2), .c(ns_lsb_high_1_c_2));  // open: dp
  _7_Segment_Display u_7_segment_display_3 (
    .g(ew_msb_high_1_g), .f(ew_msb_high_1_f_2), .a(ew_msb_high_1_a_2), .b(ew_msb_high_1_b_2),
    .e(ew_msb_high_1_e_2), .d(ew_msb_high_1_d_2), .c(ew_msb_high_1_c_2));  // open: dp
  _7_Segment_Display u_7_segment_display_4 (
    .g(ew_lsb_high_1_g), .f(ew_lsb_high_1_f_2), .a(ew_lsb_high_1_a_2), .b(ew_lsb_high_1_b_2),
    .e(ew_lsb_high_1_e_2), .d(ew_lsb_high_1_d_2), .c(ew_lsb_high_1_c_2));  // open: dp

  assign S0 = N0;
  assign S1 = N1;
  assign W0 = E0;
  assign W1 = E1;

  // Notes on the sheet:
  //   WEST
  //   NORTH
  //   SOUTH
  //   EAST
endmodule
